// Logisim project Disjoint Switch Box - Prueba Right.circ as structural Verilog: 22 circuits, main circuit Logic_Block
module GASIM (
  input  Pst,
  input  Rst,
  input  _15,
  input  _14,
  input  _13,
  input  _12,
  input  _11,
  input  _10,
  input  _9,
  input  _8,
  input  _7,
  input  _6,
  input  _5,
  input  _4,
  input  _3,
  input  _2,
  input  _1,
  input  _0,
  input  _3_2,
  input  _2_2,
  input  _7_2,
  input  _6_2,
  input  _5_2,
  input  _4_2,
  input  _3_3,
  input  _2_3,
  input  _1_2,
  input  _0_2,
  input  _7_3,
  input  _6_3,
  input  _5_3,
  input  _4_3,
  input  _3_4,
  input  _2_4,
  input  _1_3,
  input  _0_3,
  input  _1_4,
  input  _0_4,
  input  _0_5,
  input  _1_5,
  input  _2_5,
  input  _0_6,
  input  _3_5,
  input  _4_4,
  input  _0_7,
  input  _1_6,
  input  _2_6,
  input  _3_6,
  input  _4_5,
  input  _5_4,
  input  _6_4,
  input  _7_4,
  input  _8_2,
  input  _9_2,
  input  _10_2,
  input  _11_2,
  input  _12_2,
  input  _13_2,
  input  _14_2,
  input  _15_2,
  input  _1_7,
  input  _5_5,
  input  _6_5,
  input  _2_7,
  input  _7_5,
  input  _0_8,
  input  _8_3,
  input  _3_7,
  input  _9_3,
  input  _1_8,
  input  _10_3,
  input  _4_6,
  input  _11_3,
  input  Pst_2,
  input  _2_8,
  input  _12_3,
  input  Rst_2,
  input  _5_6,
  input  _13_3,
  input  _3_8,
  input  _14_3,
  input  _15_3,
  input  _6_6,
  input  _15_4,
  input  _14_4,
  input  _4_7,
  input  _13_4,
  input  _7_6,
  input  _0_9,
  input  _1_9,
  input  _2_9,
  input  _3_9,
  input  _4_8,
  input  _5_7,
  input  _6_7,
  input  _7_7,
  input  Rst_3,
  input  _12_4,
  input  _5_8,
  input  Pst_3,
  input  _11_4,
  input  _10_4,
  input  _6_8,
  input  _9_4,
  input  _8_4,
  input  _7_8,
  input  _7_9,
  input  _0_10,
  input  _6_9,
  input  _1_10,
  input  _5_9,
  input  _2_10,
  input  _4_9,
  input  _0_11,
  input  _1_11,
  input  _2_11,
  input  _3_10,
  input  _4_10,
  input  _5_10,
  input  _6_10,
  input  _7_10,
  input  _3_11,
  input  _7_11,
  input  _6_11,
  input  _5_11,
  input  _4_11,
  input  _3_12,
  input  _2_12,
  input  _1_12,
  input  _0_12,
  input  _3_13,
  input  _2_13,
  input  _1_13,
  input  _0_13,
  input  _0_14,
  input  _1_14,
  input  _2_14,
  input  _3_14,
  input  _4_12,
  input  _5_12,
  input  _6_12,
  input  _7_12,
  input  _8_5,
  input  _9_5,
  input  _10_5,
  input  _11_5,
  input  _12_5,
  input  _13_5,
  input  _14_5,
  input  _15_5,
  input  Rst_4,
  input  Pst_4,
  input  Pst_5,
  input  Rst_5,
  input  _15_6,
  input  _14_6,
  input  _13_6,
  input  _12_6,
  input  _11_6,
  input  _10_6,
  input  _9_6,
  input  _8_6,
  input  _7_13,
  input  _6_13,
  input  _5_13,
  input  _4_13,
  input  _3_15,
  input  _2_15,
  input  _1_15,
  input  _0_15,
  input  _0_16,
  input  _1_16,
  input  _2_16,
  input  _7_14,
  input  _6_14,
  input  _5_14,
  input  _4_14,
  input  _3_16,
  input  _2_17,
  input  _1_17,
  input  _0_17,
  input  _3_17,
  input  _4_15,
  input  _5_15,
  input  _6_15,
  input  _7_15,
  input  _8_7,
  input  _9_7,
  input  _10_7,
  input  _11_7,
  input  _12_7,
  input  Pst_6,
  input  _13_7,
  input  Rst_6,
  input  _14_7,
  input  _15_7,
  input  Rst_7,
  input  Pst_7,
  input  _0_18,
  input  _1_18,
  input  _2_18,
  input  _3_18,
  input  Pst_8,
  input  Rst_8,
  input  _15_8,
  input  _14_8,
  input  _13_8,
  input  _12_8,
  input  _11_8,
  input  _10_8,
  input  _9_8,
  input  _8_8,
  input  _7_16,
  input  _6_16,
  input  _5_16,
  input  _4_16,
  input  _3_19,
  input  _2_19,
  input  _1_19,
  input  _0_19,
  input  _0_20,
  input  _1_20,
  input  _2_20,
  input  _3_20,
  input  _4_17,
  input  _5_17,
  input  _6_17,
  input  _7_17,
  input  _8_9,
  input  _9_9,
  input  _10_9,
  input  _11_9,
  input  _12_9,
  input  _13_9,
  input  _14_9,
  input  _15_9,
  input  Rst_9,
  input  Pst_9,
  input  _3_21,
  input  _2_21,
  input  _1_21,
  input  _0_21,
  input  Pst_10,
  input  Rst_10,
  input  _15_10,
  input  _14_10,
  input  Rst_11,
  input  _13_10,
  input  Pst_11,
  input  _12_10,
  input  _11_10,
  input  _10_10,
  input  _9_10,
  input  _8_10,
  input  _7_18,
  input  _6_18,
  input  _5_18,
  input  _4_18,
  input  _3_22,
  input  _0_22,
  input  _1_22,
  input  _2_22,
  input  _3_23,
  input  _4_19,
  input  _5_19,
  input  _6_19,
  input  _7_19,
  input  _2_23,
  input  _1_23,
  input  _0_23,
  input  _0_24,
  input  _1_24,
  input  _2_24,
  input  _3_24,
  input  _4_20,
  input  _5_20,
  input  _6_20,
  input  _7_20,
  input  _8_11,
  input  _9_11,
  input  _10_11,
  input  _11_11,
  input  _12_11,
  input  _13_11,
  input  _14_11,
  input  _15_11,
  input  Rst_12,
  input  Pst_12
);

  wire Clk_2_out, Clk_3_out, Clk_4_out, Clk_5_out, Clk_6_out, Clk_7_out, Clk_8_out, Clk_9_out, Clk_10_out,
       Clk_11_out, Clk_12_out, Clk_out, connection_box_2__5, connection_box_2__6, connection_box_2__7,
       connection_box_2__8, connection_box_2__9, connection_box_2__10, connection_box_2__11,
       connection_box_2__12, connection_box_2__13, connection_box_2__14, connection_box_2__15,
       connection_box_2__16, connection_box_2__17, connection_box_2__18, connection_box_2__19,
       connection_box_2__20, connection_box_2__22, connection_box_2__24, connection_box_2__26,
       connection_box_2__28, connection_box_2__30, connection_box_2__32, connection_box_2__34,
       connection_box_2__36, connection_box_2__41, connection_box_2__42, connection_box_2__43,
       connection_box_2__44, connection_box_2__45, connection_box_2__46, connection_box_2__47,
       connection_box_2__48, connection_box_2__49, connection_box_2__50, connection_box_2__51,
       connection_box_2__52, connection_box_2__53, connection_box_2__54, connection_box_2__55,
       connection_box_2__56, connection_box_2__58, connection_box_2__60, connection_box_2__62,
       connection_box_2__64, connection_box_2__66, connection_box_2__68, connection_box_2__70,
       connection_box_2__72, connection_box_3__5, connection_box_3__6, connection_box_3__7,
       connection_box_3__8, connection_box_3__9, connection_box_3__10, connection_box_3__11,
       connection_box_3__12, connection_box_3__13, connection_box_3__14, connection_box_3__15,
       connection_box_3__16, connection_box_3__17, connection_box_3__18, connection_box_3__19,
       connection_box_3__20, connection_box_3__22, connection_box_3__24, connection_box_3__26,
       connection_box_3__28, connection_box_3__30, connection_box_3__32, connection_box_3__34,
       connection_box_3__36, connection_box_3__41, connection_box_3__42, connection_box_3__43,
       connection_box_3__44, connection_box_3__45, connection_box_3__46, connection_box_3__47,
       connection_box_3__48, connection_box_3__49, connection_box_3__50, connection_box_3__51,
       connection_box_3__52, connection_box_3__53, connection_box_3__54, connection_box_3__55,
       connection_box_3__56, connection_box_3__58, connection_box_3__60, connection_box_3__62,
       connection_box_3__64, connection_box_3__66, connection_box_3__68, connection_box_3__70,
       connection_box_3__72, connection_box_4__5, connection_box_4__6, connection_box_4__7,
       connection_box_4__8, connection_box_4__9, connection_box_4__10, connection_box_4__11,
       connection_box_4__12, connection_box_4__13, connection_box_4__14, connection_box_4__15,
       connection_box_4__16, connection_box_4__17, connection_box_4__18, connection_box_4__19,
       connection_box_4__20, connection_box_4__22, connection_box_4__24, connection_box_4__26,
       connection_box_4__28, connection_box_4__30, connection_box_4__32, connection_box_4__34,
       connection_box_4__36, connection_box_4__41, connection_box_4__42, connection_box_4__43,
       connection_box_4__44, connection_box_4__45, connection_box_4__46, connection_box_4__47,
       connection_box_4__48, connection_box_4__49, connection_box_4__50, connection_box_4__51,
       connection_box_4__52, connection_box_4__53, connection_box_4__54, connection_box_4__55,
       connection_box_4__56, connection_box_4__58, connection_box_4__60, connection_box_4__62,
       connection_box_4__64, connection_box_4__66, connection_box_4__68, connection_box_4__70,
       connection_box_4__72, disjoint_switch_box_2_out_33, disjoint_switch_box_2_out_34,
       disjoint_switch_box_2_out_35, disjoint_switch_box_2_out_36, disjoint_switch_box_2_out_37,
       disjoint_switch_box_2_out_38, disjoint_switch_box_2_out_39, disjoint_switch_box_2_out_40,
       disjoint_switch_box_2_out_41, disjoint_switch_box_2_out_42, disjoint_switch_box_2_out_43,
       disjoint_switch_box_2_out_44, disjoint_switch_box_2_out_45, disjoint_switch_box_2_out_46,
       disjoint_switch_box_2_out_47, disjoint_switch_box_2_out_48, disjoint_switch_box_2_out_49,
       disjoint_switch_box_2_out_50, disjoint_switch_box_2_out_51, disjoint_switch_box_2_out_52,
       disjoint_switch_box_2_out_53, disjoint_switch_box_2_out_54, disjoint_switch_box_2_out_55,
       disjoint_switch_box_2_out_56, disjoint_switch_box_2_out_57, disjoint_switch_box_2_out_58,
       disjoint_switch_box_2_out_59, disjoint_switch_box_2_out_60, disjoint_switch_box_2_out_61,
       disjoint_switch_box_2_out_62, disjoint_switch_box_2_out_63, disjoint_switch_box_2_out_64,
       input_output_block_2__17, input_output_block_2__18, input_output_block_2__19,
       input_output_block_2__20, logic_block_1__17, logic_block_1__18, logic_block_1__19, logic_block_1__20,
       logic_block_1__37, logic_block_1__38, logic_block_1__39, logic_block_1__40, logic_block_1__57,
       logic_block_1__58, logic_block_1__59, logic_block_1__60, logic_block_1__77, logic_block_1__78,
       logic_block_1__79, logic_block_1__80, logic_block_2__17, logic_block_2__18, logic_block_2__19,
       logic_block_2__20, logic_block_2__37, logic_block_2__38, logic_block_2__39, logic_block_2__40,
       logic_block_2__57, logic_block_2__58, logic_block_2__59, logic_block_2__60, logic_block_2__77,
       logic_block_2__78, logic_block_2__79, logic_block_2__80, logic_block_4__17, logic_block_4__18,
       logic_block_4__19, logic_block_4__20, logic_block_4__37, logic_block_4__38, logic_block_4__39,
       logic_block_4__40, logic_block_4__57, logic_block_4__58, logic_block_4__59, logic_block_4__60,
       logic_block_4__77, logic_block_4__78, logic_block_4__79, logic_block_4__80;

  Clock Clk (.out(Clk_out));
  LED A0 (.in(logic_block_1__17));
  LED A1 (.in(logic_block_1__18));
  LED A2 (.in(logic_block_1__19));
  LED A3 (.in(logic_block_1__20));
  LED A3_2 (.in(logic_block_1__80));
  Clock Clk_2 (.out(Clk_2_out));
  LED A0_2 (.in(logic_block_2__17));
  LED A1_2 (.in(logic_block_2__18));
  LED A2_2 (.in(logic_block_2__19));
  LED A3_3 (.in(logic_block_2__20));
  LED A0_3 (.in(logic_block_1__77));
  LED A1_3 (.in(logic_block_1__78));
  LED A2_3 (.in(logic_block_1__79));
  Input_Output_Block input_output_block_1 ();  // open: _17, _19, _20, in_16, in_15, in_14, in_13, in_12, in_11, in_10, in_9, in_8, in_7, in_6, in_5, in_4, in_3, in_2, in_1, in_17, in_18, in_19, in_20, in_21, in_22, in_23, in_24, _18
  Clock Clk_3 (.out(Clk_3_out));
  Clock Clk_4 (.out(Clk_4_out));
  LED A3_4 (.in(logic_block_1__40));
  LED A2_4 (.in(logic_block_1__39));
  LED A1_4 (.in(logic_block_1__38));
  LED A0_4 (.in(logic_block_1__37));
  LED A3_5 (.in(logic_block_2__80));
  Logic_Block logic_block_1 (
    ._1(_15_4), ._2(_14_3), ._3(_13_3), ._4(_12_3), ._5(_11_3), ._6(_10_3), ._7(_9_3), ._8(_8_3), ._9(_7_5),
    ._10(_6_5), ._11(_5_5), ._12(_4_4), ._13(_3_5), ._14(_2_5), ._15(_1_5), ._16(_0_5),
    ._17(logic_block_1__17), ._18(logic_block_1__18), ._19(logic_block_1__19), ._20(logic_block_1__20),
    ._81(Clk_out), ._82(Rst_3), ._83(Pst_3), ._57(logic_block_1__57), ._58(logic_block_1__58),
    ._59(logic_block_1__59), ._60(logic_block_1__60), ._41(_15_3), ._42(_14_4), ._89(Pst_2), ._43(_13_4),
    ._88(Rst_2), ._44(_12_4), ._87(Clk_7_out), ._45(_11_4), ._46(_10_4), ._47(_9_4), ._48(_8_4), ._49(_7_9),
    ._50(_6_9), ._51(_5_9), ._52(_4_9), ._53(_3_13), ._54(_2_13), ._55(_1_13), ._56(_0_13), ._76(_0),
    ._75(_1), ._74(_2), ._73(_3), ._72(_4), ._71(_5), ._70(_6), ._69(_7), ._68(_8), ._67(_9), ._66(_10),
    ._65(_11), ._64(_12), ._63(_13), ._62(_14), ._61(_15), ._92(Pst), ._91(Rst), ._90(Clk_3_out),
    ._80(logic_block_1__80), ._79(logic_block_1__79), ._78(logic_block_1__78), ._77(logic_block_1__77),
    ._36(_0_14), ._35(_1_14), ._34(_2_14), ._33(_3_14), ._32(_4_12), ._31(_5_12), ._30(_6_12), ._29(_7_12),
    ._28(_8_5), ._27(_9_5), ._26(_10_5), ._25(_11_5), ._24(_12_5), ._23(_13_5), ._22(_14_5), ._21(_15_5),
    ._84(Clk_4_out), ._85(Rst_4), ._86(Pst_4), ._40(logic_block_1__40), ._39(logic_block_1__39),
    ._38(logic_block_1__38), ._37(logic_block_1__37));
  LED A0_5 (.in(logic_block_2__77));
  LED A2_5 (.in(logic_block_2__79));
  LED A1_5 (.in(logic_block_2__78));
  Clock Clk_5 (.out(Clk_5_out));
  Clock Clk_6 (.out(Clk_6_out));
  Connection_Box connection_box_1 ();  // open: _72, _71, _70, _69, _68, _67, _66, _65, _64, _63, _62, _61, _60, _59, _58, _57, _21, _22, _23, _24, _25, _26, _27, _28, _29, _30, _31, _32, _33, _34, _35, _1, _2, _3, _4, _5, _6, _7, _8, _10, _11, _12, _13, _14, _15, _16, _17, _18, _19, _56, _55, _53, _52, _51, _50, _49, _48, _47, _46, _45, _44, _43, _42, _41, _40, _39, _38, _37, _36, _20, _9, _54
  LED A3_6 (.in(logic_block_1__60));
  LED A2_6 (.in(logic_block_1__59));
  LED A1_6 (.in(logic_block_1__58));
  LED A0_6 (.in(logic_block_1__57));
  Clock Clk_7 (.out(Clk_7_out));
  Logic_Block logic_block_2 (
    ._1(_15_7), ._2(_14_7), ._3(_13_7), ._4(_12_7), ._5(_11_7), ._6(_10_7), ._7(_9_7), ._8(_8_7), ._9(_7_15),
    ._10(_6_15), ._11(_5_15), ._12(_4_15), ._13(_3_17), ._14(_2_16), ._15(_1_16), ._16(_0_16),
    ._17(logic_block_2__17), ._18(logic_block_2__18), ._19(logic_block_2__19), ._20(logic_block_2__20),
    ._81(Clk_2_out), ._82(Rst_7), ._83(Pst_7), ._57(logic_block_2__57), ._58(logic_block_2__58),
    ._59(logic_block_2__59), ._60(logic_block_2__60), ._41(connection_box_2__20), ._42(connection_box_2__19),
    ._89(Pst_6), ._43(connection_box_2__18), ._88(Rst_6), ._44(connection_box_2__17), ._87(Clk_8_out),
    ._45(connection_box_2__16), ._46(connection_box_2__15), ._47(connection_box_2__14),
    ._48(connection_box_2__13), ._49(connection_box_2__12), ._50(connection_box_2__11),
    ._51(connection_box_2__10), ._52(connection_box_2__9), ._53(connection_box_2__8),
    ._54(connection_box_2__7), ._55(connection_box_2__6), ._56(connection_box_2__5), ._76(_0_15),
    ._75(_1_15), ._74(_2_15), ._73(_3_15), ._72(_4_13), ._71(_5_13), ._70(_6_13), ._69(_7_13), ._68(_8_6),
    ._67(_9_6), ._66(_10_6), ._65(_11_6), ._64(_12_6), ._63(_13_6), ._62(_14_6), ._61(_15_6), ._92(Pst_5),
    ._91(Rst_5), ._90(Clk_5_out), ._80(logic_block_2__80), ._79(logic_block_2__79), ._78(logic_block_2__78),
    ._77(logic_block_2__77), ._36(_0_20), ._35(_1_20), ._34(_2_20), ._33(_3_20), ._32(_4_17), ._31(_5_17),
    ._30(_6_17), ._29(_7_17), ._28(_8_9), ._27(_9_9), ._26(_10_9), ._25(_11_9), ._24(_12_9), ._23(_13_9),
    ._22(_14_9), ._21(_15_9), ._84(Clk_6_out), ._85(Rst_9), ._86(Pst_9), ._40(logic_block_2__40),
    ._39(logic_block_2__39), ._38(logic_block_2__38), ._37(logic_block_2__37));
  LED A2_7 (.in(logic_block_2__38));
  LED A1_7 (.in(logic_block_2__39));
  LED A3_7 (.in(logic_block_2__37));
  LED A0_7 (.in(logic_block_2__40));
  Clock Clk_8 (.out(Clk_8_out));
  LED led_1 (.in(connection_box_3__20));
  LED led_2 (.in(connection_box_3__19));
  LED led_3 (.in(connection_box_3__18));
  LED led_4 (.in(connection_box_3__17));
  LED led_5 (.in(connection_box_3__16));
  LED led_6 (.in(connection_box_3__15));
  LED led_7 (.in(connection_box_3__14));
  LED led_8 (.in(connection_box_3__13));
  LED led_9 (.in(connection_box_3__12));
  LED led_10 (.in(connection_box_3__11));
  LED led_11 (.in(connection_box_3__10));
  LED led_12 (.in(connection_box_3__9));
  LED led_13 (.in(connection_box_3__8));
  LED led_14 (.in(connection_box_3__7));
  LED led_15 (.in(connection_box_3__6));
  LED led_16 (.in(connection_box_3__5));
  LED led_17 (.in(connection_box_4__20));
  LED led_18 (.in(connection_box_4__19));
  LED led_19 (.in(connection_box_4__18));
  LED led_20 (.in(connection_box_4__17));
  LED led_21 (.in(connection_box_4__16));
  LED led_22 (.in(connection_box_4__15));
  LED led_23 (.in(connection_box_4__14));
  LED led_24 (.in(connection_box_4__13));
  LED led_25 (.in(connection_box_4__12));
  LED led_26 (.in(connection_box_4__11));
  LED led_27 (.in(connection_box_4__10));
  LED led_28 (.in(connection_box_4__9));
  LED led_29 (.in(connection_box_4__8));
  LED led_30 (.in(connection_box_4__7));
  LED led_31 (.in(connection_box_4__6));
  LED led_32 (.in(connection_box_4__5));
  LED led_33 (.in(connection_box_3__22));
  Logic_Block logic_block_3 ();  // open: _1, _2, _3, _4, _5, _6, _7, _8, _9, _10, _11, _12, _13, _14, _15, _16, _17, _18, _19, _20, _81, _82, _83, _57, _58, _59, _60, _41, _42, _89, _43, _88, _44, _87, _45, _46, _47, _48, _49, _50, _51, _52, _53, _54, _55, _56, _76, _75, _74, _73, _72, _71, _70, _69, _68, _67, _66, _65, _64, _63, _62, _61, _92, _91, _90, _80, _79, _78, _77, _36, _35, _34, _33, _32, _31, _30, _29, _28, _27, _26, _25, _24, _23, _22, _21, _84, _85, _86, _40, _39, _38, _37
  LED led_34 (.in(connection_box_4__24));
  LED led_35 (.in(connection_box_4__22));
  LED led_36 (.in(connection_box_2__72));
  LED led_37 (.in(connection_box_3__26));
  LED led_38 (.in(connection_box_3__24));
  LED led_39 (.in(connection_box_4__72));
  LED led_40 (.in(connection_box_4__70));
  LED led_41 (.in(connection_box_4__26));
  LED led_42 (.in(connection_box_4__28));
  LED led_43 (.in(connection_box_2__70));
  LED led_44 (.in(connection_box_2__68));
  LED led_45 (.in(connection_box_3__28));
  LED led_46 (.in(connection_box_3__30));
  LED led_47 (.in(connection_box_4__66));
  LED led_48 (.in(connection_box_4__68));
  LED led_49 (.in(connection_box_4__32));
  LED led_50 (.in(connection_box_4__30));
  LED led_51 (.in(connection_box_2__64));
  LED led_52 (.in(connection_box_2__66));
  LED led_53 (.in(connection_box_3__32));
  LED led_54 (.in(connection_box_3__34));
  LED led_55 (.in(connection_box_4__62));
  LED led_56 (.in(connection_box_4__64));
  LED led_57 (.in(connection_box_4__36));
  LED led_58 (.in(connection_box_4__34));
  LED led_59 (.in(connection_box_2__62));
  LED led_60 (.in(connection_box_2__60));
  Connection_Box connection_box_2 (
    ._72(connection_box_2__72), ._71(_7_14), ._70(connection_box_2__70), ._69(_6_14),
    ._68(connection_box_2__68), ._67(_5_14), ._66(connection_box_2__66), ._65(_4_14),
    ._64(connection_box_2__64), ._63(_3_16), ._62(connection_box_2__62), ._61(_2_17),
    ._60(connection_box_2__60), ._59(_1_17), ._58(connection_box_2__58), ._57(_0_17),
    ._21(connection_box_3__72), ._22(connection_box_2__22), ._23(connection_box_3__70),
    ._24(connection_box_2__24), ._25(connection_box_3__68), ._26(connection_box_2__26),
    ._27(connection_box_3__66), ._28(connection_box_2__28), ._29(connection_box_3__64),
    ._30(connection_box_2__30), ._31(connection_box_3__62), ._32(connection_box_2__32),
    ._33(connection_box_3__60), ._34(connection_box_2__34), ._35(connection_box_3__58),
    ._1(logic_block_2__60), ._2(logic_block_2__59), ._3(logic_block_2__58), ._4(logic_block_2__57),
    ._5(connection_box_2__5), ._6(connection_box_2__6), ._7(connection_box_2__7), ._8(connection_box_2__8),
    ._10(connection_box_2__10), ._11(connection_box_2__11), ._12(connection_box_2__12),
    ._13(connection_box_2__13), ._14(connection_box_2__14), ._15(connection_box_2__15),
    ._16(connection_box_2__16), ._17(connection_box_2__17), ._18(connection_box_2__18),
    ._19(connection_box_2__19), ._56(connection_box_2__56), ._55(connection_box_2__55),
    ._53(connection_box_2__53), ._52(connection_box_2__52), ._51(connection_box_2__51),
    ._50(connection_box_2__50), ._49(connection_box_2__49), ._48(connection_box_2__48),
    ._47(connection_box_2__47), ._46(connection_box_2__46), ._45(connection_box_2__45),
    ._44(connection_box_2__44), ._43(connection_box_2__43), ._42(connection_box_2__42),
    ._41(connection_box_2__41), ._40(_0_18), ._39(_1_18), ._38(_2_18), ._37(_3_18),
    ._36(connection_box_2__36), ._20(connection_box_2__20), ._9(connection_box_2__9),
    ._54(connection_box_2__54));
  Connection_Box connection_box_3 (
    ._72(connection_box_3__72), ._71(connection_box_2__22), ._70(connection_box_3__70),
    ._69(connection_box_2__24), ._68(connection_box_3__68), ._67(connection_box_2__26),
    ._66(connection_box_3__66), ._65(connection_box_2__28), ._64(connection_box_3__64),
    ._63(connection_box_2__30), ._62(connection_box_3__62), ._61(connection_box_2__32),
    ._60(connection_box_3__60), ._59(connection_box_2__34), ._58(connection_box_3__58),
    ._57(connection_box_2__36), ._21(_0_22), ._22(connection_box_3__22), ._23(_1_22),
    ._24(connection_box_3__24), ._25(_2_22), ._26(connection_box_3__26), ._27(_3_23),
    ._28(connection_box_3__28), ._29(_4_19), ._30(connection_box_3__30), ._31(_5_19),
    ._32(connection_box_3__32), ._33(_6_19), ._34(connection_box_3__34), ._35(_7_19), ._1(_3_21), ._2(_2_21),
    ._3(_1_21), ._4(_0_21), ._5(connection_box_3__5), ._6(connection_box_3__6), ._7(connection_box_3__7),
    ._8(connection_box_3__8), ._10(connection_box_3__10), ._11(connection_box_3__11),
    ._12(connection_box_3__12), ._13(connection_box_3__13), ._14(connection_box_3__14),
    ._15(connection_box_3__15), ._16(connection_box_3__16), ._17(connection_box_3__17),
    ._18(connection_box_3__18), ._19(connection_box_3__19), ._56(connection_box_3__56),
    ._55(connection_box_3__55), ._53(connection_box_3__53), ._52(connection_box_3__52),
    ._51(connection_box_3__51), ._50(connection_box_3__50), ._49(connection_box_3__49),
    ._48(connection_box_3__48), ._47(connection_box_3__47), ._46(connection_box_3__46),
    ._45(connection_box_3__45), ._44(connection_box_3__44), ._43(connection_box_3__43),
    ._42(connection_box_3__42), ._41(connection_box_3__41), ._40(logic_block_4__17), ._39(logic_block_4__18),
    ._38(logic_block_4__19), ._37(logic_block_4__20), ._36(connection_box_3__36), ._20(connection_box_3__20),
    ._9(connection_box_3__9), ._54(connection_box_3__54));
  LED led_61 (.in(connection_box_3__36));
  Disjoint_Switch_Box disjoint_switch_box_1 ();  // open: in_9, out_42, in_11, out_44, in_13, out_46, in_15, out_48, in_17, out_50, in_19, out_52, in_21, out_54, in_23, out_56, out_41, in_10, out_43, in_12, out_45, in_14, out_47, in_16, out_49, in_18, out_51, in_20, out_53, in_22, out_55, in_24, out_33, _7, out_34, _6, out_35, _5, out_36, _4, out_37, _3, out_38, _2, out_39, _1, out_40, _0, in_25, out_57, in_26, out_58, in_27, out_59, in_28, out_60, in_29, out_61, in_30, out_62, in_31, out_63, in_32, out_64
  LED led_62 (.in(connection_box_4__58));
  LED led_63 (.in(connection_box_4__60));
  Connection_Box connection_box_4 (
    ._72(connection_box_4__72), ._71(_7_2), ._70(connection_box_4__70), ._69(_6_2),
    ._68(connection_box_4__68), ._67(_5_2), ._66(connection_box_4__66), ._65(_4_2),
    ._64(connection_box_4__64), ._63(_3_3), ._62(connection_box_4__62), ._61(_2_3),
    ._60(connection_box_4__60), ._59(_1_2), ._58(connection_box_4__58), ._57(_0_2), ._21(_0_11),
    ._22(connection_box_4__22), ._23(_1_11), ._24(connection_box_4__24), ._25(_2_11),
    ._26(connection_box_4__26), ._27(_3_10), ._28(connection_box_4__28), ._29(_4_10),
    ._30(connection_box_4__30), ._31(_5_10), ._32(connection_box_4__32), ._33(_6_10),
    ._34(connection_box_4__34), ._35(_7_10), ._1(_3_2), ._2(_2_2), ._3(_1_4), ._4(_0_4),
    ._5(connection_box_4__5), ._6(connection_box_4__6), ._7(connection_box_4__7), ._8(connection_box_4__8),
    ._10(connection_box_4__10), ._11(connection_box_4__11), ._12(connection_box_4__12),
    ._13(connection_box_4__13), ._14(connection_box_4__14), ._15(connection_box_4__15),
    ._16(connection_box_4__16), ._17(connection_box_4__17), ._18(connection_box_4__18),
    ._19(connection_box_4__19), ._56(connection_box_4__56), ._55(connection_box_4__55),
    ._53(connection_box_4__53), ._52(connection_box_4__52), ._51(connection_box_4__51),
    ._50(connection_box_4__50), ._49(connection_box_4__49), ._48(connection_box_4__48),
    ._47(connection_box_4__47), ._46(connection_box_4__46), ._45(connection_box_4__45),
    ._44(connection_box_4__44), ._43(connection_box_4__43), ._42(connection_box_4__42),
    ._41(connection_box_4__41), ._40(_0_10), ._39(_1_10), ._38(_2_10), ._37(_3_11),
    ._36(connection_box_4__36), ._20(connection_box_4__20), ._9(connection_box_4__9),
    ._54(connection_box_4__54));
  LED led_64 (.in(connection_box_2__58));
  Clock Clk_9 (.out(Clk_9_out));
  LED led_65 (.in(connection_box_4__56));
  LED led_66 (.in(connection_box_4__55));
  LED led_67 (.in(connection_box_4__54));
  LED led_68 (.in(connection_box_4__53));
  LED led_69 (.in(connection_box_4__52));
  LED led_70 (.in(connection_box_4__51));
  LED led_71 (.in(connection_box_4__50));
  LED led_72 (.in(connection_box_4__49));
  LED led_73 (.in(connection_box_4__48));
  LED led_74 (.in(connection_box_4__47));
  LED led_75 (.in(connection_box_4__46));
  LED led_76 (.in(connection_box_4__45));
  LED led_77 (.in(connection_box_4__44));
  LED led_78 (.in(connection_box_4__43));
  LED led_79 (.in(connection_box_4__42));
  LED led_80 (.in(connection_box_4__41));
  LED led_81 (.in(connection_box_2__56));
  LED led_82 (.in(connection_box_2__55));
  LED led_83 (.in(connection_box_2__54));
  LED led_84 (.in(connection_box_2__53));
  LED led_85 (.in(connection_box_2__52));
  LED led_86 (.in(connection_box_2__51));
  LED led_87 (.in(connection_box_2__50));
  LED led_88 (.in(connection_box_2__49));
  LED led_89 (.in(connection_box_2__48));
  LED led_90 (.in(connection_box_2__47));
  LED led_91 (.in(connection_box_2__46));
  LED led_92 (.in(connection_box_2__45));
  LED led_93 (.in(connection_box_2__44));
  LED led_94 (.in(connection_box_2__43));
  LED led_95 (.in(connection_box_2__42));
  LED led_96 (.in(connection_box_2__41));
  LED A1_8 (.in(logic_block_4__78));
  LED A2_8 (.in(logic_block_4__79));
  LED A3_8 (.in(logic_block_4__80));
  LED A0_8 (.in(logic_block_4__77));
  Clock Clk_10 (.out(Clk_10_out));
  Clock Clk_11 (.out(Clk_11_out));
  LED led_97 (.in(disjoint_switch_box_2_out_42));
  LED led_98 (.in(disjoint_switch_box_2_out_44));
  LED led_99 (.in(disjoint_switch_box_2_out_46));
  LED led_100 (.in(disjoint_switch_box_2_out_48));
  LED led_101 (.in(disjoint_switch_box_2_out_50));
  LED led_102 (.in(disjoint_switch_box_2_out_52));
  LED led_103 (.in(disjoint_switch_box_2_out_54));
  LED led_104 (.in(disjoint_switch_box_2_out_56));
  LED A1_9 (.in(logic_block_4__39));
  LED A2_9 (.in(logic_block_4__38));
  LED A3_9 (.in(logic_block_4__37));
  LED led_105 (.in(disjoint_switch_box_2_out_57));
  LED led_106 (.in(disjoint_switch_box_2_out_58));
  Logic_Block logic_block_4 (
    ._1(connection_box_3__41), ._2(connection_box_3__42), ._3(connection_box_3__43),
    ._4(connection_box_3__44), ._5(connection_box_3__45), ._6(connection_box_3__46),
    ._7(connection_box_3__47), ._8(connection_box_3__48), ._9(connection_box_3__49),
    ._10(connection_box_3__50), ._11(connection_box_3__51), ._12(connection_box_3__52),
    ._13(connection_box_3__53), ._14(connection_box_3__54), ._15(connection_box_3__55),
    ._16(connection_box_3__56), ._17(logic_block_4__17), ._18(logic_block_4__18), ._19(logic_block_4__19),
    ._20(logic_block_4__20), ._81(Clk_9_out), ._82(Rst_11), ._83(Pst_11), ._57(logic_block_4__57),
    ._58(logic_block_4__58), ._59(logic_block_4__59), ._60(logic_block_4__60), ._41(_15_10), ._42(_14_10),
    ._89(Pst_10), ._43(_13_10), ._88(Rst_10), ._44(_12_10), ._87(Clk_12_out), ._45(_11_10), ._46(_10_10),
    ._47(_9_10), ._48(_8_10), ._49(_7_18), ._50(_6_18), ._51(_5_18), ._52(_4_18), ._53(_3_22), ._54(_2_23),
    ._55(_1_23), ._56(_0_23), ._76(_0_19), ._75(_1_19), ._74(_2_19), ._73(_3_19), ._72(_4_16), ._71(_5_16),
    ._70(_6_16), ._69(_7_16), ._68(_8_8), ._67(_9_8), ._66(_10_8), ._65(_11_8), ._64(_12_8), ._63(_13_8),
    ._62(_14_8), ._61(_15_8), ._92(Pst_8), ._91(Rst_8), ._90(Clk_10_out), ._80(logic_block_4__80),
    ._79(logic_block_4__79), ._78(logic_block_4__78), ._77(logic_block_4__77), ._36(_0_24), ._35(_1_24),
    ._34(_2_24), ._33(_3_24), ._32(_4_20), ._31(_5_20), ._30(_6_20), ._29(_7_20), ._28(_8_11), ._27(_9_11),
    ._26(_10_11), ._25(_11_11), ._24(_12_11), ._23(_13_11), ._22(_14_11), ._21(_15_11), ._84(Clk_11_out),
    ._85(Rst_12), ._86(Pst_12), ._40(logic_block_4__40), ._39(logic_block_4__39), ._38(logic_block_4__38),
    ._37(logic_block_4__37));
  LED A0_9 (.in(logic_block_4__40));
  LED led_107 (.in(disjoint_switch_box_2_out_33));
  LED led_108 (.in(disjoint_switch_box_2_out_34));
  LED led_109 (.in(disjoint_switch_box_2_out_60));
  LED led_110 (.in(disjoint_switch_box_2_out_59));
  LED led_111 (.in(disjoint_switch_box_2_out_36));
  LED led_112 (.in(disjoint_switch_box_2_out_35));
  LED led_113 (.in(disjoint_switch_box_2_out_62));
  LED led_114 (.in(disjoint_switch_box_2_out_61));
  LED led_115 (.in(disjoint_switch_box_2_out_37));
  LED led_116 (.in(disjoint_switch_box_2_out_38));
  Disjoint_Switch_Box disjoint_switch_box_2 (
    .in_9(_0_6), .out_42(disjoint_switch_box_2_out_42), .in_11(_1_7), .out_44(disjoint_switch_box_2_out_44),
    .in_13(_2_7), .out_46(disjoint_switch_box_2_out_46), .in_15(_3_7), .out_48(disjoint_switch_box_2_out_48),
    .in_17(_4_6), .out_50(disjoint_switch_box_2_out_50), .in_19(_5_6), .out_52(disjoint_switch_box_2_out_52),
    .in_21(_6_6), .out_54(disjoint_switch_box_2_out_54), .in_23(_7_6), .out_56(disjoint_switch_box_2_out_56),
    .out_41(disjoint_switch_box_2_out_41), .in_10(_0_8), .out_43(disjoint_switch_box_2_out_43), .in_12(_1_8),
    .out_45(disjoint_switch_box_2_out_45), .in_14(_2_8), .out_47(disjoint_switch_box_2_out_47), .in_16(_3_8),
    .out_49(disjoint_switch_box_2_out_49), .in_18(_4_7), .out_51(disjoint_switch_box_2_out_51), .in_20(_5_8),
    .out_53(disjoint_switch_box_2_out_53), .in_22(_6_8), .out_55(disjoint_switch_box_2_out_55), .in_24(_7_8),
    .out_33(disjoint_switch_box_2_out_33), ._7(_7_3), .out_34(disjoint_switch_box_2_out_34), ._6(_6_3),
    .out_35(disjoint_switch_box_2_out_35), ._5(_5_3), .out_36(disjoint_switch_box_2_out_36), ._4(_4_3),
    .out_37(disjoint_switch_box_2_out_37), ._3(_3_4), .out_38(disjoint_switch_box_2_out_38), ._2(_2_4),
    .out_39(disjoint_switch_box_2_out_39), ._1(_1_3), .out_40(disjoint_switch_box_2_out_40), ._0(_0_3),
    .in_25(_7_11), .out_57(disjoint_switch_box_2_out_57), .in_26(_6_11),
    .out_58(disjoint_switch_box_2_out_58), .in_27(_5_11), .out_59(disjoint_switch_box_2_out_59),
    .in_28(_4_11), .out_60(disjoint_switch_box_2_out_60), .in_29(_3_12),
    .out_61(disjoint_switch_box_2_out_61), .in_30(_2_12), .out_62(disjoint_switch_box_2_out_62),
    .in_31(_1_12), .out_63(disjoint_switch_box_2_out_63), .in_32(_0_12), .out_64(disjoint_switch_box_2_out_64));
  LED led_117 (.in(disjoint_switch_box_2_out_64));
  LED led_118 (.in(disjoint_switch_box_2_out_63));
  LED A3_10 (.in(logic_block_4__60));
  LED A2_10 (.in(logic_block_4__59));
  LED A1_10 (.in(logic_block_4__58));
  LED A0_10 (.in(logic_block_4__57));
  Clock Clk_12 (.out(Clk_12_out));
  LED led_119 (.in(disjoint_switch_box_2_out_40));
  LED led_120 (.in(disjoint_switch_box_2_out_39));
  LED led_121 (.in(disjoint_switch_box_2_out_41));
  LED led_122 (.in(disjoint_switch_box_2_out_43));
  LED led_123 (.in(disjoint_switch_box_2_out_45));
  LED led_124 (.in(disjoint_switch_box_2_out_47));
  LED led_125 (.in(disjoint_switch_box_2_out_49));
  LED led_126 (.in(disjoint_switch_box_2_out_51));
  LED led_127 (.in(disjoint_switch_box_2_out_53));
  LED led_128 (.in(disjoint_switch_box_2_out_55));
  LED led_129 (.in(input_output_block_2__18));
  LED led_130 (.in(input_output_block_2__19));
  LED led_131 (.in(input_output_block_2__17));
  LED led_132 (.in(input_output_block_2__20));
  Input_Output_Block input_output_block_2 (
    ._17(input_output_block_2__17), ._19(input_output_block_2__19), ._20(input_output_block_2__20),
    .in_16(_0_7), .in_15(_1_6), .in_14(_2_6), .in_13(_3_6), .in_12(_4_5), .in_11(_5_4), .in_10(_6_4),
    .in_9(_7_4), .in_8(_8_2), .in_7(_9_2), .in_6(_10_2), .in_5(_11_2), .in_4(_12_2), .in_3(_13_2),
    .in_2(_14_2), .in_1(_15_2), .in_17(_0_9), .in_18(_1_9), .in_19(_2_9), .in_20(_3_9), .in_21(_4_8),
    .in_22(_5_7), .in_23(_6_7), .in_24(_7_7), ._18(input_output_block_2__18));
endmodule

module Logic_Block (
  input  _76,
  input  _75,
  input  _74,
  input  _73,
  input  _72,
  input  _71,
  input  _70,
  input  _69,
  input  _68,
  input  _67,
  input  _66,
  input  _65,
  input  _64,
  input  _63,
  input  _62,
  input  _61,
  input  _1,
  input  _2,
  input  _3,
  input  _4,
  input  _5,
  input  _6,
  input  _7,
  input  _8,
  input  _9,
  input  _10,
  input  _11,
  input  _12,
  input  _13,
  input  _14,
  input  _15,
  input  _16,
  input  _92,
  input  _91,
  input  _90,
  input  _81,
  input  _89,
  input  _41,
  input  _82,
  input  _88,
  input  _42,
  input  _83,
  input  _87,
  input  _43,
  input  _44,
  input  _84,
  input  _85,
  input  _86,
  input  _45,
  input  _36,
  input  _35,
  input  _34,
  input  _33,
  input  _32,
  input  _31,
  input  _30,
  input  _29,
  input  _28,
  input  _27,
  input  _26,
  input  _25,
  input  _24,
  input  _23,
  input  _22,
  input  _21,
  input  _46,
  input  _47,
  input  _48,
  input  _49,
  input  _50,
  input  _51,
  input  _52,
  input  _53,
  input  _54,
  input  _55,
  input  _56,
  output _80,
  output _79,
  output _78,
  output _77,
  output _57,
  output _58,
  output _59,
  output _60,
  output _17,
  output _18,
  output _19,
  output _20,
  output _40,
  output _39,
  output _38,
  output _37
);

  wire Clock_out, or_1_out, or_2_out, or_3_out, or_4_out, or_5_out, or_6_out, or_7_out, or_8_out, or_9_out,
       or_10_out, or_11_out, or_12_out, or_13_out, or_14_out, or_15_out, or_16_out, Preset_out,
       programmable_local_interconnect_matrix_1__21, programmable_local_interconnect_matrix_1__22,
       programmable_local_interconnect_matrix_1__23, programmable_local_interconnect_matrix_1__24,
       programmable_local_interconnect_matrix_1__25, programmable_local_interconnect_matrix_1__26,
       programmable_local_interconnect_matrix_1__27, programmable_local_interconnect_matrix_1__28,
       programmable_local_interconnect_matrix_1__29, programmable_local_interconnect_matrix_1__30,
       programmable_local_interconnect_matrix_1__31, programmable_local_interconnect_matrix_1__32,
       programmable_local_interconnect_matrix_1__33, programmable_local_interconnect_matrix_1__34,
       programmable_local_interconnect_matrix_1__35, programmable_local_interconnect_matrix_1__36, Reset_out;

  or or_1 (or_1_out, _61, _1, _21, _41);
  or or_2 (or_2_out, _62, _2, _22, _42);
  or or_3 (or_3_out, _63, _3, _23, _43);
  or or_4 (or_4_out, _64, _4, _6, _44);
  or or_5 (or_5_out, _65, _5, _25, _45);
  or or_6 (or_6_out, _66, _6, _6, _46);
  or or_7 (or_7_out, _67, _7, _27, _47);
  or or_8 (or_8_out, _68, _6, _6, _48);
  or or_9 (or_9_out, _69, _9, _29, _49);
  or or_10 (or_10_out, _70, _10, _30, _50);
  or or_11 (or_11_out, _71, _11, _31, _51);
  or or_12 (or_12_out, _72, _12, _32, _52);
  or or_13 (or_13_out, _73, _13, _33, _53);
  or or_14 (or_14_out, _74, _14, _34, _54);
  or or_15 (or_15_out, _75, _15, _35, _55);
  or or_16 (or_16_out, _76, _16, _36, _56);
  Programmable_local_interconnect_matrix programmable_local_interconnect_matrix_1 (
    ._16(or_1_out), ._15(or_2_out), ._14(or_3_out), ._13(or_4_out), ._12(or_5_out), ._11(or_6_out),
    ._10(or_7_out), ._9(or_8_out), ._8(or_9_out), ._7(or_10_out), ._6(or_11_out), ._5(or_12_out),
    ._4(or_13_out), ._3(or_14_out), ._2(or_15_out), ._1(or_16_out), ._20(_17), ._19(_18), ._18(_19),
    ._17(_20), ._21(programmable_local_interconnect_matrix_1__21),
    ._23(programmable_local_interconnect_matrix_1__23), ._27(programmable_local_interconnect_matrix_1__27),
    ._29(programmable_local_interconnect_matrix_1__29), ._31(programmable_local_interconnect_matrix_1__31),
    ._33(programmable_local_interconnect_matrix_1__33), ._35(programmable_local_interconnect_matrix_1__35),
    ._22(programmable_local_interconnect_matrix_1__22), ._24(programmable_local_interconnect_matrix_1__24),
    ._26(programmable_local_interconnect_matrix_1__26), ._28(programmable_local_interconnect_matrix_1__28),
    ._30(programmable_local_interconnect_matrix_1__30), ._32(programmable_local_interconnect_matrix_1__32),
    ._34(programmable_local_interconnect_matrix_1__34), ._36(programmable_local_interconnect_matrix_1__36),
    ._25(programmable_local_interconnect_matrix_1__25));
  or Clock (Clock_out, _81, _84, _87, _90);
  or Reset (Reset_out, _82, _85, _88, _91);
  or Preset (Preset_out, _83, _86, _89, _92);
  Logic_element_1 logic_element_1_1 (
    .out_8(_17), .Clear(Clock_out), .in_6(Reset_out), .Preset(Preset_out),
    .A3(programmable_local_interconnect_matrix_1__21), .A2(programmable_local_interconnect_matrix_1__23),
    .A1(programmable_local_interconnect_matrix_1__25), .A0(programmable_local_interconnect_matrix_1__27));
  Logic_element_2 logic_element_2_1 (
    ._1(programmable_local_interconnect_matrix_1__29), ._2(programmable_local_interconnect_matrix_1__31),
    ._3(programmable_local_interconnect_matrix_1__33), ._4(programmable_local_interconnect_matrix_1__35),
    .out_8(_18), ._5(Clock_out), ._6(Reset_out), ._7(Preset_out));
  Logic_element_3 logic_element_3_1 (
    ._1(programmable_local_interconnect_matrix_1__22), ._2(programmable_local_interconnect_matrix_1__24),
    ._3(programmable_local_interconnect_matrix_1__26), ._4(programmable_local_interconnect_matrix_1__28),
    .out_8(_19), ._5(Clock_out), ._6(Reset_out), ._7(Preset_out));
  Logic_element_4 logic_element_4_1 (
    ._2(programmable_local_interconnect_matrix_1__32), ._3(programmable_local_interconnect_matrix_1__34),
    ._4(programmable_local_interconnect_matrix_1__36), .out_8(_20), ._5(Clock_out), ._6(Reset_out),
    ._7(Preset_out), ._1(programmable_local_interconnect_matrix_1__30));

  assign _8 = _6;
  assign _24 = _6;
  assign _26 = _6;
  assign _28 = _6;
  assign _37 = _17;
  assign _38 = _18;
  assign _39 = _19;
  assign _40 = _20;
  assign _57 = _17;
  assign _58 = _18;
  assign _59 = _19;
  assign _60 = _20;
  assign _77 = _17;
  assign _78 = _18;
  assign _79 = _19;
  assign _80 = _20;

  // Notes on the sheet:
  //   Input 00
  //   Input 15
  //   Clock
  //   General Purpose Feedback
  //   Clock
  //   Clock
  //   Clock
  //   Output 0
  //   Output 3
endmodule

module Logic_element_1 (
  input  A3,
  input  A2,
  input  A1,
  input  A0,
  input  Clear,
  input  in_6,
  input  Preset,
  output out_8
);

  wire d_ff_1_q, rom_1_data, rom_2_data;

  ROM #(.addrWidth(4), .dataWidth(1)) rom_1 (.addr({A3, A2, A1, A0}), .data(rom_1_data), .sel(1'b1));
  ROM #(.addrWidth(4), .dataWidth(1)) rom_2 (.addr(4'b1111), .data(rom_2_data), .sel(1'b1));
  D_Flip_Flop d_ff_1 (.clk(Clear), .D(rom_1_data), .Q(d_ff_1_q), .preset(in_6), .en(1'b1), .reset(Preset));  // open: Qn
  _01S u_01s_1 (._2(rom_1_data), ._3(d_ff_1_q), ._4(rom_2_data), .out_4(out_8));

  // Notes on the sheet:
  //   Look Up Table (LUT)
  //   Combinatory / Register
  //   contents of rom_1 (hex, n*v repeats v):
  //   1 0 0 1 1 0 0 1 0 1 1 0 0 1 1
  //   contents of rom_2 (hex, n*v repeats v):
  //   15*0 1
  //   Clock (Rising Edge)
endmodule

module Logic_element_2 (
  input  _1,
  input  _2,
  input  _3,
  input  _4,
  input  _5,
  input  _6,
  input  _7,
  output out_8
);

  wire d_ff_1_q, rom_1_data, rom_2_data;

  ROM #(.addrWidth(4), .dataWidth(1)) rom_1 (.addr({_1, _2, _3, _4}), .data(rom_1_data), .sel(1'b1));
  ROM #(.addrWidth(4), .dataWidth(1)) rom_2 (.addr(4'b1111), .data(rom_2_data), .sel(1'b1));
  D_Flip_Flop d_ff_1 (.clk(_5), .D(rom_1_data), .Q(d_ff_1_q), .preset(_6), .en(1'b1), .reset(_7));  // open: Qn
  _01S u_01s_1 (._2(rom_1_data), ._3(d_ff_1_q), ._4(rom_2_data), .out_4(out_8));

  // Notes on the sheet:
  //   A3
  //   A2
  //   A1
  //   A0
  //   Look Up Table (LUT)
  //   Combinatory / Register
  //   contents of rom_1 (hex, n*v repeats v):
  //   1 1 0 0 1 0 1 0 1 0 1 0 1 0 1
  //   contents of rom_2 (hex, n*v repeats v):
  //   15*0 1
  //   Clock (Rising Edge)
  //   Clear
  //   Preset
endmodule

module Logic_element_3 (
  input  _1,
  input  _2,
  input  _3,
  input  _4,
  input  _5,
  input  _6,
  input  _7,
  output out_8
);

  wire d_ff_1_q, rom_1_data, rom_2_data;

  ROM #(.addrWidth(4), .dataWidth(1)) rom_1 (.addr({_1, _2, _3, _4}), .data(rom_1_data), .sel(1'b1));
  ROM #(.addrWidth(4), .dataWidth(1)) rom_2 (.addr(4'b1111), .data(rom_2_data), .sel(1'b1));
  D_Flip_Flop d_ff_1 (.clk(_5), .D(rom_1_data), .Q(d_ff_1_q), .preset(_6), .en(1'b1), .reset(_7));  // open: Qn
  _01S u_01s_1 (._2(rom_1_data), ._3(d_ff_1_q), ._4(rom_2_data), .out_4(out_8));

  // Notes on the sheet:
  //   A3
  //   A2
  //   A1
  //   A0
  //   Look Up Table (LUT)
  //   Combinatory / Register
  //   contents of rom_1 (hex, n*v repeats v):
  //   0 1 0 0 1 1 0 5*1
  //   contents of rom_2 (hex, n*v repeats v):
  //   15*0 1
  //   Clock (Rising Edge)
  //   Clear
  //   Preset
endmodule

module Logic_element_4 (
  input  _1,
  input  _2,
  input  _3,
  input  _4,
  input  _5,
  input  _6,
  input  _7,
  output out_8
);

  wire d_ff_1_q, rom_1_data, rom_2_data;

  ROM #(.addrWidth(4), .dataWidth(1)) rom_1 (.addr({_1, _2, _3, _4}), .data(rom_1_data), .sel(1'b1));
  ROM #(.addrWidth(4), .dataWidth(1)) rom_2 (.addr(4'b1111), .data(rom_2_data), .sel(1'b1));
  D_Flip_Flop d_ff_1 (.clk(_5), .D(rom_1_data), .Q(d_ff_1_q), .preset(_6), .en(1'b1), .reset(_7));  // open: Qn
  _01S u_01s_1 (._2(rom_1_data), ._3(d_ff_1_q), ._4(rom_2_data), .out_4(out_8));

  // Notes on the sheet:
  //   A3
  //   A2
  //   A1
  //   A0
  //   Look Up Table (LUT)
  //   Combinatory / Register
  //   contents of rom_1 (hex, n*v repeats v):
  //   4*1 0 1 1 1 0 0 1
  //   contents of rom_2 (hex, n*v repeats v):
  //   15*0 1
  //   Clock (Rising Edge)
  //   Clear
  //   Preset
endmodule

// Programmable Local Interconnect Matrix
module Programmable_local_interconnect_matrix (
  input  _16,
  input  _15,
  input  _14,
  input  _13,
  input  _12,
  input  _11,
  input  _10,
  input  _9,
  input  _8,
  input  _7,
  input  _6,
  input  _5,
  input  _4,
  input  _3,
  input  _2,
  input  _1,
  input  _20,
  input  _19,
  input  _18,
  input  _17,
  output _21,
  output _22,
  output _23,
  output _24,
  output _26,
  output _25,
  output _27,
  output _28,
  output _29,
  output _30,
  output _31,
  output _32,
  output _33,
  output _34,
  output _35,
  output _36
);

  wire [4:0] rom_1_data, rom_2_data, rom_3_data, rom_4_data, rom_5_data, rom_6_data, rom_7_data, rom_8_data,
       rom_9_data, rom_10_data, rom_11_data, rom_12_data, rom_13_data, rom_14_data, rom_15_data, rom_16_data;

  _20_to_1_MUX u_20_to_1_mux_1 (
    ._8(_8), ._7(_7), ._6(_6), ._5(_5), ._4(_4), ._3(_3), ._2(_2), ._1(_1), ._9(_9), ._10(_10), ._11(_11),
    ._12(_12), ._13(_13), ._14(_14), ._15(_15), ._16(_16), ._17(_17), ._18(_18), ._19(_19), ._20(_20),
    ._21(rom_1_data[4]), ._22(rom_1_data[3]), ._23(rom_1_data[2]), ._24(rom_1_data[1]), ._25(rom_1_data[0]),
    ._26(_21));
  ROM #(.addrWidth(2), .dataWidth(5)) rom_1 (.addr(2'b11), .data(rom_1_data), .sel(1'b1));
  _20_to_1_MUX u_20_to_1_mux_2 (
    ._8(_8), ._7(_7), ._6(_6), ._5(_5), ._4(_4), ._3(_3), ._2(_2), ._1(_1), ._9(_9), ._10(_10), ._11(_11),
    ._12(_12), ._13(_13), ._14(_14), ._15(_15), ._16(_16), ._17(_17), ._18(_18), ._19(_19), ._20(_20),
    ._21(rom_2_data[4]), ._22(rom_2_data[3]), ._23(rom_2_data[2]), ._24(rom_2_data[1]), ._25(rom_2_data[0]),
    ._26(_23));
  ROM #(.addrWidth(2), .dataWidth(5)) rom_2 (.addr(2'b11), .data(rom_2_data), .sel(1'b1));
  _20_to_1_MUX u_20_to_1_mux_3 (
    ._8(_8), ._7(_7), ._6(_6), ._5(_5), ._4(_4), ._3(_3), ._2(_2), ._1(_1), ._9(_9), ._10(_10), ._11(_11),
    ._12(_12), ._13(_13), ._14(_14), ._15(_15), ._16(_16), ._17(_17), ._18(_18), ._19(_19), ._20(_20),
    ._21(rom_3_data[4]), ._22(rom_3_data[3]), ._23(rom_3_data[2]), ._24(rom_3_data[1]), ._25(rom_3_data[0]),
    ._26(_25));
  ROM #(.addrWidth(2), .dataWidth(5)) rom_3 (.addr(2'b11), .data(rom_3_data), .sel(1'b1));
  _20_to_1_MUX u_20_to_1_mux_4 (
    ._8(_8), ._7(_7), ._6(_6), ._5(_5), ._4(_4), ._3(_3), ._2(_2), ._1(_1), ._9(_9), ._10(_10), ._11(_11),
    ._12(_12), ._13(_13), ._14(_14), ._15(_15), ._16(_16), ._17(_17), ._18(_18), ._19(_19), ._20(_20),
    ._21(rom_4_data[4]), ._22(rom_4_data[3]), ._23(rom_4_data[2]), ._24(rom_4_data[1]), ._25(rom_4_data[0]),
    ._26(_27));
  ROM #(.addrWidth(2), .dataWidth(5)) rom_4 (.addr(2'b11), .data(rom_4_data), .sel(1'b1));
  _20_to_1_MUX u_20_to_1_mux_5 (
    ._8(_8), ._7(_7), ._6(_6), ._5(_5), ._4(_4), ._3(_3), ._2(_2), ._1(_1), ._9(_9), ._10(_10), ._11(_11),
    ._12(_12), ._13(_13), ._14(_14), ._15(_15), ._16(_16), ._17(_17), ._18(_18), ._19(_19), ._20(_20),
    ._21(rom_5_data[4]), ._22(rom_5_data[3]), ._23(rom_5_data[2]), ._24(rom_5_data[1]), ._25(rom_5_data[0]),
    ._26(_29));
  ROM #(.addrWidth(2), .dataWidth(5)) rom_5 (.addr(2'b11), .data(rom_5_data), .sel(1'b1));
  _20_to_1_MUX u_20_to_1_mux_6 (
    ._8(_8), ._7(_7), ._6(_6), ._5(_5), ._4(_4), ._3(_3), ._2(_2), ._1(_1), ._9(_9), ._10(_10), ._11(_11),
    ._12(_12), ._13(_13), ._14(_14), ._15(_15), ._16(_16), ._17(_17), ._18(_18), ._19(_19), ._20(_20),
    ._21(rom_6_data[4]), ._22(rom_6_data[3]), ._23(rom_6_data[2]), ._24(rom_6_data[1]), ._25(rom_6_data[0]),
    ._26(_31));
  ROM #(.addrWidth(2), .dataWidth(5)) rom_6 (.addr(2'b11), .data(rom_6_data), .sel(1'b1));
  _20_to_1_MUX u_20_to_1_mux_7 (
    ._8(_8), ._7(_7), ._6(_6), ._5(_5), ._4(_4), ._3(_3), ._2(_2), ._1(_1), ._9(_9), ._10(_10), ._11(_11),
    ._12(_12), ._13(_13), ._14(_14), ._15(_15), ._16(_16), ._17(_17), ._18(_18), ._19(_19), ._20(_20),
    ._21(rom_7_data[4]), ._22(rom_7_data[3]), ._23(rom_7_data[2]), ._24(rom_7_data[1]), ._25(rom_7_data[0]),
    ._26(_33));
  ROM #(.addrWidth(2), .dataWidth(5)) rom_7 (.addr(2'b11), .data(rom_7_data), .sel(1'b1));
  _20_to_1_MUX u_20_to_1_mux_8 (
    ._8(_8), ._7(_7), ._6(_6), ._5(_5), ._4(_4), ._3(_3), ._2(_2), ._1(_1), ._9(_9), ._10(_10), ._11(_11),
    ._12(_12), ._13(_13), ._14(_14), ._15(_15), ._16(_16), ._17(_17), ._18(_18), ._19(_19), ._20(_20),
    ._21(rom_8_data[4]), ._22(rom_8_data[3]), ._23(rom_8_data[2]), ._24(rom_8_data[1]), ._25(rom_8_data[0]),
    ._26(_35));
  ROM #(.addrWidth(2), .dataWidth(5)) rom_8 (.addr(2'b11), .data(rom_8_data), .sel(1'b1));
  ROM #(.addrWidth(2), .dataWidth(5)) rom_9 (.addr(2'b11), .data(rom_9_data), .sel(1'b1));
  ROM #(.addrWidth(2), .dataWidth(5)) rom_10 (.addr(2'b11), .data(rom_10_data), .sel(1'b1));
  ROM #(.addrWidth(2), .dataWidth(5)) rom_11 (.addr(2'b11), .data(rom_11_data), .sel(1'b1));
  ROM #(.addrWidth(2), .dataWidth(5)) rom_12 (.addr(2'b11), .data(rom_12_data), .sel(1'b1));
  ROM #(.addrWidth(2), .dataWidth(5)) rom_13 (.addr(2'b11), .data(rom_13_data), .sel(1'b1));
  ROM #(.addrWidth(2), .dataWidth(5)) rom_14 (.addr(2'b11), .data(rom_14_data), .sel(1'b1));
  ROM #(.addrWidth(2), .dataWidth(5)) rom_15 (.addr(2'b11), .data(rom_15_data), .sel(1'b1));
  ROM #(.addrWidth(2), .dataWidth(5)) rom_16 (.addr(2'b11), .data(rom_16_data), .sel(1'b1));
  _20_to_1_MUX u_20_to_1_mux_9 (
    ._8(_8), ._7(_7), ._6(_6), ._5(_5), ._4(_4), ._3(_3), ._2(_2), ._1(_1), ._9(_9), ._10(_10), ._11(_11),
    ._12(_12), ._13(_13), ._14(_14), ._15(_15), ._16(_16), ._17(_17), ._18(_18), ._19(_19), ._20(_20),
    ._21(rom_9_data[4]), ._22(rom_9_data[3]), ._23(rom_9_data[2]), ._24(rom_9_data[1]), ._25(rom_9_data[0]),
    ._26(_22));
  _20_to_1_MUX u_20_to_1_mux_10 (
    ._8(_8), ._7(_7), ._6(_6), ._5(_5), ._4(_4), ._3(_3), ._2(_2), ._1(_1), ._9(_9), ._10(_10), ._11(_11),
    ._12(_12), ._13(_13), ._14(_14), ._15(_15), ._16(_16), ._17(_17), ._18(_18), ._19(_19), ._20(_20),
    ._21(rom_10_data[4]), ._22(rom_10_data[3]), ._23(rom_10_data[2]), ._24(rom_10_data[1]),
    ._25(rom_10_data[0]), ._26(_24));
  _20_to_1_MUX u_20_to_1_mux_11 (
    ._8(_8), ._7(_7), ._6(_6), ._5(_5), ._4(_4), ._3(_3), ._2(_2), ._1(_1), ._9(_9), ._10(_10), ._11(_11),
    ._12(_12), ._13(_13), ._14(_14), ._15(_15), ._16(_16), ._17(_17), ._18(_18), ._19(_19), ._20(_20),
    ._21(rom_11_data[4]), ._22(rom_11_data[3]), ._23(rom_11_data[2]), ._24(rom_11_data[1]),
    ._25(rom_11_data[0]), ._26(_26));
  _20_to_1_MUX u_20_to_1_mux_12 (
    ._8(_8), ._7(_7), ._6(_6), ._5(_5), ._4(_4), ._3(_3), ._2(_2), ._1(_1), ._9(_9), ._10(_10), ._11(_11),
    ._12(_12), ._13(_13), ._14(_14), ._15(_15), ._16(_16), ._17(_17), ._18(_18), ._19(_19), ._20(_20),
    ._21(rom_12_data[4]), ._22(rom_12_data[3]), ._23(rom_12_data[2]), ._24(rom_12_data[1]),
    ._25(rom_12_data[0]), ._26(_28));
  _20_to_1_MUX u_20_to_1_mux_13 (
    ._8(_8), ._7(_7), ._6(_6), ._5(_5), ._4(_4), ._3(_3), ._2(_2), ._1(_1), ._9(_9), ._10(_10), ._11(_11),
    ._12(_12), ._13(_13), ._14(_14), ._15(_15), ._16(_16), ._17(_17), ._18(_18), ._19(_19), ._20(_20),
    ._21(rom_13_data[4]), ._22(rom_13_data[3]), ._23(rom_13_data[2]), ._24(rom_13_data[1]),
    ._25(rom_13_data[0]), ._26(_30));
  _20_to_1_MUX u_20_to_1_mux_14 (
    ._8(_8), ._7(_7), ._6(_6), ._5(_5), ._4(_4), ._3(_3), ._2(_2), ._1(_1), ._9(_9), ._10(_10), ._11(_11),
    ._12(_12), ._13(_13), ._14(_14), ._15(_15), ._16(_16), ._17(_17), ._18(_18), ._19(_19), ._20(_20),
    ._21(rom_14_data[4]), ._22(rom_14_data[3]), ._23(rom_14_data[2]), ._24(rom_14_data[1]),
    ._25(rom_14_data[0]), ._26(_32));
  _20_to_1_MUX u_20_to_1_mux_15 (
    ._8(_8), ._7(_7), ._6(_6), ._5(_5), ._4(_4), ._3(_3), ._2(_2), ._1(_1), ._9(_9), ._10(_10), ._11(_11),
    ._12(_12), ._13(_13), ._14(_14), ._15(_15), ._16(_16), ._17(_17), ._18(_18), ._19(_19), ._20(_20),
    ._21(rom_15_data[4]), ._22(rom_15_data[3]), ._23(rom_15_data[2]), ._24(rom_15_data[1]),
    ._25(rom_15_data[0]), ._26(_34));
  _20_to_1_MUX u_20_to_1_mux_16 (
    ._8(_8), ._7(_7), ._6(_6), ._5(_5), ._4(_4), ._3(_3), ._2(_2), ._1(_1), ._9(_9), ._10(_10), ._11(_11),
    ._12(_12), ._13(_13), ._14(_14), ._15(_15), ._16(_16), ._17(_17), ._18(_18), ._19(_19), ._20(_20),
    ._21(rom_16_data[4]), ._22(rom_16_data[3]), ._23(rom_16_data[2]), ._24(rom_16_data[1]),
    ._25(rom_16_data[0]), ._26(_36));

  // Notes on the sheet:
  //   IN 15
  //   LOCAL INPUTS
  //   IN 0
  //   LOCAL FEEDBACK
  //   LE 00
  //   LE 02
  //   LE 10
  //   LE 12
  //   LE 20
  //   LE 22
  //   LE 30
  //   LE 32
  //   contents of rom_1 (hex, n*v repeats v):
  //   0 0 0 10
  //   contents of rom_2 (hex, n*v repeats v):
  //   0 0 0 11
  //   contents of rom_3 (hex, n*v repeats v):
  //   0 0 0 12
  //   contents of rom_4 (hex, n*v repeats v):
  //   0 0 0 13
  //   contents of rom_5 (hex, n*v repeats v):
  //   0 0 0 10
  //   contents of rom_6 (hex, n*v repeats v):
  //   0 0 0 11
  //   contents of rom_7 (hex, n*v repeats v):
  //   0 0 0 12
  //   contents of rom_8 (hex, n*v repeats v):
  //   0 0 0 13
  //   LE 01
  //   LE 03
  //   LE 11
  //   LE 13
  //   LE 21
  //   LE 23
  //   LE 31
  //   LE 33
  //   contents of rom_9 (hex, n*v repeats v):
  //   0 0 0 10
  //   contents of rom_10 (hex, n*v repeats v):
  //   0 0 0 11
  //   contents of rom_11 (hex, n*v repeats v):
  //   0 0 0 12
  //   contents of rom_12 (hex, n*v repeats v):
  //   0 0 0 13
  //   contents of rom_13 (hex, n*v repeats v):
  //   0 0 0 10
  //   contents of rom_14 (hex, n*v repeats v):
  //   0 0 0 11
  //   contents of rom_15 (hex, n*v repeats v):
  //   0 0 0 12
  //   contents of rom_16 (hex, n*v repeats v):
  //   0 0 0 13
endmodule

module _20_to_1_MUX (
  input  _1,
  input  _2,
  input  _3,
  input  _4,
  input  _5,
  input  _6,
  input  _7,
  input  _8,
  input  _9,
  input  _10,
  input  _11,
  input  _12,
  input  _13,
  input  _14,
  input  _15,
  input  _16,
  input  _17,
  input  _18,
  input  _19,
  input  _20,
  input  _21,
  input  _22,
  input  _23,
  input  _24,
  input  _25,
  output _26
);

  wire mux_4_a_1_1__5, mux_8_a_1_1__5, mux_8_a_1_2__5;

  MUX_8_a_1 mux_8_a_1_1 (
    ._1(_1), ._2(_2), ._3(_3), ._4(_4), ._5(mux_8_a_1_1__5), ._6(_5), ._7(_6), ._8(_7), ._9(_8), ._10(_23),
    ._11(_24), ._12(_25));
  MUX_8_a_1 mux_8_a_1_2 (
    ._1(_9), ._2(_10), ._3(_11), ._4(_12), ._5(mux_8_a_1_2__5), ._6(_13), ._7(_14), ._8(_15), ._9(_16),
    ._10(_23), ._11(_24), ._12(_25));
  MUX_4_a_1 mux_4_a_1_1 (._1(_17), ._5(mux_4_a_1_1__5), ._6(_24), ._7(_25), ._2(_18), ._3(_19), ._4(_20));
  MUX_4_a_1 mux_4_a_1_2 (
    ._1(mux_8_a_1_1__5), ._5(_26), ._6(_21), ._7(_22), ._2(mux_8_a_1_2__5), ._3(mux_4_a_1_1__5));  // open: _4

  // Notes on the sheet:
  //   I0
  //   I20
  //   S4
  //   S0
  //   OUT
endmodule

module MUX_8_a_1 (
  input  _1,
  input  _2,
  input  _3,
  input  _4,
  input  _6,
  input  _7,
  input  _8,
  input  _9,
  input  _12,
  input  _11,
  input  _10,
  output _5
);

  wire mux_4_a_1_1__5, mux_4_a_1_2__5;

  MUX_4_a_1 mux_4_a_1_1 (._1(_1), ._5(mux_4_a_1_1__5), ._6(_11), ._7(_12), ._2(_2), ._3(_3), ._4(_4));
  MUX_4_a_1 mux_4_a_1_2 (._1(_6), ._5(mux_4_a_1_2__5), ._6(_11), ._7(_12), ._2(_7), ._3(_8), ._4(_9));
  _01S u_01s_1 (._2(mux_4_a_1_1__5), ._3(mux_4_a_1_2__5), ._4(_10), .out_4(_5));
endmodule

module MUX_4_a_1 (
  input  _1,
  input  _2,
  input  _3,
  input  _4,
  input  _7,
  input  _6,
  output _5
);

  wire n2_to_4_dec_1__3, n2_to_4_dec_1__4, n2_to_4_dec_1__5, n2_to_4_dec_1__6__y0_prime;

  _2_to_4_Dec u_2_to_4_dec_1 (
    .A__1(_7), .B__2(_6), ._3(n2_to_4_dec_1__3), ._4(n2_to_4_dec_1__4), ._5(n2_to_4_dec_1__5),
    ._6__Y0_prime(n2_to_4_dec_1__6__y0_prime));
  assign _5 = n2_to_4_dec_1__6__y0_prime ? _1 : 1'bz;  // Controlled_Buffer controlled_buffer_1
  assign _5 = n2_to_4_dec_1__5 ? _2 : 1'bz;  // Controlled_Buffer controlled_buffer_2
  assign _5 = n2_to_4_dec_1__4 ? _3 : 1'bz;  // Controlled_Buffer controlled_buffer_3
  assign _5 = n2_to_4_dec_1__3 ? _4 : 1'bz;  // Controlled_Buffer controlled_buffer_4
endmodule

module _01S (
  input  _2,
  input  _3,
  input  _4,
  output out_4
);

  wire not_1_out;

  not not_1 (not_1_out, _4);
  assign out_4 = not_1_out ? _2 : 1'bz;  // Controlled_Buffer controlled_buffer_1
  assign out_4 = _4 ? _3 : 1'bz;  // Controlled_Buffer controlled_buffer_2
endmodule

module _2_to_4_Dec (
  input  A__1,
  input  B__2,
  output _6__Y0_prime,
  output _5,
  output _4,
  output _3
);

  wire not_1_out, not_2_out;

  not not_1 (not_1_out, A__1);
  not not_2 (not_2_out, B__2);
  and and_1 (_6__Y0_prime, not_1_out, not_2_out);
  and and_2 (_5, A__1, not_2_out);
  and and_3 (_4, not_1_out, B__2);
  and and_4 (_3, A__1, B__2);
endmodule

module Connection_Box (
  input  _1,
  input  _2,
  input  _3,
  input  _4,
  input  _40,
  input  _39,
  input  _38,
  input  _37,
  input  _71,
  input  _69,
  input  _67,
  input  _65,
  input  _63,
  input  _61,
  input  _59,
  input  _57,
  input  _21,
  input  _23,
  input  _25,
  input  _27,
  input  _29,
  input  _31,
  input  _33,
  input  _35,
  output _72,
  output _70,
  output _68,
  output _66,
  output _64,
  output _62,
  output _60,
  output _58,
  output _22,
  output _24,
  output _26,
  output _28,
  output _30,
  output _32,
  output _34,
  output _36,
  output _56,
  output _5,
  output _55,
  output _6,
  output _54,
  output _7,
  output _53,
  output _8,
  output _52,
  output _9,
  output _51,
  output _10,
  output _50,
  output _11,
  output _49,
  output _12,
  output _48,
  output _13,
  output _47,
  output _14,
  output _46,
  output _15,
  output _45,
  output _16,
  output _44,
  output _17,
  output _43,
  output _18,
  output _42,
  output _19,
  output _41,
  output _20
);

  wire mini_interconection_box_1__4, mini_interconection_box_2__4, mini_interconection_box_3__4,
       mini_interconection_box_4__4, mini_interconection_box_5__4, mini_interconection_box_6__4,
       mini_interconection_box_7__4, mini_interconection_box_8__4, mux_8_a_1_1__5, mux_8_a_1_18__5,
       mux_8_a_1_35__5, mux_8_a_1_36__5, mux_8_a_1_37__5, mux_8_a_1_38__5, mux_8_a_1_39__5, mux_8_a_1_40__5;
  wire [3:0] rom_1_data, rom_2_data, rom_3_data, rom_4_data, rom_5_data, rom_6_data, rom_7_data, rom_8_data,
       rom_9_data, rom_10_data, rom_11_data, rom_12_data, rom_13_data, rom_14_data, rom_15_data, rom_16_data,
       rom_17_data, rom_18_data, rom_19_data, rom_20_data, rom_21_data, rom_22_data, rom_23_data,
       rom_24_data, rom_25_data, rom_26_data, rom_27_data, rom_28_data, rom_29_data, rom_30_data,
       rom_31_data, rom_32_data, rom_33_data, rom_34_data, rom_35_data, rom_36_data, rom_37_data,
       rom_38_data, rom_39_data, rom_40_data;

  ROM #(.addrWidth(4), .dataWidth(4)) rom_1 (.addr(4'b1111), .data(rom_1_data), .sel(1'b1));
  MUX_8_a_1 mux_8_a_1_1 (
    ._1(_40), ._2(_39), ._3(_38), ._4(_37), ._5(mux_8_a_1_1__5), ._6(_4), ._7(_3), ._8(_2), ._9(_1),
    ._10(rom_1_data[2]), ._11(rom_1_data[1]), ._12(rom_1_data[0]));
  Mini_Interconection_Box mini_interconection_box_1 (
    ._1(mux_8_a_1_1__5), ._6(_72), ._3(_21), ._5(_71), ._2(_22), ._4(mini_interconection_box_1__4));
  ROM #(.addrWidth(4), .dataWidth(4)) rom_2 (.addr(4'b1111), .data(rom_2_data), .sel(1'b1));
  MUX_8_a_1 mux_8_a_1_2 (
    ._1(mini_interconection_box_8__4), ._2(mini_interconection_box_7__4), ._3(mini_interconection_box_6__4),
    ._4(mini_interconection_box_5__4), ._5(_5), ._6(mini_interconection_box_4__4),
    ._7(mini_interconection_box_3__4), ._8(mini_interconection_box_2__4), ._9(mini_interconection_box_1__4),
    ._10(rom_2_data[2]), ._11(rom_2_data[1]), ._12(rom_2_data[0]));
  ROM #(.addrWidth(4), .dataWidth(4)) rom_3 (.addr(4'b1111), .data(rom_3_data), .sel(1'b1));
  MUX_8_a_1 mux_8_a_1_3 (
    ._1(mini_interconection_box_8__4), ._2(mini_interconection_box_7__4), ._3(mini_interconection_box_6__4),
    ._4(mini_interconection_box_5__4), ._5(_6), ._6(mini_interconection_box_4__4),
    ._7(mini_interconection_box_3__4), ._8(mini_interconection_box_2__4), ._9(mini_interconection_box_1__4),
    ._10(rom_3_data[2]), ._11(rom_3_data[1]), ._12(rom_3_data[0]));
  ROM #(.addrWidth(4), .dataWidth(4)) rom_4 (.addr(4'b1111), .data(rom_4_data), .sel(1'b1));
  MUX_8_a_1 mux_8_a_1_4 (
    ._1(mini_interconection_box_8__4), ._2(mini_interconection_box_6__4), ._3(mini_interconection_box_6__4),
    ._4(mini_interconection_box_5__4), ._5(_7), ._6(mini_interconection_box_4__4),
    ._7(mini_interconection_box_3__4), ._8(mini_interconection_box_2__4), ._9(mini_interconection_box_1__4),
    ._10(rom_4_data[2]), ._11(rom_4_data[1]), ._12(rom_4_data[0]));
  ROM #(.addrWidth(4), .dataWidth(4)) rom_5 (.addr(4'b1111), .data(rom_5_data), .sel(1'b1));
  MUX_8_a_1 mux_8_a_1_5 (
    ._1(mini_interconection_box_8__4), ._2(mini_interconection_box_7__4), ._3(mini_interconection_box_6__4),
    ._4(mini_interconection_box_5__4), ._5(_8), ._6(mini_interconection_box_4__4),
    ._7(mini_interconection_box_3__4), ._8(mini_interconection_box_2__4), ._9(mini_interconection_box_1__4),
    ._10(rom_5_data[2]), ._11(rom_5_data[1]), ._12(rom_5_data[0]));
  ROM #(.addrWidth(4), .dataWidth(4)) rom_6 (.addr(4'b1111), .data(rom_6_data), .sel(1'b1));
  MUX_8_a_1 mux_8_a_1_6 (
    ._1(mini_interconection_box_8__4), ._2(mini_interconection_box_7__4), ._3(mini_interconection_box_6__4),
    ._4(mini_interconection_box_5__4), ._5(_9), ._6(mini_interconection_box_4__4),
    ._7(mini_interconection_box_3__4), ._8(mini_interconection_box_2__4), ._9(mini_interconection_box_1__4),
    ._10(rom_6_data[2]), ._11(rom_6_data[1]), ._12(rom_6_data[0]));
  ROM #(.addrWidth(4), .dataWidth(4)) rom_7 (.addr(4'b1111), .data(rom_7_data), .sel(1'b1));
  MUX_8_a_1 mux_8_a_1_7 (
    ._1(mini_interconection_box_8__4), ._2(mini_interconection_box_7__4), ._3(mini_interconection_box_6__4),
    ._4(mini_interconection_box_5__4), ._5(_10), ._6(mini_interconection_box_4__4),
    ._7(mini_interconection_box_3__4), ._8(mini_interconection_box_2__4), ._9(mini_interconection_box_1__4),
    ._10(rom_7_data[2]), ._11(rom_7_data[1]), ._12(rom_7_data[0]));
  ROM #(.addrWidth(4), .dataWidth(4)) rom_8 (.addr(4'b1111), .data(rom_8_data), .sel(1'b1));
  MUX_8_a_1 mux_8_a_1_8 (
    ._1(mini_interconection_box_8__4), ._2(mini_interconection_box_7__4), ._3(mini_interconection_box_6__4),
    ._4(mini_interconection_box_5__4), ._5(_11), ._6(mini_interconection_box_4__4),
    ._7(mini_interconection_box_3__4), ._8(mini_interconection_box_2__4), ._9(mini_interconection_box_1__4),
    ._10(rom_8_data[2]), ._11(rom_8_data[1]), ._12(rom_8_data[0]));
  ROM #(.addrWidth(4), .dataWidth(4)) rom_9 (.addr(4'b1111), .data(rom_9_data), .sel(1'b1));
  MUX_8_a_1 mux_8_a_1_9 (
    ._1(mini_interconection_box_8__4), ._2(mini_interconection_box_7__4), ._3(mini_interconection_box_6__4),
    ._4(mini_interconection_box_5__4), ._5(_12), ._6(mini_interconection_box_4__4),
    ._7(mini_interconection_box_3__4), ._8(mini_interconection_box_2__4), ._9(mini_interconection_box_1__4),
    ._10(rom_9_data[2]), ._11(rom_9_data[1]), ._12(rom_9_data[0]));
  ROM #(.addrWidth(4), .dataWidth(4)) rom_10 (.addr(4'b1111), .data(rom_10_data), .sel(1'b1));
  MUX_8_a_1 mux_8_a_1_10 (
    ._1(mini_interconection_box_8__4), ._2(mini_interconection_box_7__4), ._3(mini_interconection_box_6__4),
    ._4(mini_interconection_box_5__4), ._5(_13), ._6(mini_interconection_box_4__4),
    ._7(mini_interconection_box_3__4), ._8(mini_interconection_box_2__4), ._9(mini_interconection_box_1__4),
    ._10(rom_10_data[2]), ._11(rom_10_data[1]), ._12(rom_10_data[0]));
  ROM #(.addrWidth(4), .dataWidth(4)) rom_11 (.addr(4'b1111), .data(rom_11_data), .sel(1'b1));
  MUX_8_a_1 mux_8_a_1_11 (
    ._1(mini_interconection_box_8__4), ._2(mini_interconection_box_7__4), ._3(mini_interconection_box_6__4),
    ._4(mini_interconection_box_5__4), ._5(_14), ._6(mini_interconection_box_4__4),
    ._7(mini_interconection_box_3__4), ._8(mini_interconection_box_2__4), ._9(mini_interconection_box_1__4),
    ._10(rom_11_data[2]), ._11(rom_11_data[1]), ._12(rom_11_data[0]));
  ROM #(.addrWidth(4), .dataWidth(4)) rom_12 (.addr(4'b1111), .data(rom_12_data), .sel(1'b1));
  MUX_8_a_1 mux_8_a_1_12 (
    ._1(mini_interconection_box_8__4), ._2(mini_interconection_box_7__4), ._3(mini_interconection_box_6__4),
    ._4(mini_interconection_box_5__4), ._5(_15), ._6(mini_interconection_box_4__4),
    ._7(mini_interconection_box_3__4), ._8(mini_interconection_box_2__4), ._9(mini_interconection_box_1__4),
    ._10(rom_12_data[2]), ._11(rom_12_data[1]), ._12(rom_12_data[0]));
  ROM #(.addrWidth(4), .dataWidth(4)) rom_13 (.addr(4'b1111), .data(rom_13_data), .sel(1'b1));
  MUX_8_a_1 mux_8_a_1_13 (
    ._1(mini_interconection_box_8__4), ._2(mini_interconection_box_7__4), ._3(mini_interconection_box_6__4),
    ._4(mini_interconection_box_5__4), ._5(_16), ._6(mini_interconection_box_4__4),
    ._7(mini_interconection_box_3__4), ._8(mini_interconection_box_2__4), ._9(mini_interconection_box_1__4),
    ._10(rom_13_data[2]), ._11(rom_13_data[1]), ._12(rom_13_data[0]));
  ROM #(.addrWidth(4), .dataWidth(4)) rom_14 (.addr(4'b1111), .data(rom_14_data), .sel(1'b1));
  MUX_8_a_1 mux_8_a_1_14 (
    ._1(mini_interconection_box_8__4), ._2(mini_interconection_box_7__4), ._3(mini_interconection_box_6__4),
    ._4(mini_interconection_box_5__4), ._5(_17), ._6(mini_interconection_box_4__4),
    ._7(mini_interconection_box_3__4), ._8(mini_interconection_box_2__4), ._9(mini_interconection_box_1__4),
    ._10(rom_14_data[2]), ._11(rom_14_data[1]), ._12(rom_14_data[0]));
  ROM #(.addrWidth(4), .dataWidth(4)) rom_15 (.addr(4'b1111), .data(rom_15_data), .sel(1'b1));
  MUX_8_a_1 mux_8_a_1_15 (
    ._1(mini_interconection_box_8__4), ._2(mini_interconection_box_7__4), ._3(mini_interconection_box_6__4),
    ._4(mini_interconection_box_5__4), ._5(_18), ._6(mini_interconection_box_4__4),
    ._7(mini_interconection_box_3__4), ._8(mini_interconection_box_2__4), ._9(mini_interconection_box_1__4),
    ._10(rom_15_data[2]), ._11(rom_15_data[1]), ._12(rom_15_data[0]));
  ROM #(.addrWidth(4), .dataWidth(4)) rom_16 (.addr(4'b1111), .data(rom_16_data), .sel(1'b1));
  MUX_8_a_1 mux_8_a_1_16 (
    ._1(mini_interconection_box_8__4), ._2(mini_interconection_box_7__4), ._3(mini_interconection_box_6__4),
    ._4(mini_interconection_box_5__4), ._5(_19), ._6(mini_interconection_box_4__4),
    ._7(mini_interconection_box_3__4), ._8(mini_interconection_box_2__4), ._9(mini_interconection_box_1__4),
    ._10(rom_16_data[2]), ._11(rom_16_data[1]), ._12(rom_16_data[0]));
  ROM #(.addrWidth(4), .dataWidth(4)) rom_17 (.addr(4'b1111), .data(rom_17_data), .sel(1'b1));
  MUX_8_a_1 mux_8_a_1_17 (
    ._1(mini_interconection_box_8__4), ._2(mini_interconection_box_7__4), ._3(mini_interconection_box_6__4),
    ._4(mini_interconection_box_5__4), ._5(_20), ._6(mini_interconection_box_4__4),
    ._7(mini_interconection_box_3__4), ._8(mini_interconection_box_2__4), ._9(mini_interconection_box_1__4),
    ._10(rom_17_data[2]), ._11(rom_17_data[1]), ._12(rom_17_data[0]));
  ROM #(.addrWidth(4), .dataWidth(4)) rom_18 (.addr(4'b1111), .data(rom_18_data), .sel(1'b1));
  MUX_8_a_1 mux_8_a_1_18 (
    ._1(_40), ._2(_39), ._3(_38), ._4(_37), ._5(mux_8_a_1_18__5), ._6(_4), ._7(_3), ._8(_2), ._9(_1),
    ._10(rom_18_data[2]), ._11(rom_18_data[1]), ._12(rom_18_data[0]));
  Mini_Interconection_Box mini_interconection_box_2 (
    ._1(mux_8_a_1_18__5), ._6(_70), ._3(_23), ._5(_69), ._2(_24), ._4(mini_interconection_box_2__4));
  ROM #(.addrWidth(4), .dataWidth(4)) rom_19 (.addr(4'b1111), .data(rom_19_data), .sel(1'b1));
  MUX_8_a_1 mux_8_a_1_19 (
    ._1(mini_interconection_box_8__4), ._2(mini_interconection_box_7__4), ._3(mini_interconection_box_6__4),
    ._4(mini_interconection_box_5__4), ._5(_56), ._6(mini_interconection_box_4__4),
    ._7(mini_interconection_box_3__4), ._8(mini_interconection_box_2__4), ._9(mini_interconection_box_1__4),
    ._10(rom_20_data[2]), ._11(rom_20_data[1]), ._12(rom_20_data[0]));
  ROM #(.addrWidth(4), .dataWidth(4)) rom_20 (.addr(4'b1111), .data(rom_20_data), .sel(1'b1));
  MUX_8_a_1 mux_8_a_1_20 (
    ._1(mini_interconection_box_8__4), ._2(mini_interconection_box_7__4), ._3(mini_interconection_box_6__4),
    ._4(mini_interconection_box_5__4), ._5(_55), ._6(mini_interconection_box_4__4),
    ._7(mini_interconection_box_3__4), ._8(mini_interconection_box_2__4), ._9(mini_interconection_box_1__4),
    ._10(rom_19_data[2]), ._11(rom_19_data[1]), ._12(rom_19_data[0]));
  MUX_8_a_1 mux_8_a_1_21 (
    ._1(mini_interconection_box_8__4), ._2(mini_interconection_box_7__4), ._3(mini_interconection_box_6__4),
    ._4(mini_interconection_box_5__4), ._5(_54), ._6(mini_interconection_box_4__4),
    ._7(mini_interconection_box_3__4), ._8(mini_interconection_box_2__4), ._9(mini_interconection_box_1__4),
    ._10(rom_21_data[2]), ._11(rom_21_data[1]), ._12(rom_21_data[0]));
  ROM #(.addrWidth(4), .dataWidth(4)) rom_21 (.addr(4'b1111), .data(rom_21_data), .sel(1'b1));
  MUX_8_a_1 mux_8_a_1_22 (
    ._1(mini_interconection_box_8__4), ._2(mini_interconection_box_7__4), ._3(mini_interconection_box_6__4),
    ._4(mini_interconection_box_5__4), ._5(_53), ._6(mini_interconection_box_4__4),
    ._7(mini_interconection_box_3__4), ._8(mini_interconection_box_2__4), ._9(mini_interconection_box_1__4),
    ._10(rom_22_data[2]), ._11(rom_22_data[1]), ._12(rom_22_data[0]));
  ROM #(.addrWidth(4), .dataWidth(4)) rom_22 (.addr(4'b1111), .data(rom_22_data), .sel(1'b1));
  MUX_8_a_1 mux_8_a_1_23 (
    ._1(mini_interconection_box_8__4), ._2(mini_interconection_box_7__4), ._3(mini_interconection_box_6__4),
    ._4(mini_interconection_box_5__4), ._5(_52), ._6(mini_interconection_box_4__4),
    ._7(mini_interconection_box_3__4), ._8(mini_interconection_box_2__4), ._9(mini_interconection_box_1__4),
    ._10(rom_23_data[2]), ._11(rom_23_data[1]), ._12(rom_23_data[0]));
  ROM #(.addrWidth(4), .dataWidth(4)) rom_23 (.addr(4'b1111), .data(rom_23_data), .sel(1'b1));
  MUX_8_a_1 mux_8_a_1_24 (
    ._1(mini_interconection_box_8__4), ._2(mini_interconection_box_7__4), ._3(mini_interconection_box_6__4),
    ._4(mini_interconection_box_5__4), ._5(_51), ._6(mini_interconection_box_4__4),
    ._7(mini_interconection_box_3__4), ._8(mini_interconection_box_2__4), ._9(mini_interconection_box_1__4),
    ._10(rom_24_data[2]), ._11(rom_24_data[1]), ._12(rom_24_data[0]));
  ROM #(.addrWidth(4), .dataWidth(4)) rom_24 (.addr(4'b1111), .data(rom_24_data), .sel(1'b1));
  MUX_8_a_1 mux_8_a_1_25 (
    ._1(mini_interconection_box_8__4), ._2(mini_interconection_box_7__4), ._3(mini_interconection_box_6__4),
    ._4(mini_interconection_box_5__4), ._5(_50), ._6(mini_interconection_box_4__4),
    ._7(mini_interconection_box_3__4), ._8(mini_interconection_box_2__4), ._9(mini_interconection_box_1__4),
    ._10(rom_25_data[2]), ._11(rom_25_data[1]), ._12(rom_25_data[0]));
  ROM #(.addrWidth(4), .dataWidth(4)) rom_25 (.addr(4'b1111), .data(rom_25_data), .sel(1'b1));
  MUX_8_a_1 mux_8_a_1_26 (
    ._1(mini_interconection_box_8__4), ._2(mini_interconection_box_7__4), ._3(mini_interconection_box_6__4),
    ._4(mini_interconection_box_5__4), ._5(_49), ._6(mini_interconection_box_4__4),
    ._7(mini_interconection_box_3__4), ._8(mini_interconection_box_2__4), ._9(mini_interconection_box_1__4),
    ._10(rom_26_data[2]), ._11(rom_26_data[1]), ._12(rom_26_data[0]));
  ROM #(.addrWidth(4), .dataWidth(4)) rom_26 (.addr(4'b1111), .data(rom_26_data), .sel(1'b1));
  MUX_8_a_1 mux_8_a_1_27 (
    ._1(mini_interconection_box_8__4), ._2(mini_interconection_box_7__4), ._3(mini_interconection_box_6__4),
    ._4(mini_interconection_box_5__4), ._5(_48), ._6(mini_interconection_box_4__4),
    ._7(mini_interconection_box_3__4), ._8(mini_interconection_box_2__4), ._9(mini_interconection_box_1__4),
    ._10(rom_27_data[2]), ._11(rom_27_data[1]), ._12(rom_27_data[0]));
  ROM #(.addrWidth(4), .dataWidth(4)) rom_27 (.addr(4'b1111), .data(rom_27_data), .sel(1'b1));
  MUX_8_a_1 mux_8_a_1_28 (
    ._1(mini_interconection_box_8__4), ._2(mini_interconection_box_7__4), ._3(mini_interconection_box_6__4),
    ._4(mini_interconection_box_5__4), ._5(_47), ._6(mini_interconection_box_4__4),
    ._7(mini_interconection_box_3__4), ._8(mini_interconection_box_2__4), ._9(mini_interconection_box_1__4),
    ._10(rom_28_data[2]), ._11(rom_28_data[1]), ._12(rom_28_data[0]));
  ROM #(.addrWidth(4), .dataWidth(4)) rom_28 (.addr(4'b1111), .data(rom_28_data), .sel(1'b1));
  MUX_8_a_1 mux_8_a_1_29 (
    ._1(mini_interconection_box_8__4), ._2(mini_interconection_box_7__4), ._3(mini_interconection_box_6__4),
    ._4(mini_interconection_box_5__4), ._5(_46), ._6(mini_interconection_box_4__4),
    ._7(mini_interconection_box_3__4), ._8(mini_interconection_box_2__4), ._9(mini_interconection_box_1__4),
    ._10(rom_29_data[2]), ._11(rom_29_data[1]), ._12(rom_29_data[0]));
  ROM #(.addrWidth(4), .dataWidth(4)) rom_29 (.addr(4'b1111), .data(rom_29_data), .sel(1'b1));
  MUX_8_a_1 mux_8_a_1_30 (
    ._1(mini_interconection_box_8__4), ._2(mini_interconection_box_7__4), ._3(mini_interconection_box_6__4),
    ._4(mini_interconection_box_5__4), ._5(_45), ._6(mini_interconection_box_4__4),
    ._7(mini_interconection_box_3__4), ._8(mini_interconection_box_2__4), ._9(mini_interconection_box_1__4),
    ._10(rom_30_data[2]), ._11(rom_30_data[1]), ._12(rom_30_data[0]));
  ROM #(.addrWidth(4), .dataWidth(4)) rom_30 (.addr(4'b1111), .data(rom_30_data), .sel(1'b1));
  MUX_8_a_1 mux_8_a_1_31 (
    ._1(mini_interconection_box_8__4), ._2(mini_interconection_box_7__4), ._3(mini_interconection_box_6__4),
    ._4(mini_interconection_box_5__4), ._5(_44), ._6(mini_interconection_box_4__4),
    ._7(mini_interconection_box_3__4), ._8(mini_interconection_box_2__4), ._9(mini_interconection_box_1__4),
    ._10(rom_31_data[2]), ._11(rom_31_data[1]), ._12(rom_31_data[0]));
  ROM #(.addrWidth(4), .dataWidth(4)) rom_31 (.addr(4'b1111), .data(rom_31_data), .sel(1'b1));
  MUX_8_a_1 mux_8_a_1_32 (
    ._1(mini_interconection_box_8__4), ._2(mini_interconection_box_7__4), ._3(mini_interconection_box_6__4),
    ._4(mini_interconection_box_5__4), ._5(_43), ._6(mini_interconection_box_4__4),
    ._7(mini_interconection_box_3__4), ._8(mini_interconection_box_2__4), ._9(mini_interconection_box_1__4),
    ._10(rom_32_data[2]), ._11(rom_32_data[1]), ._12(rom_32_data[0]));
  ROM #(.addrWidth(4), .dataWidth(4)) rom_32 (.addr(4'b1111), .data(rom_32_data), .sel(1'b1));
  MUX_8_a_1 mux_8_a_1_33 (
    ._1(mini_interconection_box_8__4), ._2(mini_interconection_box_7__4), ._3(mini_interconection_box_6__4),
    ._4(mini_interconection_box_5__4), ._5(_42), ._6(mini_interconection_box_4__4),
    ._7(mini_interconection_box_3__4), ._8(mini_interconection_box_2__4), ._9(mini_interconection_box_1__4),
    ._10(rom_33_data[2]), ._11(rom_33_data[1]), ._12(rom_33_data[0]));
  ROM #(.addrWidth(4), .dataWidth(4)) rom_33 (.addr(4'b1111), .data(rom_33_data), .sel(1'b1));
  MUX_8_a_1 mux_8_a_1_34 (
    ._1(mini_interconection_box_8__4), ._2(mini_interconection_box_7__4), ._3(mini_interconection_box_6__4),
    ._4(mini_interconection_box_5__4), ._5(_41), ._6(mini_interconection_box_4__4),
    ._7(mini_interconection_box_3__4), ._8(mini_interconection_box_2__4), ._9(mini_interconection_box_1__4),
    ._10(rom_34_data[2]), ._11(rom_34_data[1]), ._12(rom_34_data[0]));
  ROM #(.addrWidth(4), .dataWidth(4)) rom_34 (.addr(4'b1111), .data(rom_34_data), .sel(1'b1));
  ROM #(.addrWidth(4), .dataWidth(4)) rom_35 (.addr(4'b1111), .data(rom_35_data), .sel(1'b1));
  MUX_8_a_1 mux_8_a_1_35 (
    ._1(_40), ._2(_39), ._3(_38), ._4(_37), ._5(mux_8_a_1_35__5), ._6(_4), ._7(_3), ._8(_2), ._9(_1),
    ._10(rom_35_data[2]), ._11(rom_35_data[1]), ._12(rom_35_data[0]));
  Mini_Interconection_Box mini_interconection_box_3 (
    ._1(mux_8_a_1_35__5), ._6(_68), ._3(_25), ._5(_67), ._2(_26), ._4(mini_interconection_box_3__4));
  ROM #(.addrWidth(4), .dataWidth(4)) rom_36 (.addr(4'b1111), .data(rom_36_data), .sel(1'b1));
  MUX_8_a_1 mux_8_a_1_36 (
    ._1(_40), ._2(_39), ._3(_38), ._4(_37), ._5(mux_8_a_1_36__5), ._6(_4), ._7(_3), ._8(_2), ._9(_1),
    ._10(rom_36_data[2]), ._11(rom_36_data[1]), ._12(rom_36_data[0]));
  Mini_Interconection_Box mini_interconection_box_4 (
    ._1(mux_8_a_1_36__5), ._6(_66), ._3(_27), ._5(_65), ._2(_28), ._4(mini_interconection_box_4__4));
  ROM #(.addrWidth(4), .dataWidth(4)) rom_37 (.addr(4'b1111), .data(rom_37_data), .sel(1'b1));
  MUX_8_a_1 mux_8_a_1_37 (
    ._1(_40), ._2(_39), ._3(_38), ._4(_37), ._5(mux_8_a_1_37__5), ._6(_4), ._7(_3), ._8(_2), ._9(_1),
    ._10(rom_37_data[2]), ._11(rom_37_data[1]), ._12(rom_37_data[0]));
  Mini_Interconection_Box mini_interconection_box_5 (
    ._1(mux_8_a_1_37__5), ._6(_64), ._3(_29), ._5(_63), ._2(_30), ._4(mini_interconection_box_5__4));
  ROM #(.addrWidth(4), .dataWidth(4)) rom_38 (.addr(4'b1111), .data(rom_38_data), .sel(1'b1));
  MUX_8_a_1 mux_8_a_1_38 (
    ._1(_40), ._2(_39), ._3(_38), ._4(_37), ._5(mux_8_a_1_38__5), ._6(_4), ._7(_3), ._8(_2), ._9(_1),
    ._10(rom_38_data[2]), ._11(rom_38_data[1]), ._12(rom_38_data[0]));
  Mini_Interconection_Box mini_interconection_box_6 (
    ._1(mux_8_a_1_38__5), ._6(_62), ._3(_31), ._5(_61), ._2(_32), ._4(mini_interconection_box_6__4));
  ROM #(.addrWidth(4), .dataWidth(4)) rom_39 (.addr(4'b1111), .data(rom_39_data), .sel(1'b1));
  MUX_8_a_1 mux_8_a_1_39 (
    ._1(_40), ._2(_39), ._3(_38), ._4(_37), ._5(mux_8_a_1_39__5), ._6(_4), ._7(_3), ._8(_2), ._9(_1),
    ._10(rom_39_data[2]), ._11(rom_39_data[1]), ._12(rom_39_data[0]));
  Mini_Interconection_Box mini_interconection_box_7 (
    ._1(mux_8_a_1_39__5), ._6(_60), ._3(_33), ._5(_59), ._2(_34), ._4(mini_interconection_box_7__4));
  ROM #(.addrWidth(4), .dataWidth(4)) rom_40 (.addr(4'b1111), .data(rom_40_data), .sel(1'b1));
  MUX_8_a_1 mux_8_a_1_40 (
    ._1(_40), ._2(_39), ._3(_38), ._4(_37), ._5(mux_8_a_1_40__5), ._6(_4), ._7(_3), ._8(_2), ._9(_1),
    ._10(rom_40_data[2]), ._11(rom_40_data[1]), ._12(rom_40_data[0]));
  Mini_Interconection_Box mini_interconection_box_8 (
    ._1(mux_8_a_1_40__5), ._6(_58), ._3(_35), ._5(_57), ._2(_36), ._4(mini_interconection_box_8__4));

  // Notes on the sheet:
  //   0 - Right Output 0
  //   1 - Right Output 1
  //   2 - Right Output 2
  //   3 - Right Output 3
  //   4 - Left Output 0
  //   5 - Left Output 1
  //   6 - Left Output 2
  //   7 - Left Output 3
  //   From Left Logic Block Outputs
  //   CHANNEL MUX Programming
  //   contents of rom_1 (hex, n*v repeats v):
  //   15*0 4
  //   To Left Logic Block Inputs
  //   0
  //   1
  //   2
  //   3
  //   4
  //   5
  //   6
  //   7
  //   8
  //   9
  //   10
  //   11
  //   12
  //   13
  //   14
  //   15
  //   contents of rom_3 (hex, n*v repeats v):
  //   15*0 1
  //   contents of rom_4 (hex, n*v repeats v):
  //   15*0 2
  //   contents of rom_5 (hex, n*v repeats v):
  //   15*0 3
  //   contents of rom_6 (hex, n*v repeats v):
  //   15*0 4
  //   contents of rom_7 (hex, n*v repeats v):
  //   15*0 5
  //   contents of rom_8 (hex, n*v repeats v):
  //   15*0 6
  //   contents of rom_9 (hex, n*v repeats v):
  //   15*0 7
  //   contents of rom_10 (hex, n*v repeats v):
  //   15*0 8
  //   contents of rom_11 (hex, n*v repeats v):
  //   15*0 9
  //   contents of rom_12 (hex, n*v repeats v):
  //   15*0 a
  //   contents of rom_13 (hex, n*v repeats v):
  //   15*0 b
  //   contents of rom_14 (hex, n*v repeats v):
  //   15*0 c
  //   contents of rom_15 (hex, n*v repeats v):
  //   15*0 d
  //   contents of rom_16 (hex, n*v repeats v):
  //   15*0 e
  //   contents of rom_17 (hex, n*v repeats v):
  //   15*0 f
  //   contents of rom_18 (hex, n*v repeats v):
  //   15*0 5
  //   contents of rom_19 (hex, n*v repeats v):
  //   15*0 1
  //   contents of rom_21 (hex, n*v repeats v):
  //   15*0 2
  //   contents of rom_22 (hex, n*v repeats v):
  //   15*0 3
  //   contents of rom_23 (hex, n*v repeats v):
  //   15*0 4
  //   contents of rom_24 (hex, n*v repeats v):
  //   15*0 5
  //   contents of rom_25 (hex, n*v repeats v):
  //   15*0 6
  //   contents of rom_26 (hex, n*v repeats v):
  //   15*0 7
  //   contents of rom_27 (hex, n*v repeats v):
  //   15*0 8
  //   contents of rom_28 (hex, n*v repeats v):
  //   15*0 9
  //   contents of rom_29 (hex, n*v repeats v):
  //   15*0 a
  //   contents of rom_30 (hex, n*v repeats v):
  //   15*0 b
  //   contents of rom_31 (hex, n*v repeats v):
  //   15*0 c
  //   contents of rom_32 (hex, n*v repeats v):
  //   15*0 d
  //   contents of rom_33 (hex, n*v repeats v):
  //   15*0 e
  //   contents of rom_34 (hex, n*v repeats v):
  //   15*0 f
  //   contents of rom_35 (hex, n*v repeats v):
  //   15*0 6
  //   0
  //   1
  //   2
  //   3
  //   4
  //   5
  //   6
  //   7
  //   8
  //   9
  //   10
  //   11
  //   12
  //   13
  //   14
  //   15
  //   To Right Logic Block Inputs
  //   INPUT MUX Programming
  //   0 - Channel 0
  //   1 - Channel 1
  //   2 - Channel 2
  //   5 - Channel 5
  //   6 - Channel 5
  //   6 - Left Output 2
  //   contents of rom_36 (hex, n*v repeats v):
  //   15*0 7
  //   contents of rom_37 (hex, n*v repeats v):
  //   15*0 3
  //   contents of rom_38 (hex, n*v repeats v):
  //   15*0 2
  //   contents of rom_39 (hex, n*v repeats v):
  //   15*0 1
  //   From Right Logic Block Outputs
endmodule

module Mini_Interconection_Box (
  input  _5,
  input  _1,
  input  _3,
  output _6,
  output _4,
  output _2
);

  wire [1:0] rom_1_data;

  ROM #(.addrWidth(4), .dataWidth(2)) rom_1 (.addr(4'b1111), .data(rom_1_data), .sel(1'b1));
  _01S u_01s_1 (._2(_5), ._3(_1), ._4(rom_1_data[0]), .out_4(_2));
  _01S u_01s_2 (._2(_3), ._3(_1), ._4(rom_1_data[0]), .out_4(_6));
  MUX_4_a_1 mux_4_a_1_1 (._1(_5), ._5(_4), ._6(rom_1_data[0]), ._7(rom_1_data[1]), ._2(_3), ._3(_1), ._4(_1));

  // Notes on the sheet:
  //   |D1|D0|
  //   Mini Interconection Box
  //   |0|0| Input UP & ByPass Selected
  //   |0|1| Input Down & ByPass Selected
  //   contents of rom_1 (hex, n*v repeats v):
  //   15*0 3
  //   |1|X| Output (to UP Channel, Down Channel and Inputs)
  //   OUTPUT / INPUT & BYPASS'
  //   INPUT DOWN / INPUT UP'
  //   FROM OUTPUTS
  //   TO INPUTS
endmodule

module Disjoint_Switch_Box (
  input  _7,
  input  _6,
  input  _5,
  input  _4,
  input  _3,
  input  _2,
  input  _1,
  input  _0,
  input  in_9,
  input  in_10,
  input  in_11,
  input  in_12,
  input  in_13,
  input  in_14,
  input  in_15,
  input  in_16,
  input  in_17,
  input  in_18,
  input  in_19,
  input  in_20,
  input  in_21,
  input  in_22,
  input  in_23,
  input  in_24,
  input  in_25,
  input  in_26,
  input  in_27,
  input  in_28,
  input  in_29,
  input  in_30,
  input  in_31,
  input  in_32,
  output out_33,
  output out_34,
  output out_35,
  output out_36,
  output out_37,
  output out_38,
  output out_39,
  output out_40,
  output out_41,
  output out_42,
  output out_43,
  output out_44,
  output out_45,
  output out_46,
  output out_47,
  output out_48,
  output out_49,
  output out_50,
  output out_51,
  output out_52,
  output out_53,
  output out_54,
  output out_55,
  output out_56,
  output out_57,
  output out_58,
  output out_59,
  output out_60,
  output out_61,
  output out_62,
  output out_63,
  output out_64
);

  wire [1:0] rom_1_data, rom_2_data, rom_3_data, rom_4_data, rom_5_data, rom_6_data, rom_7_data, rom_8_data,
       rom_9_data, rom_10_data, rom_11_data, rom_12_data, rom_13_data, rom_14_data, rom_15_data, rom_16_data,
       rom_17_data, rom_18_data, rom_19_data, rom_20_data, rom_21_data, rom_22_data, rom_23_data,
       rom_24_data, rom_25_data, rom_26_data, rom_27_data, rom_28_data, rom_29_data, rom_30_data,
       rom_31_data, rom_32_data;

  ROM #(.addrWidth(4), .dataWidth(2)) rom_1 (.addr(4'b1111), .data(rom_1_data), .sel(1'b1));
  ROM #(.addrWidth(4), .dataWidth(2)) rom_2 (.addr(4'b1111), .data(rom_2_data), .sel(1'b1));
  ROM #(.addrWidth(4), .dataWidth(2)) rom_3 (.addr(4'b1111), .data(rom_3_data), .sel(1'b1));
  ROM #(.addrWidth(4), .dataWidth(2)) rom_4 (.addr(4'b1111), .data(rom_4_data), .sel(1'b1));
  ROM #(.addrWidth(4), .dataWidth(2)) rom_5 (.addr(4'b1111), .data(rom_5_data), .sel(1'b1));
  ROM #(.addrWidth(4), .dataWidth(2)) rom_6 (.addr(4'b1111), .data(rom_6_data), .sel(1'b1));
  ROM #(.addrWidth(4), .dataWidth(2)) rom_7 (.addr(4'b1111), .data(rom_7_data), .sel(1'b1));
  ROM #(.addrWidth(4), .dataWidth(2)) rom_8 (.addr(4'b1111), .data(rom_8_data), .sel(1'b1));
  MUX_4_a_1 mux_4_a_1_1 (
    ._1(in_10), ._5(out_42), ._6(rom_1_data[1]), ._7(rom_1_data[0]), ._2(in_32), ._3(_0), ._4(in_9));
  MUX_4_a_1 mux_4_a_1_2 (
    ._1(in_12), ._5(out_44), ._6(rom_2_data[1]), ._7(rom_2_data[0]), ._2(in_31), ._3(_1), ._4(in_11));
  MUX_4_a_1 mux_4_a_1_3 (
    ._1(in_14), ._5(out_46), ._6(rom_3_data[1]), ._7(rom_3_data[0]), ._2(in_30), ._3(_2), ._4(in_13));
  MUX_4_a_1 mux_4_a_1_4 (
    ._1(in_16), ._5(out_48), ._6(rom_4_data[1]), ._7(rom_4_data[0]), ._2(in_29), ._3(_3), ._4(in_15));
  MUX_4_a_1 mux_4_a_1_5 (
    ._1(in_18), ._5(out_50), ._6(rom_5_data[1]), ._7(rom_5_data[0]), ._2(in_28), ._3(_4), ._4(in_17));
  MUX_4_a_1 mux_4_a_1_6 (
    ._1(in_20), ._5(out_52), ._6(rom_6_data[1]), ._7(rom_6_data[0]), ._2(in_27), ._3(_5), ._4(in_19));
  MUX_4_a_1 mux_4_a_1_7 (
    ._1(in_22), ._5(out_54), ._6(rom_7_data[1]), ._7(rom_7_data[0]), ._2(in_26), ._3(_6), ._4(in_21));
  MUX_4_a_1 mux_4_a_1_8 (
    ._1(in_24), ._5(out_56), ._6(rom_8_data[1]), ._7(rom_8_data[0]), ._2(in_25), ._3(_7), ._4(in_23));
  ROM #(.addrWidth(4), .dataWidth(2)) rom_9 (.addr(4'b1111), .data(rom_9_data), .sel(1'b1));
  MUX_4_a_1 mux_4_a_1_9 (
    ._1(in_25), ._5(out_33), ._6(rom_9_data[1]), ._7(rom_9_data[0]), ._2(in_23), ._3(in_24), ._4(_7));
  MUX_4_a_1 mux_4_a_1_10 (
    ._1(_7), ._5(out_57), ._6(rom_10_data[1]), ._7(rom_10_data[0]), ._2(in_24), ._3(in_23), ._4(in_25));
  ROM #(.addrWidth(4), .dataWidth(2)) rom_10 (.addr(4'b1111), .data(rom_10_data), .sel(1'b1));
  ROM #(.addrWidth(4), .dataWidth(2)) rom_11 (.addr(4'b1111), .data(rom_11_data), .sel(1'b1));
  MUX_4_a_1 mux_4_a_1_11 (
    ._1(in_26), ._5(out_34), ._6(rom_11_data[1]), ._7(rom_11_data[0]), ._2(in_21), ._3(in_22), ._4(_6));
  MUX_4_a_1 mux_4_a_1_12 (
    ._1(_6), ._5(out_58), ._6(rom_12_data[1]), ._7(rom_12_data[0]), ._2(in_22), ._3(in_21), ._4(in_26));
  ROM #(.addrWidth(4), .dataWidth(2)) rom_12 (.addr(4'b1111), .data(rom_12_data), .sel(1'b1));
  ROM #(.addrWidth(4), .dataWidth(2)) rom_13 (.addr(4'b1111), .data(rom_13_data), .sel(1'b1));
  MUX_4_a_1 mux_4_a_1_13 (
    ._1(in_27), ._5(out_35), ._6(rom_13_data[1]), ._7(rom_13_data[0]), ._2(in_19), ._3(in_20), ._4(_5));
  MUX_4_a_1 mux_4_a_1_14 (
    ._1(_5), ._5(out_59), ._6(rom_14_data[1]), ._7(rom_14_data[0]), ._2(in_20), ._3(in_19), ._4(in_27));
  ROM #(.addrWidth(4), .dataWidth(2)) rom_14 (.addr(4'b1111), .data(rom_14_data), .sel(1'b1));
  ROM #(.addrWidth(4), .dataWidth(2)) rom_15 (.addr(4'b1111), .data(rom_15_data), .sel(1'b1));
  MUX_4_a_1 mux_4_a_1_15 (
    ._1(in_28), ._5(out_36), ._6(rom_15_data[1]), ._7(rom_15_data[0]), ._2(in_17), ._3(in_18), ._4(_4));
  MUX_4_a_1 mux_4_a_1_16 (
    ._1(_4), ._5(out_60), ._6(rom_16_data[1]), ._7(rom_16_data[0]), ._2(in_18), ._3(in_17), ._4(in_28));
  ROM #(.addrWidth(4), .dataWidth(2)) rom_16 (.addr(4'b1111), .data(rom_16_data), .sel(1'b1));
  ROM #(.addrWidth(4), .dataWidth(2)) rom_17 (.addr(4'b1111), .data(rom_17_data), .sel(1'b1));
  MUX_4_a_1 mux_4_a_1_17 (
    ._1(in_29), ._5(out_37), ._6(rom_17_data[1]), ._7(rom_17_data[0]), ._2(in_15), ._3(in_16), ._4(_3));
  MUX_4_a_1 mux_4_a_1_18 (
    ._1(_3), ._5(out_61), ._6(rom_18_data[1]), ._7(rom_18_data[0]), ._2(in_16), ._3(in_15), ._4(in_29));
  ROM #(.addrWidth(4), .dataWidth(2)) rom_18 (.addr(4'b1111), .data(rom_18_data), .sel(1'b1));
  ROM #(.addrWidth(4), .dataWidth(2)) rom_19 (.addr(4'b1111), .data(rom_19_data), .sel(1'b1));
  MUX_4_a_1 mux_4_a_1_19 (
    ._1(in_30), ._5(out_38), ._6(rom_19_data[1]), ._7(rom_19_data[0]), ._2(in_13), ._3(in_14), ._4(_2));
  MUX_4_a_1 mux_4_a_1_20 (
    ._1(_2), ._5(out_62), ._6(rom_20_data[1]), ._7(rom_20_data[0]), ._2(in_14), ._3(in_13), ._4(in_30));
  ROM #(.addrWidth(4), .dataWidth(2)) rom_20 (.addr(4'b1111), .data(rom_20_data), .sel(1'b1));
  ROM #(.addrWidth(4), .dataWidth(2)) rom_21 (.addr(4'b1111), .data(rom_21_data), .sel(1'b1));
  MUX_4_a_1 mux_4_a_1_21 (
    ._1(in_31), ._5(out_39), ._6(rom_21_data[1]), ._7(rom_21_data[0]), ._2(in_11), ._3(in_12), ._4(_1));
  MUX_4_a_1 mux_4_a_1_22 (
    ._1(_1), ._5(out_63), ._6(rom_22_data[1]), ._7(rom_22_data[0]), ._2(in_12), ._3(in_11), ._4(in_31));
  ROM #(.addrWidth(4), .dataWidth(2)) rom_22 (.addr(4'b1111), .data(rom_22_data), .sel(1'b1));
  ROM #(.addrWidth(4), .dataWidth(2)) rom_23 (.addr(4'b1111), .data(rom_23_data), .sel(1'b1));
  MUX_4_a_1 mux_4_a_1_23 (
    ._1(in_32), ._5(out_40), ._6(rom_23_data[1]), ._7(rom_23_data[0]), ._2(in_9), ._3(in_10), ._4(_0));
  MUX_4_a_1 mux_4_a_1_24 (
    ._1(_0), ._5(out_64), ._6(rom_24_data[1]), ._7(rom_24_data[0]), ._2(in_10), ._3(in_9), ._4(in_32));
  ROM #(.addrWidth(4), .dataWidth(2)) rom_24 (.addr(4'b1111), .data(rom_24_data), .sel(1'b1));
  ROM #(.addrWidth(4), .dataWidth(2)) rom_25 (.addr(4'b1111), .data(rom_25_data), .sel(1'b1));
  ROM #(.addrWidth(4), .dataWidth(2)) rom_26 (.addr(4'b1111), .data(rom_26_data), .sel(1'b1));
  ROM #(.addrWidth(4), .dataWidth(2)) rom_27 (.addr(4'b1111), .data(rom_27_data), .sel(1'b1));
  ROM #(.addrWidth(4), .dataWidth(2)) rom_28 (.addr(4'b1111), .data(rom_28_data), .sel(1'b1));
  ROM #(.addrWidth(4), .dataWidth(2)) rom_29 (.addr(4'b1111), .data(rom_29_data), .sel(1'b1));
  ROM #(.addrWidth(4), .dataWidth(2)) rom_30 (.addr(4'b1111), .data(rom_30_data), .sel(1'b1));
  ROM #(.addrWidth(4), .dataWidth(2)) rom_31 (.addr(4'b1111), .data(rom_31_data), .sel(1'b1));
  ROM #(.addrWidth(4), .dataWidth(2)) rom_32 (.addr(4'b1111), .data(rom_32_data), .sel(1'b1));
  MUX_4_a_1 mux_4_a_1_25 (
    ._1(in_9), ._5(out_41), ._6(rom_25_data[1]), ._7(rom_25_data[0]), ._2(_0), ._3(in_32), ._4(in_10));
  MUX_4_a_1 mux_4_a_1_26 (
    ._1(in_11), ._5(out_43), ._6(rom_26_data[1]), ._7(rom_26_data[0]), ._2(_1), ._3(in_31), ._4(in_12));
  MUX_4_a_1 mux_4_a_1_27 (
    ._1(in_13), ._5(out_45), ._6(rom_27_data[1]), ._7(rom_27_data[0]), ._2(_2), ._3(in_30), ._4(in_14));
  MUX_4_a_1 mux_4_a_1_28 (
    ._1(in_15), ._5(out_47), ._6(rom_28_data[1]), ._7(rom_28_data[0]), ._2(_3), ._3(in_29), ._4(in_16));
  MUX_4_a_1 mux_4_a_1_29 (
    ._1(in_17), ._5(out_49), ._6(rom_29_data[1]), ._7(rom_29_data[0]), ._2(_4), ._3(in_28), ._4(in_18));
  MUX_4_a_1 mux_4_a_1_30 (
    ._1(in_19), ._5(out_51), ._6(rom_30_data[1]), ._7(rom_30_data[0]), ._2(_5), ._3(in_27), ._4(in_20));
  MUX_4_a_1 mux_4_a_1_31 (
    ._1(in_21), ._5(out_53), ._6(rom_31_data[1]), ._7(rom_31_data[0]), ._2(_6), ._3(in_26), ._4(in_22));
  MUX_4_a_1 mux_4_a_1_32 (
    ._1(in_23), ._5(out_55), ._6(rom_32_data[1]), ._7(rom_32_data[0]), ._2(_7), ._3(in_25), ._4(in_24));

  // Notes on the sheet:
  //   Programming
  //   0
  //   1
  //   2
  //   3
  //   4
  //   5
  //   6
  //   7
  //   DISJOINT SWITCH BOX
  //   Only same Number Channels
  //   Can be connected
  //   --------------------------------------------------
  //   --------------------------------------------------
  //   00 - Front Channel
  //   01 - Right Channel
  //   02 - Left Channel
  //   04 - U-Turn Channel
  //   contents of rom_9 (hex, n*v repeats v):
  //   15*0 2
  //   7
  //   contents of rom_10 (hex, n*v repeats v):
  //   15*0 1
  //   contents of rom_11 (hex, n*v repeats v):
  //   15*0 2
  //   contents of rom_12 (hex, n*v repeats v):
  //   15*0 1
  //   6
  //   contents of rom_13 (hex, n*v repeats v):
  //   15*0 2
  //   5
  //   contents of rom_14 (hex, n*v repeats v):
  //   15*0 1
  //   contents of rom_15 (hex, n*v repeats v):
  //   15*0 2
  //   4
  //   contents of rom_16 (hex, n*v repeats v):
  //   15*0 1
  //   contents of rom_17 (hex, n*v repeats v):
  //   15*0 2
  //   3
  //   contents of rom_18 (hex, n*v repeats v):
  //   15*0 1
  //   contents of rom_19 (hex, n*v repeats v):
  //   15*0 2
  //   contents of rom_20 (hex, n*v repeats v):
  //   15*0 1
  //   2
  //   contents of rom_21 (hex, n*v repeats v):
  //   15*0 2
  //   1
  //   contents of rom_22 (hex, n*v repeats v):
  //   15*0 1
  //   contents of rom_23 (hex, n*v repeats v):
  //   15*0 2
  //   0
  //   contents of rom_24 (hex, n*v repeats v):
  //   15*0 1
  //   contents of rom_25 (hex, n*v repeats v):
  //   15*0 3
  //   contents of rom_26 (hex, n*v repeats v):
  //   15*0 3
  //   contents of rom_27 (hex, n*v repeats v):
  //   15*0 3
  //   contents of rom_28 (hex, n*v repeats v):
  //   15*0 3
  //   contents of rom_29 (hex, n*v repeats v):
  //   15*0 3
  //   contents of rom_30 (hex, n*v repeats v):
  //   15*0 3
  //   contents of rom_31 (hex, n*v repeats v):
  //   15*0 3
  //   contents of rom_32 (hex, n*v repeats v):
  //   15*0 3
  //   0
  //   1
  //   2
  //   3
  //   4
  //   5
  //   6
  //   7
endmodule

module Input_Output_Block (
  input  in_1,
  input  in_2,
  input  in_3,
  input  in_4,
  input  in_5,
  input  in_6,
  input  in_7,
  input  in_8,
  input  in_9,
  input  in_10,
  input  in_11,
  input  in_12,
  input  in_13,
  input  in_14,
  input  in_15,
  input  in_16,
  input  in_17,
  input  in_18,
  input  in_19,
  input  in_20,
  input  in_21,
  input  in_22,
  input  in_23,
  input  in_24,
  output _17,
  output _18,
  output _19,
  output _20
);

  wire i_o_cell_1__2, i_o_cell_2__2, i_o_cell_3__2, i_o_cell_4__2, i_o_cell_5__2, i_o_cell_6__2,
       i_o_cell_7__2, i_o_cell_8__2, programmable_local_interconnect_matrix_16_to_8_1__21,
       programmable_local_interconnect_matrix_16_to_8_1__22,
       programmable_local_interconnect_matrix_16_to_8_1__23,
       programmable_local_interconnect_matrix_16_to_8_1__24,
       programmable_local_interconnect_matrix_16_to_8_1__25,
       programmable_local_interconnect_matrix_16_to_8_1__26,
       programmable_local_interconnect_matrix_16_to_8_1__27,
       programmable_local_interconnect_matrix_16_to_8_1__28;
  wire [7:0] rom_1_data;

  Programmable_local_interconnect_matrix_16_to_8 programmable_local_interconnect_matrix_16_to_8_1 (
    ._1(in_16), ._2(in_15), ._3(in_14), ._4(in_13), ._5(in_12), ._7(in_10), ._8(in_9), ._9(in_8), ._10(in_7),
    ._11(in_6), ._12(in_5), ._13(in_4), ._14(in_3), ._15(in_2), ._16(in_1), ._6(in_11),
    ._21(programmable_local_interconnect_matrix_16_to_8_1__21),
    ._22(programmable_local_interconnect_matrix_16_to_8_1__22),
    ._23(programmable_local_interconnect_matrix_16_to_8_1__23),
    ._24(programmable_local_interconnect_matrix_16_to_8_1__24),
    ._25(programmable_local_interconnect_matrix_16_to_8_1__25),
    ._26(programmable_local_interconnect_matrix_16_to_8_1__26),
    ._27(programmable_local_interconnect_matrix_16_to_8_1__27),
    ._28(programmable_local_interconnect_matrix_16_to_8_1__28));  // open: _17, _18, _19, _20
  Programmable_Local_Interconnect_Matrix_8_to_4 programmable_local_interconnect_matrix_8_to_4_1 (
    ._8(i_o_cell_8__2), ._7(i_o_cell_7__2), ._6(i_o_cell_6__2), ._5(i_o_cell_5__2), ._4(i_o_cell_4__2),
    ._3(i_o_cell_3__2), ._2(i_o_cell_2__2), ._1(i_o_cell_1__2), ._13(_17), ._14(_18), ._15(_19), ._16(_20));  // open: _12, _10, _9, _11
  ROM #(.addrWidth(4)) rom_1 (.addr(4'b1111), .data(rom_1_data), .sel(1'b1));
  I_O_CELL i_o_cell_1 (
    ._2(i_o_cell_1__2), ._4(programmable_local_interconnect_matrix_16_to_8_1__21), ._1(rom_1_data[0]),
    ._3(in_17));
  I_O_CELL i_o_cell_2 (
    ._2(i_o_cell_2__2), ._4(programmable_local_interconnect_matrix_16_to_8_1__22), ._1(rom_1_data[1]),
    ._3(in_18));
  I_O_CELL i_o_cell_3 (
    ._2(i_o_cell_3__2), ._4(programmable_local_interconnect_matrix_16_to_8_1__23), ._1(rom_1_data[2]),
    ._3(in_19));
  I_O_CELL i_o_cell_4 (
    ._2(i_o_cell_4__2), ._4(programmable_local_interconnect_matrix_16_to_8_1__24), ._1(rom_1_data[3]),
    ._3(in_20));
  I_O_CELL i_o_cell_5 (
    ._2(i_o_cell_5__2), ._4(programmable_local_interconnect_matrix_16_to_8_1__25), ._1(rom_1_data[4]),
    ._3(in_21));
  I_O_CELL i_o_cell_6 (
    ._2(i_o_cell_6__2), ._4(programmable_local_interconnect_matrix_16_to_8_1__26), ._1(rom_1_data[5]),
    ._3(in_22));
  I_O_CELL i_o_cell_7 (
    ._2(i_o_cell_7__2), ._4(programmable_local_interconnect_matrix_16_to_8_1__27), ._1(rom_1_data[6]),
    ._3(in_23));
  I_O_CELL i_o_cell_8 (
    ._2(i_o_cell_8__2), ._4(programmable_local_interconnect_matrix_16_to_8_1__28), ._1(rom_1_data[7]),
    ._3(in_24));
endmodule

module I_O_CELL (
  input  _1,
  input  _3,
  input  _4,
  output _2
);

  wire not_1_out;

  not not_1 (not_1_out, _1);
  assign _2 = not_1_out ? _3 : 1'bz;  // Controlled_Buffer controlled_buffer_1
  assign _3 = _1 ? _4 : 1'bz;  // Controlled_Buffer controlled_buffer_2

  // Notes on the sheet:
  //   INTERNOS
  //   CONTROL - IN / OUT
  //   OUTPUT
  //   INPUT
  //   PIN
endmodule

module Programmable_local_interconnect_matrix_16_to_8 (
  input  _16,
  input  _15,
  input  _14,
  input  _13,
  input  _12,
  input  _11,
  input  _10,
  input  _9,
  input  _8,
  input  _7,
  input  _6,
  input  _5,
  input  _4,
  input  _3,
  input  _2,
  input  _1,
  input  _20,
  input  _19,
  input  _18,
  input  _17,
  output _21,
  output _22,
  output _23,
  output _24,
  output _25,
  output _26,
  output _27,
  output _28
);

  wire [4:0] rom_1_data, rom_2_data, rom_3_data, rom_4_data, rom_5_data, rom_6_data, rom_7_data, rom_8_data;

  ROM #(.addrWidth(2), .dataWidth(5)) rom_1 (.addr(2'b11), .data(rom_1_data), .sel(1'b1));
  ROM #(.addrWidth(2), .dataWidth(5)) rom_2 (.addr(2'b11), .data(rom_2_data), .sel(1'b1));
  ROM #(.addrWidth(2), .dataWidth(5)) rom_3 (.addr(2'b11), .data(rom_3_data), .sel(1'b1));
  ROM #(.addrWidth(2), .dataWidth(5)) rom_4 (.addr(2'b11), .data(rom_4_data), .sel(1'b1));
  _20_to_1_MUX u_20_to_1_mux_1 (
    ._8(_8), ._7(_7), ._6(_6), ._5(_5), ._4(_4), ._3(_3), ._2(_2), ._1(_1), ._9(_9), ._10(_10), ._11(_11),
    ._12(_12), ._13(_13), ._14(_14), ._15(_15), ._16(_16), ._17(_17), ._18(_18), ._19(_19), ._20(_20),
    ._21(rom_1_data[4]), ._22(rom_1_data[3]), ._23(rom_1_data[2]), ._24(rom_1_data[1]), ._25(rom_1_data[0]),
    ._26(_21));
  _20_to_1_MUX u_20_to_1_mux_2 (
    ._8(_8), ._7(_7), ._6(_6), ._5(_5), ._4(_4), ._3(_3), ._2(_2), ._1(_1), ._9(_9), ._10(_10), ._11(_11),
    ._12(_12), ._13(_13), ._14(_14), ._15(_15), ._16(_16), ._17(_17), ._18(_18), ._19(_19), ._20(_20),
    ._21(rom_2_data[4]), ._22(rom_2_data[3]), ._23(rom_2_data[2]), ._24(rom_2_data[1]), ._25(rom_2_data[0]),
    ._26(_23));
  _20_to_1_MUX u_20_to_1_mux_3 (
    ._8(_8), ._7(_7), ._6(_6), ._5(_5), ._4(_4), ._3(_3), ._2(_2), ._1(_1), ._9(_9), ._10(_10), ._11(_11),
    ._12(_12), ._13(_13), ._14(_14), ._15(_15), ._16(_16), ._17(_17), ._18(_18), ._19(_19), ._20(_20),
    ._21(rom_3_data[4]), ._22(rom_3_data[3]), ._23(rom_3_data[2]), ._24(rom_3_data[1]), ._25(rom_3_data[0]),
    ._26(_25));
  _20_to_1_MUX u_20_to_1_mux_4 (
    ._8(_8), ._7(_7), ._6(_6), ._5(_5), ._4(_4), ._3(_3), ._2(_2), ._1(_1), ._9(_9), ._10(_10), ._11(_11),
    ._12(_12), ._13(_13), ._14(_14), ._15(_15), ._16(_16), ._17(_17), ._18(_18), ._19(_19), ._20(_20),
    ._21(rom_4_data[4]), ._22(rom_4_data[3]), ._23(rom_4_data[2]), ._24(rom_4_data[1]), ._25(rom_4_data[0]),
    ._26(_27));
  ROM #(.addrWidth(2), .dataWidth(5)) rom_5 (.addr(2'b11), .data(rom_5_data), .sel(1'b1));
  ROM #(.addrWidth(2), .dataWidth(5)) rom_6 (.addr(2'b11), .data(rom_6_data), .sel(1'b1));
  ROM #(.addrWidth(2), .dataWidth(5)) rom_7 (.addr(2'b11), .data(rom_7_data), .sel(1'b1));
  ROM #(.addrWidth(2), .dataWidth(5)) rom_8 (.addr(2'b11), .data(rom_8_data), .sel(1'b1));
  _20_to_1_MUX u_20_to_1_mux_5 (
    ._8(_8), ._7(_7), ._6(_6), ._5(_5), ._4(_4), ._3(_3), ._2(_2), ._1(_1), ._9(_9), ._10(_10), ._11(_11),
    ._12(_12), ._13(_13), ._14(_14), ._15(_15), ._16(_16), ._17(_17), ._18(_18), ._19(_19), ._20(_20),
    ._21(rom_5_data[4]), ._22(rom_5_data[3]), ._23(rom_5_data[2]), ._24(rom_5_data[1]), ._25(rom_5_data[0]),
    ._26(_22));
  _20_to_1_MUX u_20_to_1_mux_6 (
    ._8(_8), ._7(_7), ._6(_6), ._5(_5), ._4(_4), ._3(_3), ._2(_2), ._1(_1), ._9(_9), ._10(_10), ._11(_11),
    ._12(_12), ._13(_13), ._14(_14), ._15(_15), ._16(_16), ._17(_17), ._18(_18), ._19(_19), ._20(_20),
    ._21(rom_6_data[4]), ._22(rom_6_data[3]), ._23(rom_6_data[2]), ._24(rom_6_data[1]), ._25(rom_6_data[0]),
    ._26(_24));
  _20_to_1_MUX u_20_to_1_mux_7 (
    ._8(_8), ._7(_7), ._6(_6), ._5(_5), ._4(_4), ._3(_3), ._2(_2), ._1(_1), ._9(_9), ._10(_10), ._11(_11),
    ._12(_12), ._13(_13), ._14(_14), ._15(_15), ._16(_16), ._17(_17), ._18(_18), ._19(_19), ._20(_20),
    ._21(rom_7_data[4]), ._22(rom_7_data[3]), ._23(rom_7_data[2]), ._24(rom_7_data[1]), ._25(rom_7_data[0]),
    ._26(_26));
  _20_to_1_MUX u_20_to_1_mux_8 (
    ._8(_8), ._7(_7), ._6(_6), ._5(_5), ._4(_4), ._3(_3), ._2(_2), ._1(_1), ._9(_9), ._10(_10), ._11(_11),
    ._12(_12), ._13(_13), ._14(_14), ._15(_15), ._16(_16), ._17(_17), ._18(_18), ._19(_19), ._20(_20),
    ._21(rom_8_data[4]), ._22(rom_8_data[3]), ._23(rom_8_data[2]), ._24(rom_8_data[1]), ._25(rom_8_data[0]),
    ._26(_28));

  // Notes on the sheet:
  //   LOCAL INPUTS 
  //   LOCAL FEEDBACK
endmodule
// Programmable Local Interconnect Matrix 16 to 8
module Programmable_Local_Interconnect_Matrix_8_to_4 (
  input  _8,
  input  _7,
  input  _6,
  input  _5,
  input  _4,
  input  _3,
  input  _2,
  input  _1,
  input  _12,
  input  _11,
  input  _10,
  input  _9,
  output _13,
  output _14,
  output _15,
  output _16
);

  wire [4:0] rom_1_data, rom_2_data, rom_3_data, rom_4_data;

  ROM #(.addrWidth(2), .dataWidth(5)) rom_1 (.addr(2'b11), .data(rom_1_data), .sel(1'b1));
  ROM #(.addrWidth(2), .dataWidth(5)) rom_2 (.addr(2'b11), .data(rom_2_data), .sel(1'b1));
  _20_to_1_MUX u_20_to_1_mux_1 (
    ._8(_8), ._7(_7), ._6(_6), ._5(_5), ._4(_4), ._3(_3), ._2(_2), ._1(_1), ._17(_9), ._18(_10), ._19(_11),
    ._20(_12), ._21(rom_1_data[4]), ._22(rom_1_data[3]), ._23(rom_1_data[2]), ._24(rom_1_data[1]),
    ._25(rom_1_data[0]), ._26(_13));  // open: _9, _10, _11, _12, _13, _14, _15, _16
  _20_to_1_MUX u_20_to_1_mux_2 (
    ._8(_8), ._7(_7), ._6(_6), ._5(_5), ._4(_4), ._3(_3), ._2(_2), ._1(_1), ._17(_9), ._18(_10), ._19(_11),
    ._20(_12), ._21(rom_2_data[4]), ._22(rom_2_data[3]), ._23(rom_2_data[2]), ._24(rom_2_data[1]),
    ._25(rom_2_data[0]), ._26(_15));  // open: _9, _10, _11, _12, _13, _14, _15, _16
  ROM #(.addrWidth(2), .dataWidth(5)) rom_3 (.addr(2'b11), .data(rom_3_data), .sel(1'b1));
  ROM #(.addrWidth(2), .dataWidth(5)) rom_4 (.addr(2'b11), .data(rom_4_data), .sel(1'b1));
  _20_to_1_MUX u_20_to_1_mux_3 (
    ._8(_8), ._7(_7), ._6(_6), ._5(_5), ._4(_4), ._3(_3), ._2(_2), ._1(_1), ._17(_9), ._18(_10), ._19(_11),
    ._20(_12), ._21(rom_3_data[4]), ._22(rom_3_data[3]), ._23(rom_3_data[2]), ._24(rom_3_data[1]),
    ._25(rom_3_data[0]), ._26(_14));  // open: _9, _10, _11, _12, _13, _14, _15, _16
  _20_to_1_MUX u_20_to_1_mux_4 (
    ._8(_8), ._7(_7), ._6(_6), ._5(_5), ._4(_4), ._3(_3), ._2(_2), ._1(_1), ._17(_9), ._18(_10), ._19(_11),
    ._20(_12), ._21(rom_4_data[4]), ._22(rom_4_data[3]), ._23(rom_4_data[2]), ._24(rom_4_data[1]),
    ._25(rom_4_data[0]), ._26(_16));  // open: _9, _10, _11, _12, _13, _14, _15, _16

  // Notes on the sheet:
  //   LOCAL INPUTS 
  //   LOCAL FEEDBACK
endmodule

module Prueba (
  input  in_1,
  input  in_2,
  input  in_3,
  input  in_4,
  input  in_5,
  input  in_6,
  input  in_7,
  input  in_8,
  input  in_9,
  input  in_10,
  input  in_11,
  input  in_12,
  input  in_13,
  input  in_14,
  input  in_15,
  input  in_16,
  input  in_17,
  input  in_18,
  input  in_19,
  input  in_20,
  input  in_21,
  input  in_22,
  input  in_23,
  input  in_24,
  input  in_25,
  input  in_26,
  input  in_27,
  input  in_28,
  input  in_29,
  input  in_30,
  input  in_31,
  input  in_32,
  input  in_33,
  input  in_34,
  input  in_35,
  input  in_36,
  input  in_37,
  input  in_38,
  input  in_39,
  input  in_40,
  input  in_41,
  input  in_42,
  input  in_43,
  input  in_44,
  input  in_45,
  input  in_46,
  input  in_47,
  input  in_48,
  input  in_49,
  input  in_50,
  input  in_51,
  input  in_52,
  input  in_53,
  input  in_54,
  input  in_55,
  input  in_56,
  input  in_57,
  input  in_58,
  input  in_59,
  input  in_60,
  input  in_61,
  input  in_62,
  input  in_63,
  input  in_64,
  input  in_65,
  input  in_66,
  input  in_67,
  input  in_68,
  input  in_69,
  input  LE_00,
  input  in_71,
  input  in_72,
  input  in_73,
  input  in_74,
  input  in_75,
  input  _2_BITS,
  input  in_77,
  input  in_78,
  input  in_79,
  input  in_80,
  input  in_81,
  input  in_82,
  input  in_83,
  input  in_84,
  input  in_85,
  input  in_86,
  input  in_87,
  input  in_88,
  input  in_89,
  input  in_90,
  input  in_91,
  input  in_92,
  input  in_93,
  input  in_94,
  input  in_95,
  input  in_96,
  input  in_97,
  input  in_98,
  input  in_99,
  output [4:0] out_100
);

  wire clock_1_out, clock_2_out, clock_3_out, clock_4_out, clock_5_out, clock_6_out, clock_7_out,
       clock_8_out, clock_9_out, logic_element_1_1_out_8, logic_element_1_2_out_8, logic_element_1_3_out_8,
       logic_element_2_1_out_8, logic_element_2_2_out_8, logic_element_2_3_out_8, logic_element_3_1_out_8,
       logic_element_3_2_out_8, logic_element_4_1_out_8, mux_4_a_1_1__5, mux_8_a_1_1__5, n01s_1_out_4,
       n20_to_1_mux_1__26, n20_to_1_mux_2__26, or_1_out;

  _01S u_01s_1 (._2(in_11), ._3(in_15), ._4(in_22), .out_4(n01s_1_out_4));
  LED led_1 (.in(n01s_1_out_4));
  MUX_4_a_1 mux_4_a_1_1 (._1(in_37), ._5(mux_4_a_1_1__5), ._6(in_61), ._7(in_62), ._2(in_48), ._3(in_51), ._4(in_54));
  Clock clock_1 (.out(clock_1_out));
  Clock clock_2 (.out(clock_2_out));
  I_O_CELL i_o_cell_1 ();  // open: _2, _4, _1, _3
  LED led_2 (.in(mux_4_a_1_1__5));
  Logic_element_1 logic_element_1_1 (
    .out_8(logic_element_1_1_out_8), .Clear(clock_1_out), .in_6(in_75), .Preset(_2_BITS), .A3(in_71),
    .A2(in_74), .A1(logic_element_2_1_out_8), .A0(logic_element_1_1_out_8));
  Logic_element_2 logic_element_2_1 (
    ._1(in_81), ._2(in_83), ._3(logic_element_2_1_out_8), ._4(logic_element_1_1_out_8),
    .out_8(logic_element_2_1_out_8), ._5(clock_2_out), ._6(in_84), ._7(in_85));
  MUX_8_a_1 mux_8_a_1_1 (
    ._1(in_8), ._2(in_12), ._3(in_16), ._4(in_19), ._5(mux_8_a_1_1__5), ._6(in_23), ._7(in_26), ._8(in_29),
    ._9(in_32), ._10(in_45), ._11(in_46), ._12(in_47));
  or or_1 (or_1_out, in_57, in_60, in_65, in_68);
  LED led_3 (.in(logic_element_1_1_out_8));
  LED led_4 (.in(logic_element_2_1_out_8));
  LED led_5 (.in(mux_8_a_1_1__5));
  LED led_6 (.in(or_1_out));
  Clock clock_3 (.out(clock_3_out));
  Clock clock_4 (.out(clock_4_out));
  Clock clock_5 (.out(clock_5_out));
  Logic_element_1 logic_element_1_2 (
    .out_8(logic_element_1_2_out_8), .Clear(clock_3_out), .in_6(in_77), .Preset(in_78), .A3(in_72),
    .A2(logic_element_3_1_out_8), .A1(logic_element_2_2_out_8), .A0(logic_element_1_2_out_8));
  Logic_element_2 logic_element_2_2 (
    ._1(in_82), ._2(logic_element_3_1_out_8), ._3(logic_element_2_2_out_8), ._4(logic_element_1_2_out_8),
    .out_8(logic_element_2_2_out_8), ._5(clock_4_out), ._6(in_86), ._7(in_87));
  Logic_element_3 logic_element_3_1 (
    ._1(in_90), ._2(logic_element_3_1_out_8), ._3(logic_element_2_2_out_8), ._4(logic_element_1_2_out_8),
    .out_8(logic_element_3_1_out_8), ._5(clock_5_out), ._6(in_91), ._7(in_92));
  LED led_7 (.in(logic_element_1_2_out_8));
  LED led_8 (.in(logic_element_2_2_out_8));
  LED led_9 (.in(logic_element_3_1_out_8));
  _20_to_1_MUX u_20_to_1_mux_1 (
    ._8(in_24), ._7(in_20), ._6(in_17), ._5(in_13), ._4(in_9), ._3(in_6), ._2(in_4), ._1(in_2), ._9(in_27),
    ._10(in_30), ._11(in_33), ._12(in_35), ._13(in_38), ._14(in_49), ._15(in_52), ._16(in_55), ._17(in_58),
    ._18(in_63), ._19(in_66), ._20(in_69), ._21(in_39), ._22(in_40), ._23(in_41), ._24(in_42), ._25(in_43),
    ._26(n20_to_1_mux_1__26));
  LED led_10 (.in(n20_to_1_mux_1__26));
  Clock clock_6 (.out(clock_6_out));
  Clock clock_7 (.out(clock_7_out));
  Clock clock_8 (.out(clock_8_out));
  Clock clock_9 (.out(clock_9_out));
  Logic_element_1 logic_element_1_3 (
    .out_8(logic_element_1_3_out_8), .Clear(clock_6_out), .in_6(in_79), .Preset(in_80),
    .A3(logic_element_4_1_out_8), .A2(logic_element_3_2_out_8), .A1(logic_element_2_3_out_8),
    .A0(logic_element_1_3_out_8));
  Logic_element_2 logic_element_2_3 (
    ._1(logic_element_4_1_out_8), ._2(logic_element_3_2_out_8), ._3(logic_element_2_3_out_8),
    ._4(logic_element_1_3_out_8), .out_8(logic_element_2_3_out_8), ._5(clock_7_out), ._6(in_88), ._7(in_89));
  Logic_element_3 logic_element_3_2 (
    ._1(logic_element_4_1_out_8), ._2(logic_element_3_2_out_8), ._3(logic_element_2_3_out_8),
    ._4(logic_element_1_3_out_8), .out_8(logic_element_3_2_out_8), ._5(clock_8_out), ._6(in_93), ._7(in_94));
  Logic_element_4 logic_element_4_1 (
    ._2(logic_element_3_2_out_8), ._3(logic_element_2_3_out_8), ._4(logic_element_1_3_out_8),
    .out_8(logic_element_4_1_out_8), ._5(clock_9_out), ._6(in_98), ._7(in_99), ._1(logic_element_4_1_out_8));
  LED led_11 (.in(logic_element_1_3_out_8));
  LED led_12 (.in(logic_element_2_3_out_8));
  LED led_13 (.in(logic_element_3_2_out_8));
  LED led_14 (.in(logic_element_4_1_out_8));
  ROM #(.addrWidth(2), .dataWidth(5)) rom_1 (.addr({in_73, LE_00}), .data(out_100), .sel(1'b1));
  _20_to_1_MUX u_20_to_1_mux_2 (
    ._8(in_21), ._7(in_18), ._6(in_14), ._5(in_10), ._4(in_7), ._3(in_5), ._2(in_3), ._1(in_1), ._9(in_25),
    ._10(in_28), ._11(in_31), ._12(in_34), ._13(in_36), ._14(in_44), ._15(in_50), ._16(in_53), ._17(in_56),
    ._18(in_59), ._19(in_64), ._20(in_67), ._21(out_100[4]), ._22(out_100[3]), ._23(out_100[2]),
    ._24(out_100[1]), ._25(out_100[0]), ._26(n20_to_1_mux_2__26));
  LED led_15 (.in(n20_to_1_mux_2__26));

  // Notes on the sheet:
  //   in_39: pull=down
  //   1001
  //   1100
  //   Empieza en 11
  //   3 BITS
  //   01010110
  //   01101010
  //   11110000
  //   Empieza en 100
  //   4 BITS
  //   1001100101100110
  //   1100101010101010
  //   0100110111110000
  //   1111011100100000
  //   Empieza en 1011
  //   contents of rom_1 (hex, n*v repeats v):
  //   13
endmodule

module Prueba_Local_Matrix (
  input  in_1,
  input  in_2,
  input  in_3,
  input  in_4,
  input  in_5,
  input  _15,
  input  in_7,
  input  in_8,
  input  _14,
  input  in_10,
  input  in_11,
  input  _13,
  input  _12,
  input  in_14,
  input  _11,
  input  _10,
  input  _9,
  input  in_18,
  input  in_19,
  input  _8,
  input  in_21,
  input  in_22,
  input  _7,
  input  _6,
  input  in_25,
  input  _5,
  input  _4,
  input  _3,
  input  _2,
  input  in_30,
  input  in_31,
  input  _1,
  input  in_33,
  input  in_34,
  input  _0,
  input  _15_2,
  input  _14_2,
  input  in_38,
  input  in_39,
  input  _13_2,
  input  _12_2,
  input  _11_2,
  input  _10_2,
  input  _9_2,
  input  _8_2,
  input  in_46,
  input  in_47,
  input  _7_2,
  input  _6_2,
  input  _5_2,
  input  _4_2,
  input  _3_2,
  input  _2_2,
  input  _1_2,
  input  in_55,
  input  in_56,
  input  _0_2,
  input  in_58,
  input  in_59
);

  wire clock_1_out, clock_2_out, clock_3_out, clock_4_out, clock_5_out, clock_6_out, clock_7_out,
       clock_8_out, clock_9_out, clock_10_out, logic_element_1_1_out_8, logic_element_1_2_out_8,
       logic_element_1_3_out_8, logic_element_2_1_out_8, logic_element_2_2_out_8, logic_element_2_3_out_8,
       logic_element_3_1_out_8, logic_element_3_2_out_8, logic_element_3_3_out_8, logic_element_4_1_out_8,
       programmable_local_interconnect_matrix_1__21, programmable_local_interconnect_matrix_1__22,
       programmable_local_interconnect_matrix_1__23, programmable_local_interconnect_matrix_1__24,
       programmable_local_interconnect_matrix_1__25, programmable_local_interconnect_matrix_1__26,
       programmable_local_interconnect_matrix_1__27, programmable_local_interconnect_matrix_1__28,
       programmable_local_interconnect_matrix_1__29, programmable_local_interconnect_matrix_1__30,
       programmable_local_interconnect_matrix_1__31, programmable_local_interconnect_matrix_1__32,
       programmable_local_interconnect_matrix_1__33, programmable_local_interconnect_matrix_1__34,
       programmable_local_interconnect_matrix_1__35, programmable_local_interconnect_matrix_1__36,
       programmable_local_interconnect_matrix_2__21, programmable_local_interconnect_matrix_2__22,
       programmable_local_interconnect_matrix_2__29;

  Programmable_local_interconnect_matrix programmable_local_interconnect_matrix_1 (
    ._16(_15_2), ._15(_14_2), ._14(_13_2), ._13(_12_2), ._12(_11_2), ._11(_10_2), ._10(_9_2), ._9(_8_2),
    ._8(_7_2), ._7(_6_2), ._6(_5_2), ._5(_4_2), ._4(_3_2), ._3(_2_2), ._2(_1_2), ._1(_0_2),
    ._20(logic_element_1_2_out_8), ._19(logic_element_2_2_out_8), ._18(logic_element_3_2_out_8),
    ._17(logic_element_4_1_out_8), ._21(programmable_local_interconnect_matrix_1__21),
    ._23(programmable_local_interconnect_matrix_1__23), ._27(programmable_local_interconnect_matrix_1__27),
    ._29(programmable_local_interconnect_matrix_1__29), ._31(programmable_local_interconnect_matrix_1__31),
    ._33(programmable_local_interconnect_matrix_1__33), ._35(programmable_local_interconnect_matrix_1__35),
    ._22(programmable_local_interconnect_matrix_1__22), ._24(programmable_local_interconnect_matrix_1__24),
    ._26(programmable_local_interconnect_matrix_1__26), ._28(programmable_local_interconnect_matrix_1__28),
    ._30(programmable_local_interconnect_matrix_1__30), ._32(programmable_local_interconnect_matrix_1__32),
    ._34(programmable_local_interconnect_matrix_1__34), ._36(programmable_local_interconnect_matrix_1__36),
    ._25(programmable_local_interconnect_matrix_1__25));
  Clock clock_1 (.out(clock_1_out));
  Clock clock_2 (.out(clock_2_out));
  Clock clock_3 (.out(clock_3_out));
  Logic_element_1 logic_element_1_1 (
    .out_8(logic_element_1_1_out_8), .Clear(clock_1_out), .in_6(in_7), .Preset(in_8), .A3(in_5),
    .A2(logic_element_3_1_out_8), .A1(logic_element_2_1_out_8), .A0(logic_element_1_1_out_8));
  Logic_element_2 logic_element_2_1 (
    ._1(in_14), ._2(logic_element_3_1_out_8), ._3(logic_element_2_1_out_8), ._4(logic_element_1_1_out_8),
    .out_8(logic_element_2_1_out_8), ._5(clock_2_out), ._6(in_18), ._7(in_19));
  Logic_element_3 logic_element_3_1 (
    ._1(in_25), ._2(logic_element_3_1_out_8), ._3(logic_element_2_1_out_8), ._4(logic_element_1_1_out_8),
    .out_8(logic_element_3_1_out_8), ._5(clock_3_out), ._6(in_30), ._7(in_31));
  LED led_1 (.in(logic_element_1_1_out_8));
  LED led_2 (.in(logic_element_2_1_out_8));
  LED led_3 (.in(logic_element_3_1_out_8));
  Clock clock_4 (.out(clock_4_out));
  Clock clock_5 (.out(clock_5_out));
  Clock clock_6 (.out(clock_6_out));
  Clock clock_7 (.out(clock_7_out));
  Logic_element_1 logic_element_1_2 (
    .out_8(logic_element_1_2_out_8), .Clear(clock_4_out), .in_6(in_38), .Preset(in_39),
    .A3(programmable_local_interconnect_matrix_1__21), .A2(programmable_local_interconnect_matrix_1__23),
    .A1(programmable_local_interconnect_matrix_1__25), .A0(programmable_local_interconnect_matrix_1__27));
  Logic_element_2 logic_element_2_2 (
    ._1(programmable_local_interconnect_matrix_1__29), ._2(programmable_local_interconnect_matrix_1__31),
    ._3(programmable_local_interconnect_matrix_1__33), ._4(programmable_local_interconnect_matrix_1__35),
    .out_8(logic_element_2_2_out_8), ._5(clock_5_out), ._6(in_46), ._7(in_47));
  Logic_element_3 logic_element_3_2 (
    ._1(programmable_local_interconnect_matrix_1__22), ._2(programmable_local_interconnect_matrix_1__24),
    ._3(programmable_local_interconnect_matrix_1__26), ._4(programmable_local_interconnect_matrix_1__28),
    .out_8(logic_element_3_2_out_8), ._5(clock_6_out), ._6(in_55), ._7(in_56));
  Logic_element_4 logic_element_4_1 (
    ._2(programmable_local_interconnect_matrix_1__32), ._3(programmable_local_interconnect_matrix_1__34),
    ._4(programmable_local_interconnect_matrix_1__36), .out_8(logic_element_4_1_out_8), ._5(clock_7_out),
    ._6(in_58), ._7(in_59), ._1(programmable_local_interconnect_matrix_1__30));
  LED led_4 (.in(logic_element_1_2_out_8));
  LED led_5 (.in(logic_element_2_2_out_8));
  LED led_6 (.in(logic_element_3_2_out_8));
  LED led_7 (.in(logic_element_4_1_out_8));
  Programmable_local_interconnect_matrix programmable_local_interconnect_matrix_2 (
    ._16(_15), ._15(_14), ._14(_13), ._13(_12), ._12(_11), ._11(_10), ._10(_9), ._9(_8), ._8(_7), ._7(_6),
    ._6(_5), ._5(_4), ._4(_3), ._3(_2), ._2(_1), ._1(_0), ._20(in_1), ._19(in_2), ._18(in_3), ._17(in_4),
    ._21(programmable_local_interconnect_matrix_2__21), ._29(programmable_local_interconnect_matrix_2__29),
    ._22(programmable_local_interconnect_matrix_2__22));  // open: _23, _27, _31, _33, _35, _24, _26, _28, _30, _32, _34, _36, _25
  Clock clock_8 (.out(clock_8_out));
  Clock clock_9 (.out(clock_9_out));
  Clock clock_10 (.out(clock_10_out));
  Logic_element_1 logic_element_1_3 (
    .out_8(logic_element_1_3_out_8), .Clear(clock_8_out), .in_6(in_10), .Preset(in_11),
    .A3(programmable_local_interconnect_matrix_2__21), .A2(logic_element_3_3_out_8),
    .A1(logic_element_2_3_out_8), .A0(logic_element_1_3_out_8));
  Logic_element_2 logic_element_2_3 (
    ._1(programmable_local_interconnect_matrix_2__29), ._2(logic_element_3_3_out_8),
    ._3(logic_element_2_3_out_8), ._4(logic_element_1_3_out_8), .out_8(logic_element_2_3_out_8),
    ._5(clock_9_out), ._6(in_21), ._7(in_22));
  Logic_element_3 logic_element_3_3 (
    ._1(programmable_local_interconnect_matrix_2__22), ._2(logic_element_3_3_out_8),
    ._3(logic_element_2_3_out_8), ._4(logic_element_1_3_out_8), .out_8(logic_element_3_3_out_8),
    ._5(clock_10_out), ._6(in_33), ._7(in_34));
  LED led_8 (.in(logic_element_1_3_out_8));
  LED led_9 (.in(logic_element_2_3_out_8));
  LED led_10 (.in(logic_element_3_3_out_8));

  // Notes on the sheet:
  //   3 BITS Up/Down
  //   1
  //   01101010
  //   11110000
endmodule

module aa (
  input  _7,
  input  _6,
  input  _5,
  input  _4,
  input  _3,
  input  _2,
  input  _1,
  input  _0,
  input  _7_2,
  input  _6_2,
  input  _5_2,
  input  _4_2,
  input  _3_2,
  input  _2_2,
  input  _1_2,
  input  _0_2,
  input  _0_3,
  input  _0_4,
  input  _1_3,
  input  _1_4,
  input  _2_3,
  input  _2_4,
  input  _0_5,
  input  _0_6,
  input  _3_3,
  input  _3_4,
  input  _1_5,
  input  _1_6,
  input  _4_3,
  input  _4_4,
  input  _2_5,
  input  _2_6,
  input  _5_3,
  input  _5_4,
  input  _3_5,
  input  _3_6,
  input  _6_3,
  input  _6_4,
  input  _4_5,
  input  _4_6,
  input  _7_3,
  input  _7_4,
  input  _5_5,
  input  _5_6,
  input  _6_5,
  input  _6_6,
  input  _7_5,
  input  _7_6,
  input  _7_7,
  input  _6_7,
  input  _5_7,
  input  _4_7,
  input  _3_7,
  input  _2_7,
  input  _1_7,
  input  _0_7,
  input  _7_8,
  input  _6_8,
  input  _5_8,
  input  _4_8,
  input  _3_8,
  input  _2_8,
  input  _1_8,
  input  _0_8,
  input  _7_9,
  input  _6_9,
  input  _5_9,
  input  _4_9,
  input  _3_9,
  input  _2_9,
  input  _1_9,
  input  _0_9,
  input  _7_10,
  input  _6_10,
  input  _5_10,
  input  _4_10,
  input  _3_10,
  input  _2_10,
  input  _1_10,
  input  _0_10,
  input  _0_11,
  input  _0_12,
  input  _1_11,
  input  _1_12,
  input  _2_11,
  input  _2_12,
  input  _0_13,
  input  _0_14,
  input  _3_11,
  input  _3_12,
  input  _1_13,
  input  _1_14,
  input  _4_11,
  input  _4_12,
  input  _2_13,
  input  _2_14,
  input  _5_11,
  input  _5_12,
  input  _3_13,
  input  _3_14,
  input  _6_11,
  input  _6_12,
  input  _4_13,
  input  _4_14,
  input  _7_11,
  input  _7_12,
  input  _5_13,
  input  _5_14,
  input  _6_13,
  input  _6_14,
  input  _7_13,
  input  _7_14,
  input  _7_15,
  input  _6_15,
  input  _5_15,
  input  _4_15,
  input  _3_15,
  input  _2_15,
  input  _1_15,
  input  _0_15,
  input  _7_16,
  input  _6_16,
  input  _5_16,
  input  _4_16,
  input  _3_16,
  input  _2_16,
  input  _1_16,
  input  _0_16
);

  wire disjoint_switch_box_1_out_33, disjoint_switch_box_1_out_34, disjoint_switch_box_1_out_35,
       disjoint_switch_box_1_out_36, disjoint_switch_box_1_out_37, disjoint_switch_box_1_out_38,
       disjoint_switch_box_1_out_39, disjoint_switch_box_1_out_40, disjoint_switch_box_1_out_41,
       disjoint_switch_box_1_out_42, disjoint_switch_box_1_out_43, disjoint_switch_box_1_out_44,
       disjoint_switch_box_1_out_45, disjoint_switch_box_1_out_46, disjoint_switch_box_1_out_47,
       disjoint_switch_box_1_out_48, disjoint_switch_box_1_out_49, disjoint_switch_box_1_out_50,
       disjoint_switch_box_1_out_51, disjoint_switch_box_1_out_52, disjoint_switch_box_1_out_53,
       disjoint_switch_box_1_out_54, disjoint_switch_box_1_out_55, disjoint_switch_box_1_out_56,
       disjoint_switch_box_1_out_57, disjoint_switch_box_1_out_58, disjoint_switch_box_1_out_59,
       disjoint_switch_box_1_out_60, disjoint_switch_box_1_out_61, disjoint_switch_box_1_out_62,
       disjoint_switch_box_1_out_63, disjoint_switch_box_1_out_64, disjoint_switch_box_2_out_33,
       disjoint_switch_box_2_out_34, disjoint_switch_box_2_out_35, disjoint_switch_box_2_out_36,
       disjoint_switch_box_2_out_37, disjoint_switch_box_2_out_38, disjoint_switch_box_2_out_39,
       disjoint_switch_box_2_out_40, disjoint_switch_box_2_out_41, disjoint_switch_box_2_out_42,
       disjoint_switch_box_2_out_43, disjoint_switch_box_2_out_44, disjoint_switch_box_2_out_45,
       disjoint_switch_box_2_out_46, disjoint_switch_box_2_out_47, disjoint_switch_box_2_out_48,
       disjoint_switch_box_2_out_49, disjoint_switch_box_2_out_50, disjoint_switch_box_2_out_51,
       disjoint_switch_box_2_out_52, disjoint_switch_box_2_out_53, disjoint_switch_box_2_out_54,
       disjoint_switch_box_2_out_55, disjoint_switch_box_2_out_56, disjoint_switch_box_2_out_57,
       disjoint_switch_box_2_out_58, disjoint_switch_box_2_out_59, disjoint_switch_box_2_out_60,
       disjoint_switch_box_2_out_61, disjoint_switch_box_2_out_62, disjoint_switch_box_2_out_63,
       disjoint_switch_box_2_out_64, disjoint_switch_box_3_out_33, disjoint_switch_box_3_out_34,
       disjoint_switch_box_3_out_35, disjoint_switch_box_3_out_36, disjoint_switch_box_3_out_37,
       disjoint_switch_box_3_out_38, disjoint_switch_box_3_out_39, disjoint_switch_box_3_out_40,
       disjoint_switch_box_3_out_41, disjoint_switch_box_3_out_42, disjoint_switch_box_3_out_43,
       disjoint_switch_box_3_out_44, disjoint_switch_box_3_out_45, disjoint_switch_box_3_out_46,
       disjoint_switch_box_3_out_47, disjoint_switch_box_3_out_48, disjoint_switch_box_3_out_49,
       disjoint_switch_box_3_out_50, disjoint_switch_box_3_out_51, disjoint_switch_box_3_out_52,
       disjoint_switch_box_3_out_53, disjoint_switch_box_3_out_54, disjoint_switch_box_3_out_55,
       disjoint_switch_box_3_out_56, disjoint_switch_box_3_out_57, disjoint_switch_box_3_out_58,
       disjoint_switch_box_3_out_59, disjoint_switch_box_3_out_60, disjoint_switch_box_3_out_61,
       disjoint_switch_box_3_out_62, disjoint_switch_box_3_out_63, disjoint_switch_box_3_out_64,
       disjoint_switch_box_4_out_33, disjoint_switch_box_4_out_34, disjoint_switch_box_4_out_35,
       disjoint_switch_box_4_out_36, disjoint_switch_box_4_out_37, disjoint_switch_box_4_out_38,
       disjoint_switch_box_4_out_39, disjoint_switch_box_4_out_40, disjoint_switch_box_4_out_41,
       disjoint_switch_box_4_out_42, disjoint_switch_box_4_out_43, disjoint_switch_box_4_out_44,
       disjoint_switch_box_4_out_45, disjoint_switch_box_4_out_46, disjoint_switch_box_4_out_47,
       disjoint_switch_box_4_out_48, disjoint_switch_box_4_out_49, disjoint_switch_box_4_out_50,
       disjoint_switch_box_4_out_51, disjoint_switch_box_4_out_52, disjoint_switch_box_4_out_53,
       disjoint_switch_box_4_out_54, disjoint_switch_box_4_out_55, disjoint_switch_box_4_out_56,
       disjoint_switch_box_4_out_57, disjoint_switch_box_4_out_58, disjoint_switch_box_4_out_59,
       disjoint_switch_box_4_out_60, disjoint_switch_box_4_out_61, disjoint_switch_box_4_out_62,
       disjoint_switch_box_4_out_63, disjoint_switch_box_4_out_64;

  LED led_1 (.in(disjoint_switch_box_1_out_42));
  LED led_2 (.in(disjoint_switch_box_1_out_44));
  LED led_3 (.in(disjoint_switch_box_1_out_46));
  LED led_4 (.in(disjoint_switch_box_1_out_48));
  LED led_5 (.in(disjoint_switch_box_1_out_50));
  LED led_6 (.in(disjoint_switch_box_1_out_52));
  LED led_7 (.in(disjoint_switch_box_1_out_54));
  LED led_8 (.in(disjoint_switch_box_1_out_56));
  LED led_9 (.in(disjoint_switch_box_2_out_42));
  LED led_10 (.in(disjoint_switch_box_2_out_44));
  LED led_11 (.in(disjoint_switch_box_2_out_46));
  LED led_12 (.in(disjoint_switch_box_2_out_48));
  LED led_13 (.in(disjoint_switch_box_2_out_50));
  LED led_14 (.in(disjoint_switch_box_2_out_52));
  LED led_15 (.in(disjoint_switch_box_2_out_54));
  LED led_16 (.in(disjoint_switch_box_2_out_56));
  LED led_17 (.in(disjoint_switch_box_1_out_57));
  LED led_18 (.in(disjoint_switch_box_2_out_57));
  LED led_19 (.in(disjoint_switch_box_1_out_33));
  LED led_20 (.in(disjoint_switch_box_1_out_59));
  LED led_21 (.in(disjoint_switch_box_1_out_58));
  LED led_22 (.in(disjoint_switch_box_2_out_33));
  LED led_23 (.in(disjoint_switch_box_2_out_59));
  LED led_24 (.in(disjoint_switch_box_2_out_58));
  LED led_25 (.in(disjoint_switch_box_1_out_35));
  LED led_26 (.in(disjoint_switch_box_1_out_34));
  LED led_27 (.in(disjoint_switch_box_1_out_60));
  LED led_28 (.in(disjoint_switch_box_1_out_61));
  LED led_29 (.in(disjoint_switch_box_2_out_35));
  LED led_30 (.in(disjoint_switch_box_2_out_34));
  LED led_31 (.in(disjoint_switch_box_2_out_60));
  LED led_32 (.in(disjoint_switch_box_2_out_61));
  LED led_33 (.in(disjoint_switch_box_1_out_36));
  LED led_34 (.in(disjoint_switch_box_1_out_37));
  LED led_35 (.in(disjoint_switch_box_1_out_62));
  LED led_36 (.in(disjoint_switch_box_1_out_63));
  LED led_37 (.in(disjoint_switch_box_2_out_36));
  LED led_38 (.in(disjoint_switch_box_2_out_37));
  LED led_39 (.in(disjoint_switch_box_2_out_62));
  LED led_40 (.in(disjoint_switch_box_2_out_63));
  LED led_41 (.in(disjoint_switch_box_1_out_38));
  LED led_42 (.in(disjoint_switch_box_1_out_39));
  Disjoint_Switch_Box disjoint_switch_box_1 (
    .in_9(_0_3), .out_42(disjoint_switch_box_1_out_42), .in_11(_1_3), .out_44(disjoint_switch_box_1_out_44),
    .in_13(_2_3), .out_46(disjoint_switch_box_1_out_46), .in_15(_3_3), .out_48(disjoint_switch_box_1_out_48),
    .in_17(_4_3), .out_50(disjoint_switch_box_1_out_50), .in_19(_5_3), .out_52(disjoint_switch_box_1_out_52),
    .in_21(_6_3), .out_54(disjoint_switch_box_1_out_54), .in_23(_7_3), .out_56(disjoint_switch_box_1_out_56),
    .out_41(disjoint_switch_box_1_out_41), .in_10(_0_5), .out_43(disjoint_switch_box_1_out_43), .in_12(_1_5),
    .out_45(disjoint_switch_box_1_out_45), .in_14(_2_5), .out_47(disjoint_switch_box_1_out_47), .in_16(_3_5),
    .out_49(disjoint_switch_box_1_out_49), .in_18(_4_5), .out_51(disjoint_switch_box_1_out_51), .in_20(_5_5),
    .out_53(disjoint_switch_box_1_out_53), .in_22(_6_5), .out_55(disjoint_switch_box_1_out_55), .in_24(_7_5),
    .out_33(disjoint_switch_box_1_out_33), ._7(_7), .out_34(disjoint_switch_box_1_out_34), ._6(_6),
    .out_35(disjoint_switch_box_1_out_35), ._5(_5), .out_36(disjoint_switch_box_1_out_36), ._4(_4),
    .out_37(disjoint_switch_box_1_out_37), ._3(_3), .out_38(disjoint_switch_box_1_out_38), ._2(_2),
    .out_39(disjoint_switch_box_1_out_39), ._1(_1), .out_40(disjoint_switch_box_1_out_40), ._0(_0),
    .in_25(_7_7), .out_57(disjoint_switch_box_1_out_57), .in_26(_6_7), .out_58(disjoint_switch_box_1_out_58),
    .in_27(_5_7), .out_59(disjoint_switch_box_1_out_59), .in_28(_4_7), .out_60(disjoint_switch_box_1_out_60),
    .in_29(_3_7), .out_61(disjoint_switch_box_1_out_61), .in_30(_2_7), .out_62(disjoint_switch_box_1_out_62),
    .in_31(_1_7), .out_63(disjoint_switch_box_1_out_63), .in_32(_0_7), .out_64(disjoint_switch_box_1_out_64));
  LED led_43 (.in(disjoint_switch_box_1_out_64));
  LED led_44 (.in(disjoint_switch_box_2_out_39));
  LED led_45 (.in(disjoint_switch_box_2_out_38));
  Disjoint_Switch_Box disjoint_switch_box_2 (
    .in_9(_0_11), .out_42(disjoint_switch_box_2_out_42), .in_11(_1_11),
    .out_44(disjoint_switch_box_2_out_44), .in_13(_2_11), .out_46(disjoint_switch_box_2_out_46),
    .in_15(_3_11), .out_48(disjoint_switch_box_2_out_48), .in_17(_4_11),
    .out_50(disjoint_switch_box_2_out_50), .in_19(_5_11), .out_52(disjoint_switch_box_2_out_52),
    .in_21(_6_11), .out_54(disjoint_switch_box_2_out_54), .in_23(_7_11),
    .out_56(disjoint_switch_box_2_out_56), .out_41(disjoint_switch_box_2_out_41), .in_10(_0_13),
    .out_43(disjoint_switch_box_2_out_43), .in_12(_1_13), .out_45(disjoint_switch_box_2_out_45),
    .in_14(_2_13), .out_47(disjoint_switch_box_2_out_47), .in_16(_3_13),
    .out_49(disjoint_switch_box_2_out_49), .in_18(_4_13), .out_51(disjoint_switch_box_2_out_51),
    .in_20(_5_13), .out_53(disjoint_switch_box_2_out_53), .in_22(_6_13),
    .out_55(disjoint_switch_box_2_out_55), .in_24(_7_13), .out_33(disjoint_switch_box_2_out_33), ._7(_7_9),
    .out_34(disjoint_switch_box_2_out_34), ._6(_6_9), .out_35(disjoint_switch_box_2_out_35), ._5(_5_9),
    .out_36(disjoint_switch_box_2_out_36), ._4(_4_9), .out_37(disjoint_switch_box_2_out_37), ._3(_3_9),
    .out_38(disjoint_switch_box_2_out_38), ._2(_2_9), .out_39(disjoint_switch_box_2_out_39), ._1(_1_9),
    .out_40(disjoint_switch_box_2_out_40), ._0(_0_9), .in_25(_7_15), .out_57(disjoint_switch_box_2_out_57),
    .in_26(_6_15), .out_58(disjoint_switch_box_2_out_58), .in_27(_5_15),
    .out_59(disjoint_switch_box_2_out_59), .in_28(_4_15), .out_60(disjoint_switch_box_2_out_60),
    .in_29(_3_15), .out_61(disjoint_switch_box_2_out_61), .in_30(_2_15),
    .out_62(disjoint_switch_box_2_out_62), .in_31(_1_15), .out_63(disjoint_switch_box_2_out_63),
    .in_32(_0_15), .out_64(disjoint_switch_box_2_out_64));
  LED led_46 (.in(disjoint_switch_box_2_out_64));
  LED led_47 (.in(disjoint_switch_box_1_out_40));
  LED led_48 (.in(disjoint_switch_box_2_out_40));
  LED led_49 (.in(disjoint_switch_box_1_out_41));
  LED led_50 (.in(disjoint_switch_box_1_out_43));
  LED led_51 (.in(disjoint_switch_box_1_out_45));
  LED led_52 (.in(disjoint_switch_box_1_out_47));
  LED led_53 (.in(disjoint_switch_box_1_out_49));
  LED led_54 (.in(disjoint_switch_box_1_out_51));
  LED led_55 (.in(disjoint_switch_box_1_out_53));
  LED led_56 (.in(disjoint_switch_box_1_out_55));
  LED led_57 (.in(disjoint_switch_box_2_out_41));
  LED led_58 (.in(disjoint_switch_box_2_out_43));
  LED led_59 (.in(disjoint_switch_box_2_out_45));
  LED led_60 (.in(disjoint_switch_box_2_out_47));
  LED led_61 (.in(disjoint_switch_box_2_out_49));
  LED led_62 (.in(disjoint_switch_box_2_out_51));
  LED led_63 (.in(disjoint_switch_box_2_out_53));
  LED led_64 (.in(disjoint_switch_box_2_out_55));
  LED led_65 (.in(disjoint_switch_box_3_out_42));
  LED led_66 (.in(disjoint_switch_box_3_out_44));
  LED led_67 (.in(disjoint_switch_box_3_out_46));
  LED led_68 (.in(disjoint_switch_box_3_out_48));
  LED led_69 (.in(disjoint_switch_box_3_out_50));
  LED led_70 (.in(disjoint_switch_box_3_out_52));
  LED led_71 (.in(disjoint_switch_box_3_out_54));
  LED led_72 (.in(disjoint_switch_box_3_out_56));
  LED led_73 (.in(disjoint_switch_box_4_out_42));
  LED led_74 (.in(disjoint_switch_box_4_out_44));
  LED led_75 (.in(disjoint_switch_box_4_out_46));
  LED led_76 (.in(disjoint_switch_box_4_out_48));
  LED led_77 (.in(disjoint_switch_box_4_out_50));
  LED led_78 (.in(disjoint_switch_box_4_out_52));
  LED led_79 (.in(disjoint_switch_box_4_out_54));
  LED led_80 (.in(disjoint_switch_box_4_out_56));
  LED led_81 (.in(disjoint_switch_box_3_out_57));
  LED led_82 (.in(disjoint_switch_box_4_out_57));
  LED led_83 (.in(disjoint_switch_box_3_out_33));
  LED led_84 (.in(disjoint_switch_box_3_out_59));
  LED led_85 (.in(disjoint_switch_box_3_out_58));
  LED led_86 (.in(disjoint_switch_box_4_out_33));
  LED led_87 (.in(disjoint_switch_box_4_out_59));
  LED led_88 (.in(disjoint_switch_box_4_out_58));
  LED led_89 (.in(disjoint_switch_box_3_out_35));
  LED led_90 (.in(disjoint_switch_box_3_out_34));
  LED led_91 (.in(disjoint_switch_box_3_out_60));
  LED led_92 (.in(disjoint_switch_box_3_out_61));
  LED led_93 (.in(disjoint_switch_box_4_out_34));
  LED led_94 (.in(disjoint_switch_box_4_out_35));
  LED led_95 (.in(disjoint_switch_box_4_out_60));
  LED led_96 (.in(disjoint_switch_box_4_out_61));
  LED led_97 (.in(disjoint_switch_box_3_out_36));
  LED led_98 (.in(disjoint_switch_box_3_out_37));
  LED led_99 (.in(disjoint_switch_box_3_out_62));
  LED led_100 (.in(disjoint_switch_box_3_out_63));
  LED led_101 (.in(disjoint_switch_box_4_out_37));
  LED led_102 (.in(disjoint_switch_box_4_out_36));
  LED led_103 (.in(disjoint_switch_box_4_out_63));
  LED led_104 (.in(disjoint_switch_box_4_out_62));
  LED led_105 (.in(disjoint_switch_box_3_out_38));
  LED led_106 (.in(disjoint_switch_box_3_out_39));
  Disjoint_Switch_Box disjoint_switch_box_3 (
    .in_9(_0_4), .out_42(disjoint_switch_box_3_out_42), .in_11(_1_4), .out_44(disjoint_switch_box_3_out_44),
    .in_13(_2_4), .out_46(disjoint_switch_box_3_out_46), .in_15(_3_4), .out_48(disjoint_switch_box_3_out_48),
    .in_17(_4_4), .out_50(disjoint_switch_box_3_out_50), .in_19(_5_4), .out_52(disjoint_switch_box_3_out_52),
    .in_21(_6_4), .out_54(disjoint_switch_box_3_out_54), .in_23(_7_4), .out_56(disjoint_switch_box_3_out_56),
    .out_41(disjoint_switch_box_3_out_41), .in_10(_0_6), .out_43(disjoint_switch_box_3_out_43), .in_12(_1_6),
    .out_45(disjoint_switch_box_3_out_45), .in_14(_2_6), .out_47(disjoint_switch_box_3_out_47), .in_16(_3_6),
    .out_49(disjoint_switch_box_3_out_49), .in_18(_4_6), .out_51(disjoint_switch_box_3_out_51), .in_20(_5_6),
    .out_53(disjoint_switch_box_3_out_53), .in_22(_6_6), .out_55(disjoint_switch_box_3_out_55), .in_24(_7_6),
    .out_33(disjoint_switch_box_3_out_33), ._7(_7_2), .out_34(disjoint_switch_box_3_out_34), ._6(_6_2),
    .out_35(disjoint_switch_box_3_out_35), ._5(_5_2), .out_36(disjoint_switch_box_3_out_36), ._4(_4_2),
    .out_37(disjoint_switch_box_3_out_37), ._3(_3_2), .out_38(disjoint_switch_box_3_out_38), ._2(_2_2),
    .out_39(disjoint_switch_box_3_out_39), ._1(_1_2), .out_40(disjoint_switch_box_3_out_40), ._0(_0_2),
    .in_25(_7_8), .out_57(disjoint_switch_box_3_out_57), .in_26(_6_8), .out_58(disjoint_switch_box_3_out_58),
    .in_27(_5_8), .out_59(disjoint_switch_box_3_out_59), .in_28(_4_8), .out_60(disjoint_switch_box_3_out_60),
    .in_29(_3_8), .out_61(disjoint_switch_box_3_out_61), .in_30(_2_8), .out_62(disjoint_switch_box_3_out_62),
    .in_31(_1_8), .out_63(disjoint_switch_box_3_out_63), .in_32(_0_8), .out_64(disjoint_switch_box_3_out_64));
  LED led_107 (.in(disjoint_switch_box_3_out_64));
  LED led_108 (.in(disjoint_switch_box_4_out_39));
  LED led_109 (.in(disjoint_switch_box_4_out_38));
  Disjoint_Switch_Box disjoint_switch_box_4 (
    .in_9(_0_12), .out_42(disjoint_switch_box_4_out_42), .in_11(_1_12),
    .out_44(disjoint_switch_box_4_out_44), .in_13(_2_12), .out_46(disjoint_switch_box_4_out_46),
    .in_15(_3_12), .out_48(disjoint_switch_box_4_out_48), .in_17(_4_12),
    .out_50(disjoint_switch_box_4_out_50), .in_19(_5_12), .out_52(disjoint_switch_box_4_out_52),
    .in_21(_6_12), .out_54(disjoint_switch_box_4_out_54), .in_23(_7_12),
    .out_56(disjoint_switch_box_4_out_56), .out_41(disjoint_switch_box_4_out_41), .in_10(_0_14),
    .out_43(disjoint_switch_box_4_out_43), .in_12(_1_14), .out_45(disjoint_switch_box_4_out_45),
    .in_14(_2_14), .out_47(disjoint_switch_box_4_out_47), .in_16(_3_14),
    .out_49(disjoint_switch_box_4_out_49), .in_18(_4_14), .out_51(disjoint_switch_box_4_out_51),
    .in_20(_5_14), .out_53(disjoint_switch_box_4_out_53), .in_22(_6_14),
    .out_55(disjoint_switch_box_4_out_55), .in_24(_7_14), .out_33(disjoint_switch_box_4_out_33), ._7(_7_10),
    .out_34(disjoint_switch_box_4_out_34), ._6(_6_10), .out_35(disjoint_switch_box_4_out_35), ._5(_5_10),
    .out_36(disjoint_switch_box_4_out_36), ._4(_4_10), .out_37(disjoint_switch_box_4_out_37), ._3(_3_10),
    .out_38(disjoint_switch_box_4_out_38), ._2(_2_10), .out_39(disjoint_switch_box_4_out_39), ._1(_1_10),
    .out_40(disjoint_switch_box_4_out_40), ._0(_0_10), .in_25(_7_16), .out_57(disjoint_switch_box_4_out_57),
    .in_26(_6_16), .out_58(disjoint_switch_box_4_out_58), .in_27(_5_16),
    .out_59(disjoint_switch_box_4_out_59), .in_28(_4_16), .out_60(disjoint_switch_box_4_out_60),
    .in_29(_3_16), .out_61(disjoint_switch_box_4_out_61), .in_30(_2_16),
    .out_62(disjoint_switch_box_4_out_62), .in_31(_1_16), .out_63(disjoint_switch_box_4_out_63),
    .in_32(_0_16), .out_64(disjoint_switch_box_4_out_64));
  LED led_110 (.in(disjoint_switch_box_4_out_64));
  LED led_111 (.in(disjoint_switch_box_3_out_40));
  LED led_112 (.in(disjoint_switch_box_4_out_40));
  LED led_113 (.in(disjoint_switch_box_3_out_41));
  LED led_114 (.in(disjoint_switch_box_3_out_43));
  LED led_115 (.in(disjoint_switch_box_3_out_45));
  LED led_116 (.in(disjoint_switch_box_3_out_47));
  LED led_117 (.in(disjoint_switch_box_3_out_49));
  LED led_118 (.in(disjoint_switch_box_3_out_51));
  LED led_119 (.in(disjoint_switch_box_3_out_53));
  LED led_120 (.in(disjoint_switch_box_3_out_55));
  LED led_121 (.in(disjoint_switch_box_4_out_41));
  LED led_122 (.in(disjoint_switch_box_4_out_43));
  LED led_123 (.in(disjoint_switch_box_4_out_45));
  LED led_124 (.in(disjoint_switch_box_4_out_47));
  LED led_125 (.in(disjoint_switch_box_4_out_49));
  LED led_126 (.in(disjoint_switch_box_4_out_51));
  LED led_127 (.in(disjoint_switch_box_4_out_53));
  LED led_128 (.in(disjoint_switch_box_4_out_55));
endmodule
