// Logisim project Bloque Logico - 4 BITS.circ as structural Verilog: 14 circuits, main circuit Logic_Block
module GASIM (
  input  Pst,
  input  Rst,
  input  _15,
  input  _14,
  input  _13,
  input  _12,
  input  _11,
  input  _10,
  input  _9,
  input  _8,
  input  _7,
  input  _6,
  input  _5,
  input  _4,
  input  _3,
  input  _2,
  input  _1,
  input  _0,
  input  _0_2,
  input  _1_2,
  input  _2_2,
  input  _3_2,
  input  _4_2,
  input  _5_2,
  input  _6_2,
  input  _7_2,
  input  _8_2,
  input  _9_2,
  input  _10_2,
  input  _11_2,
  input  Pst_2,
  input  _12_2,
  input  Rst_2,
  input  _13_2,
  input  _14_2,
  input  _15_2,
  input  _15_3,
  input  _14_3,
  input  _13_3,
  input  Rst_3,
  input  _12_3,
  input  Pst_3,
  input  _11_3,
  input  _10_3,
  input  _9_3,
  input  _8_3,
  input  _7_3,
  input  _6_3,
  input  _5_3,
  input  _4_3,
  input  _3_3,
  input  _2_3,
  input  _1_3,
  input  _0_3,
  input  _0_4,
  input  _1_4,
  input  _2_4,
  input  _3_4,
  input  _4_4,
  input  _5_4,
  input  _6_4,
  input  _7_4,
  input  _8_4,
  input  _9_4,
  input  _10_4,
  input  _11_4,
  input  _12_4,
  input  _13_4,
  input  _14_4,
  input  _15_4,
  input  Rst_4,
  input  Pst_4
);

  wire Clk_2_out, Clk_3_out, Clk_4_out, Clk_out, logic_block_1__17, logic_block_1__18, logic_block_1__19,
       logic_block_1__20, logic_block_1__37, logic_block_1__38, logic_block_1__39, logic_block_1__40,
       logic_block_1__57, logic_block_1__58, logic_block_1__59, logic_block_1__60, logic_block_1__77,
       logic_block_1__78, logic_block_1__79, logic_block_1__80;

  Clock Clk (.out(Clk_out));
  LED A0 (.in(logic_block_1__17));
  LED A1 (.in(logic_block_1__18));
  LED A2 (.in(logic_block_1__19));
  LED A3 (.in(logic_block_1__20));
  LED A1_2 (.in(logic_block_1__78));
  LED A2_2 (.in(logic_block_1__79));
  LED A0_2 (.in(logic_block_1__77));
  LED A3_2 (.in(logic_block_1__80));
  Clock Clk_2 (.out(Clk_2_out));
  Clock Clk_3 (.out(Clk_3_out));
  LED A3_3 (.in(logic_block_1__40));
  LED A1_3 (.in(logic_block_1__38));
  LED A2_3 (.in(logic_block_1__39));
  Logic_Block logic_block_1 (
    ._1(_15_3), ._2(_14_2), ._3(_13_2), ._4(_12_2), ._5(_11_2), ._6(_10_2), ._7(_9_2), ._8(_8_2), ._9(_7_2),
    ._10(_6_2), ._11(_5_2), ._12(_4_2), ._13(_3_2), ._14(_2_2), ._15(_1_2), ._16(_0_2),
    ._17(logic_block_1__17), ._18(logic_block_1__18), ._19(logic_block_1__19), ._20(logic_block_1__20),
    ._81(Clk_out), ._82(Rst_3), ._83(Pst_3), ._57(logic_block_1__57), ._58(logic_block_1__58),
    ._59(logic_block_1__59), ._60(logic_block_1__60), ._41(_15_2), ._42(_14_3), ._89(Pst_2), ._43(_13_3),
    ._88(Rst_2), ._44(_12_3), ._87(Clk_4_out), ._45(_11_3), ._46(_10_3), ._47(_9_3), ._48(_8_3), ._49(_7_3),
    ._50(_6_3), ._51(_5_3), ._52(_4_3), ._53(_3_3), ._54(_2_3), ._55(_1_3), ._56(_0_3), ._76(_0), ._75(_1),
    ._74(_2), ._73(_3), ._72(_4), ._71(_5), ._70(_6), ._69(_7), ._68(_8), ._67(_9), ._66(_10), ._65(_11),
    ._64(_12), ._63(_13), ._62(_14), ._61(_15), ._92(Pst), ._91(Rst), ._90(Clk_2_out),
    ._80(logic_block_1__80), ._79(logic_block_1__79), ._78(logic_block_1__78), ._77(logic_block_1__77),
    ._36(_0_4), ._35(_1_4), ._34(_2_4), ._33(_3_4), ._32(_4_4), ._31(_5_4), ._30(_6_4), ._29(_7_4),
    ._28(_8_4), ._27(_9_4), ._26(_10_4), ._25(_11_4), ._24(_12_4), ._23(_13_4), ._22(_14_4), ._21(_15_4),
    ._84(Clk_3_out), ._85(Rst_4), ._86(Pst_4), ._40(logic_block_1__40), ._39(logic_block_1__39),
    ._38(logic_block_1__38), ._37(logic_block_1__37));
  LED A0_3 (.in(logic_block_1__37));
  LED A0_4 (.in(logic_block_1__57));
  LED A1_4 (.in(logic_block_1__58));
  LED A2_4 (.in(logic_block_1__59));
  LED A3_4 (.in(logic_block_1__60));
  Clock Clk_4 (.out(Clk_4_out));
endmodule

module Logic_Block (
  input  _76,
  input  _75,
  input  _74,
  input  _73,
  input  _72,
  input  _71,
  input  _70,
  input  _69,
  input  _68,
  input  _67,
  input  _66,
  input  _65,
  input  _64,
  input  _63,
  input  _62,
  input  _61,
  input  _1,
  input  _2,
  input  _3,
  input  _4,
  input  _5,
  input  _6,
  input  _7,
  input  _8,
  input  _9,
  input  _10,
  input  _11,
  input  _12,
  input  _13,
  input  _14,
  input  _15,
  input  _16,
  input  _92,
  input  _91,
  input  _90,
  input  _81,
  input  _89,
  input  _41,
  input  _82,
  input  _88,
  input  _42,
  input  _83,
  input  _87,
  input  _43,
  input  _44,
  input  _84,
  input  _85,
  input  _86,
  input  _45,
  input  _36,
  input  _35,
  input  _34,
  input  _33,
  input  _32,
  input  _31,
  input  _30,
  input  _29,
  input  _28,
  input  _27,
  input  _26,
  input  _25,
  input  _24,
  input  _23,
  input  _22,
  input  _21,
  input  _46,
  input  _47,
  input  _48,
  input  _49,
  input  _50,
  input  _51,
  input  _52,
  input  _53,
  input  _54,
  input  _55,
  input  _56,
  output _80,
  output _79,
  output _78,
  output _77,
  output _57,
  output _58,
  output _59,
  output _60,
  output _17,
  output _18,
  output _19,
  output _20,
  output _40,
  output _39,
  output _38,
  output _37
);

  wire Clock_out, or_1_out, or_2_out, or_3_out, or_4_out, or_5_out, or_6_out, or_7_out, or_8_out, or_9_out,
       or_10_out, or_11_out, or_12_out, or_13_out, or_14_out, or_15_out, or_16_out, Preset_out,
       programmable_local_interconnect_matrix_1__21, programmable_local_interconnect_matrix_1__22,
       programmable_local_interconnect_matrix_1__23, programmable_local_interconnect_matrix_1__24,
       programmable_local_interconnect_matrix_1__25, programmable_local_interconnect_matrix_1__26,
       programmable_local_interconnect_matrix_1__27, programmable_local_interconnect_matrix_1__28,
       programmable_local_interconnect_matrix_1__29, programmable_local_interconnect_matrix_1__30,
       programmable_local_interconnect_matrix_1__31, programmable_local_interconnect_matrix_1__32,
       programmable_local_interconnect_matrix_1__33, programmable_local_interconnect_matrix_1__34,
       programmable_local_interconnect_matrix_1__35, programmable_local_interconnect_matrix_1__36, Reset_out;

  or or_1 (or_1_out, _61, _1, _21, _41);
  or or_2 (or_2_out, _62, _2, _22, _42);
  or or_3 (or_3_out, _63, _3, _23, _43);
  or or_4 (or_4_out, _64, _4, _24, _44);
  or or_5 (or_5_out, _65, _5, _25, _45);
  or or_6 (or_6_out, _66, _6, _26, _46);
  or or_7 (or_7_out, _67, _7, _27, _47);
  or or_8 (or_8_out, _68, _8, _28, _48);
  or or_9 (or_9_out, _69, _9, _29, _49);
  or or_10 (or_10_out, _70, _10, _30, _50);
  or or_11 (or_11_out, _71, _11, _31, _51);
  or or_12 (or_12_out, _72, _12, _32, _52);
  or or_13 (or_13_out, _73, _13, _33, _53);
  or or_14 (or_14_out, _74, _14, _34, _54);
  or or_15 (or_15_out, _75, _15, _35, _55);
  or or_16 (or_16_out, _76, _16, _36, _56);
  Programmable_local_interconnect_matrix programmable_local_interconnect_matrix_1 (
    ._16(or_1_out), ._15(or_2_out), ._14(or_3_out), ._13(or_4_out), ._12(or_5_out), ._11(or_6_out),
    ._10(or_7_out), ._9(or_8_out), ._8(or_9_out), ._7(or_10_out), ._6(or_11_out), ._5(or_12_out),
    ._4(or_13_out), ._3(or_14_out), ._2(or_15_out), ._1(or_16_out), ._20(_17), ._19(_18), ._18(_19),
    ._17(_20), ._21(programmable_local_interconnect_matrix_1__21),
    ._23(programmable_local_interconnect_matrix_1__23), ._27(programmable_local_interconnect_matrix_1__27),
    ._29(programmable_local_interconnect_matrix_1__29), ._31(programmable_local_interconnect_matrix_1__31),
    ._33(programmable_local_interconnect_matrix_1__33), ._35(programmable_local_interconnect_matrix_1__35),
    ._22(programmable_local_interconnect_matrix_1__22), ._24(programmable_local_interconnect_matrix_1__24),
    ._26(programmable_local_interconnect_matrix_1__26), ._28(programmable_local_interconnect_matrix_1__28),
    ._30(programmable_local_interconnect_matrix_1__30), ._32(programmable_local_interconnect_matrix_1__32),
    ._34(programmable_local_interconnect_matrix_1__34), ._36(programmable_local_interconnect_matrix_1__36),
    ._25(programmable_local_interconnect_matrix_1__25));
  or Clock (Clock_out, _81, _84, _87, _90);
  or Reset (Reset_out, _82, _85, _88, _91);
  or Preset (Preset_out, _83, _86, _89, _92);
  Logic_element_1 logic_element_1_1 (
    .out_8(_17), .Clear(Clock_out), .in_6(Reset_out), .Preset(Preset_out),
    .A3(programmable_local_interconnect_matrix_1__21), .A2(programmable_local_interconnect_matrix_1__23),
    .A1(programmable_local_interconnect_matrix_1__25), .A0(programmable_local_interconnect_matrix_1__27));
  Logic_element_2 logic_element_2_1 (
    ._1(programmable_local_interconnect_matrix_1__29), ._2(programmable_local_interconnect_matrix_1__31),
    ._3(programmable_local_interconnect_matrix_1__33), ._4(programmable_local_interconnect_matrix_1__35),
    .out_8(_18), ._5(Clock_out), ._6(Reset_out), ._7(Preset_out));
  Logic_element_3 logic_element_3_1 (
    ._1(programmable_local_interconnect_matrix_1__22), ._2(programmable_local_interconnect_matrix_1__24),
    ._3(programmable_local_interconnect_matrix_1__26), ._4(programmable_local_interconnect_matrix_1__28),
    .out_8(_19), ._5(Clock_out), ._6(Reset_out), ._7(Preset_out));
  Logic_element_4 logic_element_4_1 (
    ._2(programmable_local_interconnect_matrix_1__32), ._3(programmable_local_interconnect_matrix_1__34),
    ._4(programmable_local_interconnect_matrix_1__36), .out_8(_20), ._5(Clock_out), ._6(Reset_out),
    ._7(Preset_out), ._1(programmable_local_interconnect_matrix_1__30));

  assign _37 = _17;
  assign _38 = _18;
  assign _39 = _19;
  assign _40 = _20;
  assign _57 = _17;
  assign _58 = _18;
  assign _59 = _19;
  assign _60 = _20;
  assign _77 = _17;
  assign _78 = _18;
  assign _79 = _19;
  assign _80 = _20;

  // Notes on the sheet:
  //   Input 00
  //   Input 15
  //   Clock
  //   General Purpose Feedback
  //   Clock
  //   Clock
  //   Clock
  //   Output 0
  //   Output 3
endmodule

module Logic_element_1 (
  input  A3,
  input  A2,
  input  A1,
  input  A0,
  input  Clear,
  input  in_6,
  input  Preset,
  output out_8
);

  wire d_ff_1_q, rom_1_data, rom_2_data;

  ROM #(.addrWidth(4), .dataWidth(1)) rom_1 (.addr({A3, A2, A1, A0}), .data(rom_1_data), .sel(1'b1));
  ROM #(.addrWidth(4), .dataWidth(1)) rom_2 (.addr(4'b1111), .data(rom_2_data), .sel(1'b1));
  D_Flip_Flop d_ff_1 (.clk(Clear), .D(rom_1_data), .Q(d_ff_1_q), .preset(in_6), .en(1'b1), .reset(Preset));  // open: Qn
  _01S u_01s_1 (._2(rom_1_data), ._3(d_ff_1_q), ._4(rom_2_data), .out_4(out_8));

  // Notes on the sheet:
  //   Look Up Table (LUT)
  //   Combinatory / Register
  //   contents of rom_1 (hex, n*v repeats v):
  //   1 0 0 1 1 0 0 1 0 1 1 0 0 1 1
  //   contents of rom_2 (hex, n*v repeats v):
  //   15*0 1
  //   Clock (Rising Edge)
endmodule

module Logic_element_2 (
  input  _1,
  input  _2,
  input  _3,
  input  _4,
  input  _5,
  input  _6,
  input  _7,
  output out_8
);

  wire d_ff_1_q, rom_1_data, rom_2_data;

  ROM #(.addrWidth(4), .dataWidth(1)) rom_1 (.addr({_1, _2, _3, _4}), .data(rom_1_data), .sel(1'b1));
  ROM #(.addrWidth(4), .dataWidth(1)) rom_2 (.addr(4'b1111), .data(rom_2_data), .sel(1'b1));
  D_Flip_Flop d_ff_1 (.clk(_5), .D(rom_1_data), .Q(d_ff_1_q), .preset(_6), .en(1'b1), .reset(_7));  // open: Qn
  _01S u_01s_1 (._2(rom_1_data), ._3(d_ff_1_q), ._4(rom_2_data), .out_4(out_8));

  // Notes on the sheet:
  //   A3
  //   A2
  //   A1
  //   A0
  //   Look Up Table (LUT)
  //   Combinatory / Register
  //   contents of rom_1 (hex, n*v repeats v):
  //   1 1 0 0 1 0 1 0 1 0 1 0 1 0 1
  //   contents of rom_2 (hex, n*v repeats v):
  //   15*0 1
  //   Clock (Rising Edge)
  //   Clear
  //   Preset
endmodule

module Logic_element_3 (
  input  _1,
  input  _2,
  input  _3,
  input  _4,
  input  _5,
  input  _6,
  input  _7,
  output out_8
);

  wire d_ff_1_q, rom_1_data, rom_2_data;

  ROM #(.addrWidth(4), .dataWidth(1)) rom_1 (.addr({_1, _2, _3, _4}), .data(rom_1_data), .sel(1'b1));
  ROM #(.addrWidth(4), .dataWidth(1)) rom_2 (.addr(4'b1111), .data(rom_2_data), .sel(1'b1));
  D_Flip_Flop d_ff_1 (.clk(_5), .D(rom_1_data), .Q(d_ff_1_q), .preset(_6), .en(1'b1), .reset(_7));  // open: Qn
  _01S u_01s_1 (._2(rom_1_data), ._3(d_ff_1_q), ._4(rom_2_data), .out_4(out_8));

  // Notes on the sheet:
  //   A3
  //   A2
  //   A1
  //   A0
  //   Look Up Table (LUT)
  //   Combinatory / Register
  //   contents of rom_1 (hex, n*v repeats v):
  //   0 1 0 0 1 1 0 5*1
  //   contents of rom_2 (hex, n*v repeats v):
  //   15*0 1
  //   Clock (Rising Edge)
  //   Clear
  //   Preset
endmodule

module Logic_element_4 (
  input  _1,
  input  _2,
  input  _3,
  input  _4,
  input  _5,
  input  _6,
  input  _7,
  output out_8
);

  wire d_ff_1_q, rom_1_data, rom_2_data;

  ROM #(.addrWidth(4), .dataWidth(1)) rom_1 (.addr({_1, _2, _3, _4}), .data(rom_1_data), .sel(1'b1));
  ROM #(.addrWidth(4), .dataWidth(1)) rom_2 (.addr(4'b1111), .data(rom_2_data), .sel(1'b1));
  D_Flip_Flop d_ff_1 (.clk(_5), .D(rom_1_data), .Q(d_ff_1_q), .preset(_6), .en(1'b1), .reset(_7));  // open: Qn
  _01S u_01s_1 (._2(rom_1_data), ._3(d_ff_1_q), ._4(rom_2_data), .out_4(out_8));

  // Notes on the sheet:
  //   A3
  //   A2
  //   A1
  //   A0
  //   Look Up Table (LUT)
  //   Combinatory / Register
  //   contents of rom_1 (hex, n*v repeats v):
  //   4*1 0 1 1 1 0 0 1
  //   contents of rom_2 (hex, n*v repeats v):
  //   15*0 1
  //   Clock (Rising Edge)
  //   Clear
  //   Preset
endmodule

// Programmable Local Interconnect Matrix
module Programmable_local_interconnect_matrix (
  input  _16,
  input  _15,
  input  _14,
  input  _13,
  input  _12,
  input  _11,
  input  _10,
  input  _9,
  input  _8,
  input  _7,
  input  _6,
  input  _5,
  input  _4,
  input  _3,
  input  _2,
  input  _1,
  input  _20,
  input  _19,
  input  _18,
  input  _17,
  output _21,
  output _22,
  output _23,
  output _24,
  output _26,
  output _25,
  output _27,
  output _28,
  output _29,
  output _30,
  output _31,
  output _32,
  output _33,
  output _34,
  output _35,
  output _36
);

  wire [4:0] rom_1_data, rom_2_data, rom_3_data, rom_4_data, rom_5_data, rom_6_data, rom_7_data, rom_8_data,
       rom_9_data, rom_10_data, rom_11_data, rom_12_data, rom_13_data, rom_14_data, rom_15_data, rom_16_data;

  _20_to_1_MUX u_20_to_1_mux_1 (
    ._8(_8), ._7(_7), ._6(_6), ._5(_5), ._4(_4), ._3(_3), ._2(_2), ._1(_1), ._9(_9), ._10(_10), ._11(_11),
    ._12(_12), ._13(_13), ._14(_14), ._15(_15), ._16(_16), ._17(_17), ._18(_18), ._19(_19), ._20(_20),
    ._21(rom_1_data[4]), ._22(rom_1_data[3]), ._23(rom_1_data[2]), ._24(rom_1_data[1]), ._25(rom_1_data[0]),
    ._26(_21));
  ROM #(.addrWidth(2), .dataWidth(5)) rom_1 (.addr(2'b11), .data(rom_1_data), .sel(1'b1));
  _20_to_1_MUX u_20_to_1_mux_2 (
    ._8(_8), ._7(_7), ._6(_6), ._5(_5), ._4(_4), ._3(_3), ._2(_2), ._1(_1), ._9(_9), ._10(_10), ._11(_11),
    ._12(_12), ._13(_13), ._14(_14), ._15(_15), ._16(_16), ._17(_17), ._18(_18), ._19(_19), ._20(_20),
    ._21(rom_2_data[4]), ._22(rom_2_data[3]), ._23(rom_2_data[2]), ._24(rom_2_data[1]), ._25(rom_2_data[0]),
    ._26(_23));
  ROM #(.addrWidth(2), .dataWidth(5)) rom_2 (.addr(2'b11), .data(rom_2_data), .sel(1'b1));
  _20_to_1_MUX u_20_to_1_mux_3 (
    ._8(_8), ._7(_7), ._6(_6), ._5(_5), ._4(_4), ._3(_3), ._2(_2), ._1(_1), ._9(_9), ._10(_10), ._11(_11),
    ._12(_12), ._13(_13), ._14(_14), ._15(_15), ._16(_16), ._17(_17), ._18(_18), ._19(_19), ._20(_20),
    ._21(rom_3_data[4]), ._22(rom_3_data[3]), ._23(rom_3_data[2]), ._24(rom_3_data[1]), ._25(rom_3_data[0]),
    ._26(_25));
  ROM #(.addrWidth(2), .dataWidth(5)) rom_3 (.addr(2'b11), .data(rom_3_data), .sel(1'b1));
  _20_to_1_MUX u_20_to_1_mux_4 (
    ._8(_8), ._7(_7), ._6(_6), ._5(_5), ._4(_4), ._3(_3), ._2(_2), ._1(_1), ._9(_9), ._10(_10), ._11(_11),
    ._12(_12), ._13(_13), ._14(_14), ._15(_15), ._16(_16), ._17(_17), ._18(_18), ._19(_19), ._20(_20),
    ._21(rom_4_data[4]), ._22(rom_4_data[3]), ._23(rom_4_data[2]), ._24(rom_4_data[1]), ._25(rom_4_data[0]),
    ._26(_27));
  ROM #(.addrWidth(2), .dataWidth(5)) rom_4 (.addr(2'b11), .data(rom_4_data), .sel(1'b1));
  _20_to_1_MUX u_20_to_1_mux_5 (
    ._8(_8), ._7(_7), ._6(_6), ._5(_5), ._4(_4), ._3(_3), ._2(_2), ._1(_1), ._9(_9), ._10(_10), ._11(_11),
    ._12(_12), ._13(_13), ._14(_14), ._15(_15), ._16(_16), ._17(_17), ._18(_18), ._19(_19), ._20(_20),
    ._21(rom_5_data[4]), ._22(rom_5_data[3]), ._23(rom_5_data[2]), ._24(rom_5_data[1]), ._25(rom_5_data[0]),
    ._26(_29));
  ROM #(.addrWidth(2), .dataWidth(5)) rom_5 (.addr(2'b11), .data(rom_5_data), .sel(1'b1));
  _20_to_1_MUX u_20_to_1_mux_6 (
    ._8(_8), ._7(_7), ._6(_6), ._5(_5), ._4(_4), ._3(_3), ._2(_2), ._1(_1), ._9(_9), ._10(_10), ._11(_11),
    ._12(_12), ._13(_13), ._14(_14), ._15(_15), ._16(_16), ._17(_17), ._18(_18), ._19(_19), ._20(_20),
    ._21(rom_6_data[4]), ._22(rom_6_data[3]), ._23(rom_6_data[2]), ._24(rom_6_data[1]), ._25(rom_6_data[0]),
    ._26(_31));
  ROM #(.addrWidth(2), .dataWidth(5)) rom_6 (.addr(2'b11), .data(rom_6_data), .sel(1'b1));
  _20_to_1_MUX u_20_to_1_mux_7 (
    ._8(_8), ._7(_7), ._6(_6), ._5(_5), ._4(_4), ._3(_3), ._2(_2), ._1(_1), ._9(_9), ._10(_10), ._11(_11),
    ._12(_12), ._13(_13), ._14(_14), ._15(_15), ._16(_16), ._17(_17), ._18(_18), ._19(_19), ._20(_20),
    ._21(rom_7_data[4]), ._22(rom_7_data[3]), ._23(rom_7_data[2]), ._24(rom_7_data[1]), ._25(rom_7_data[0]),
    ._26(_33));
  ROM #(.addrWidth(2), .dataWidth(5)) rom_7 (.addr(2'b11), .data(rom_7_data), .sel(1'b1));
  _20_to_1_MUX u_20_to_1_mux_8 (
    ._8(_8), ._7(_7), ._6(_6), ._5(_5), ._4(_4), ._3(_3), ._2(_2), ._1(_1), ._9(_9), ._10(_10), ._11(_11),
    ._12(_12), ._13(_13), ._14(_14), ._15(_15), ._16(_16), ._17(_17), ._18(_18), ._19(_19), ._20(_20),
    ._21(rom_8_data[4]), ._22(rom_8_data[3]), ._23(rom_8_data[2]), ._24(rom_8_data[1]), ._25(rom_8_data[0]),
    ._26(_35));
  ROM #(.addrWidth(2), .dataWidth(5)) rom_8 (.addr(2'b11), .data(rom_8_data), .sel(1'b1));
  ROM #(.addrWidth(2), .dataWidth(5)) rom_9 (.addr(2'b11), .data(rom_9_data), .sel(1'b1));
  ROM #(.addrWidth(2), .dataWidth(5)) rom_10 (.addr(2'b11), .data(rom_10_data), .sel(1'b1));
  ROM #(.addrWidth(2), .dataWidth(5)) rom_11 (.addr(2'b11), .data(rom_11_data), .sel(1'b1));
  ROM #(.addrWidth(2), .dataWidth(5)) rom_12 (.addr(2'b11), .data(rom_12_data), .sel(1'b1));
  ROM #(.addrWidth(2), .dataWidth(5)) rom_13 (.addr(2'b11), .data(rom_13_data), .sel(1'b1));
  ROM #(.addrWidth(2), .dataWidth(5)) rom_14 (.addr(2'b11), .data(rom_14_data), .sel(1'b1));
  ROM #(.addrWidth(2), .dataWidth(5)) rom_15 (.addr(2'b11), .data(rom_15_data), .sel(1'b1));
  ROM #(.addrWidth(2), .dataWidth(5)) rom_16 (.addr(2'b11), .data(rom_16_data), .sel(1'b1));
  _20_to_1_MUX u_20_to_1_mux_9 (
    ._8(_8), ._7(_7), ._6(_6), ._5(_5), ._4(_4), ._3(_3), ._2(_2), ._1(_1), ._9(_9), ._10(_10), ._11(_11),
    ._12(_12), ._13(_13), ._14(_14), ._15(_15), ._16(_16), ._17(_17), ._18(_18), ._19(_19), ._20(_20),
    ._21(rom_9_data[4]), ._22(rom_9_data[3]), ._23(rom_9_data[2]), ._24(rom_9_data[1]), ._25(rom_9_data[0]),
    ._26(_22));
  _20_to_1_MUX u_20_to_1_mux_10 (
    ._8(_8), ._7(_7), ._6(_6), ._5(_5), ._4(_4), ._3(_3), ._2(_2), ._1(_1), ._9(_9), ._10(_10), ._11(_11),
    ._12(_12), ._13(_13), ._14(_14), ._15(_15), ._16(_16), ._17(_17), ._18(_18), ._19(_19), ._20(_20),
    ._21(rom_10_data[4]), ._22(rom_10_data[3]), ._23(rom_10_data[2]), ._24(rom_10_data[1]),
    ._25(rom_10_data[0]), ._26(_24));
  _20_to_1_MUX u_20_to_1_mux_11 (
    ._8(_8), ._7(_7), ._6(_6), ._5(_5), ._4(_4), ._3(_3), ._2(_2), ._1(_1), ._9(_9), ._10(_10), ._11(_11),
    ._12(_12), ._13(_13), ._14(_14), ._15(_15), ._16(_16), ._17(_17), ._18(_18), ._19(_19), ._20(_20),
    ._21(rom_11_data[4]), ._22(rom_11_data[3]), ._23(rom_11_data[2]), ._24(rom_11_data[1]),
    ._25(rom_11_data[0]), ._26(_26));
  _20_to_1_MUX u_20_to_1_mux_12 (
    ._8(_8), ._7(_7), ._6(_6), ._5(_5), ._4(_4), ._3(_3), ._2(_2), ._1(_1), ._9(_9), ._10(_10), ._11(_11),
    ._12(_12), ._13(_13), ._14(_14), ._15(_15), ._16(_16), ._17(_17), ._18(_18), ._19(_19), ._20(_20),
    ._21(rom_12_data[4]), ._22(rom_12_data[3]), ._23(rom_12_data[2]), ._24(rom_12_data[1]),
    ._25(rom_12_data[0]), ._26(_28));
  _20_to_1_MUX u_20_to_1_mux_13 (
    ._8(_8), ._7(_7), ._6(_6), ._5(_5), ._4(_4), ._3(_3), ._2(_2), ._1(_1), ._9(_9), ._10(_10), ._11(_11),
    ._12(_12), ._13(_13), ._14(_14), ._15(_15), ._16(_16), ._17(_17), ._18(_18), ._19(_19), ._20(_20),
    ._21(rom_13_data[4]), ._22(rom_13_data[3]), ._23(rom_13_data[2]), ._24(rom_13_data[1]),
    ._25(rom_13_data[0]), ._26(_30));
  _20_to_1_MUX u_20_to_1_mux_14 (
    ._8(_8), ._7(_7), ._6(_6), ._5(_5), ._4(_4), ._3(_3), ._2(_2), ._1(_1), ._9(_9), ._10(_10), ._11(_11),
    ._12(_12), ._13(_13), ._14(_14), ._15(_15), ._16(_16), ._17(_17), ._18(_18), ._19(_19), ._20(_20),
    ._21(rom_14_data[4]), ._22(rom_14_data[3]), ._23(rom_14_data[2]), ._24(rom_14_data[1]),
    ._25(rom_14_data[0]), ._26(_32));
  _20_to_1_MUX u_20_to_1_mux_15 (
    ._8(_8), ._7(_7), ._6(_6), ._5(_5), ._4(_4), ._3(_3), ._2(_2), ._1(_1), ._9(_9), ._10(_10), ._11(_11),
    ._12(_12), ._13(_13), ._14(_14), ._15(_15), ._16(_16), ._17(_17), ._18(_18), ._19(_19), ._20(_20),
    ._21(rom_15_data[4]), ._22(rom_15_data[3]), ._23(rom_15_data[2]), ._24(rom_15_data[1]),
    ._25(rom_15_data[0]), ._26(_34));
  _20_to_1_MUX u_20_to_1_mux_16 (
    ._8(_8), ._7(_7), ._6(_6), ._5(_5), ._4(_4), ._3(_3), ._2(_2), ._1(_1), ._9(_9), ._10(_10), ._11(_11),
    ._12(_12), ._13(_13), ._14(_14), ._15(_15), ._16(_16), ._17(_17), ._18(_18), ._19(_19), ._20(_20),
    ._21(rom_16_data[4]), ._22(rom_16_data[3]), ._23(rom_16_data[2]), ._24(rom_16_data[1]),
    ._25(rom_16_data[0]), ._26(_36));

  // Notes on the sheet:
  //   IN 15
  //   LOCAL INPUTS
  //   IN 0
  //   LOCAL FEEDBACK
  //   LE 00
  //   LE 02
  //   LE 10
  //   LE 12
  //   LE 20
  //   LE 22
  //   LE 30
  //   LE 32
  //   contents of rom_1 (hex, n*v repeats v):
  //   0 0 0 10
  //   contents of rom_2 (hex, n*v repeats v):
  //   0 0 0 11
  //   contents of rom_3 (hex, n*v repeats v):
  //   0 0 0 12
  //   contents of rom_4 (hex, n*v repeats v):
  //   0 0 0 13
  //   contents of rom_5 (hex, n*v repeats v):
  //   0 0 0 10
  //   contents of rom_6 (hex, n*v repeats v):
  //   0 0 0 11
  //   contents of rom_7 (hex, n*v repeats v):
  //   0 0 0 12
  //   contents of rom_8 (hex, n*v repeats v):
  //   0 0 0 13
  //   LE 01
  //   LE 03
  //   LE 11
  //   LE 13
  //   LE 21
  //   LE 23
  //   LE 31
  //   LE 33
  //   contents of rom_9 (hex, n*v repeats v):
  //   0 0 0 10
  //   contents of rom_10 (hex, n*v repeats v):
  //   0 0 0 11
  //   contents of rom_11 (hex, n*v repeats v):
  //   0 0 0 12
  //   contents of rom_12 (hex, n*v repeats v):
  //   0 0 0 13
  //   contents of rom_13 (hex, n*v repeats v):
  //   0 0 0 10
  //   contents of rom_14 (hex, n*v repeats v):
  //   0 0 0 11
  //   contents of rom_15 (hex, n*v repeats v):
  //   0 0 0 12
  //   contents of rom_16 (hex, n*v repeats v):
  //   0 0 0 13
endmodule

module _20_to_1_MUX (
  input  _1,
  input  _2,
  input  _3,
  input  _4,
  input  _5,
  input  _6,
  input  _7,
  input  _8,
  input  _9,
  input  _10,
  input  _11,
  input  _12,
  input  _13,
  input  _14,
  input  _15,
  input  _16,
  input  _17,
  input  _18,
  input  _19,
  input  _20,
  input  _21,
  input  _22,
  input  _23,
  input  _24,
  input  _25,
  output _26
);

  wire mux_4_a_1_1__5, mux_8_a_1_1__5, mux_8_a_1_2__5;

  MUX_8_a_1 mux_8_a_1_1 (
    ._1(_1), ._2(_2), ._3(_3), ._4(_4), ._5(mux_8_a_1_1__5), ._6(_5), ._7(_6), ._8(_7), ._9(_8), ._10(_23),
    ._11(_24), ._12(_25));
  MUX_8_a_1 mux_8_a_1_2 (
    ._1(_9), ._2(_10), ._3(_11), ._4(_12), ._5(mux_8_a_1_2__5), ._6(_13), ._7(_14), ._8(_15), ._9(_16),
    ._10(_23), ._11(_24), ._12(_25));
  MUX_4_a_1 mux_4_a_1_1 (._1(_17), ._5(mux_4_a_1_1__5), ._6(_24), ._7(_25), ._2(_18), ._3(_19), ._4(_20));
  MUX_4_a_1 mux_4_a_1_2 (
    ._1(mux_8_a_1_1__5), ._5(_26), ._6(_21), ._7(_22), ._2(mux_8_a_1_2__5), ._3(mux_4_a_1_1__5));  // open: _4

  // Notes on the sheet:
  //   I0
  //   I20
  //   S4
  //   S0
  //   OUT
endmodule

module MUX_8_a_1 (
  input  _1,
  input  _2,
  input  _3,
  input  _4,
  input  _6,
  input  _7,
  input  _8,
  input  _9,
  input  _12,
  input  _11,
  input  _10,
  output _5
);

  wire mux_4_a_1_1__5, mux_4_a_1_2__5;

  MUX_4_a_1 mux_4_a_1_1 (._1(_1), ._5(mux_4_a_1_1__5), ._6(_11), ._7(_12), ._2(_2), ._3(_3), ._4(_4));
  MUX_4_a_1 mux_4_a_1_2 (._1(_6), ._5(mux_4_a_1_2__5), ._6(_11), ._7(_12), ._2(_7), ._3(_8), ._4(_9));
  _01S u_01s_1 (._2(mux_4_a_1_1__5), ._3(mux_4_a_1_2__5), ._4(_10), .out_4(_5));
endmodule

module MUX_4_a_1 (
  input  _1,
  input  _2,
  input  _3,
  input  _4,
  input  _7,
  input  _6,
  output _5
);

  wire n2_to_4_dec_1__3, n2_to_4_dec_1__4, n2_to_4_dec_1__5, n2_to_4_dec_1__6__y0_prime;

  _2_to_4_Dec u_2_to_4_dec_1 (
    .A__1(_7), .B__2(_6), ._3(n2_to_4_dec_1__3), ._4(n2_to_4_dec_1__4), ._5(n2_to_4_dec_1__5),
    ._6__Y0_prime(n2_to_4_dec_1__6__y0_prime));
  assign _5 = n2_to_4_dec_1__6__y0_prime ? _1 : 1'bz;  // Controlled_Buffer controlled_buffer_1
  assign _5 = n2_to_4_dec_1__5 ? _2 : 1'bz;  // Controlled_Buffer controlled_buffer_2
  assign _5 = n2_to_4_dec_1__4 ? _3 : 1'bz;  // Controlled_Buffer controlled_buffer_3
  assign _5 = n2_to_4_dec_1__3 ? _4 : 1'bz;  // Controlled_Buffer controlled_buffer_4
endmodule

module _01S (
  input  _2,
  input  _3,
  input  _4,
  output out_4
);

  wire not_1_out;

  not not_1 (not_1_out, _4);
  assign out_4 = not_1_out ? _2 : 1'bz;  // Controlled_Buffer controlled_buffer_1
  assign out_4 = _4 ? _3 : 1'bz;  // Controlled_Buffer controlled_buffer_2
endmodule

module _2_to_4_Dec (
  input  A__1,
  input  B__2,
  output _6__Y0_prime,
  output _5,
  output _4,
  output _3
);

  wire not_1_out, not_2_out;

  not not_1 (not_1_out, A__1);
  not not_2 (not_2_out, B__2);
  and and_1 (_6__Y0_prime, not_1_out, not_2_out);
  and and_2 (_5, A__1, not_2_out);
  and and_3 (_4, not_1_out, B__2);
  and and_4 (_3, A__1, B__2);
endmodule

module Prueba (
  input  in_1,
  input  in_2,
  input  in_3,
  input  in_4,
  input  in_5,
  input  in_6,
  input  in_7,
  input  in_8,
  input  in_9,
  input  in_10,
  input  in_11,
  input  in_12,
  input  in_13,
  input  in_14,
  input  in_15,
  input  in_16,
  input  in_17,
  input  in_18,
  input  in_19,
  input  in_20,
  input  in_21,
  input  in_22,
  input  in_23,
  input  in_24,
  input  in_25,
  input  in_26,
  input  in_27,
  input  in_28,
  input  in_29,
  input  in_30,
  input  in_31,
  input  in_32,
  input  in_33,
  input  in_34,
  input  in_35,
  input  in_36,
  input  in_37,
  input  in_38,
  input  in_39,
  input  in_40,
  input  in_41,
  input  in_42,
  input  in_43,
  input  in_44,
  input  in_45,
  input  in_46,
  input  in_47,
  input  in_48,
  input  in_49,
  input  in_50,
  input  in_51,
  input  in_52,
  input  in_53,
  input  in_54,
  input  in_55,
  input  in_56,
  input  in_57,
  input  in_58,
  input  in_59,
  input  in_60,
  input  in_61,
  input  in_62,
  input  in_63,
  input  in_64,
  input  in_65,
  input  in_66,
  input  in_67,
  input  in_68,
  input  in_69,
  input  LE_00,
  input  in_71,
  input  in_72,
  input  in_73,
  input  in_74,
  input  in_75,
  input  _2_BITS,
  input  in_77,
  input  in_78,
  input  in_79,
  input  in_80,
  input  in_81,
  input  in_82,
  input  in_83,
  input  in_84,
  input  in_85,
  input  in_86,
  input  in_87,
  input  in_88,
  input  in_89,
  input  in_90,
  input  in_91,
  input  in_92,
  input  in_93,
  input  in_94,
  input  in_95,
  input  in_96,
  output [4:0] out_97
);

  wire clock_1_out, clock_2_out, clock_3_out, clock_4_out, clock_5_out, clock_6_out, clock_7_out,
       clock_8_out, clock_9_out, logic_element_1_1_out_8, logic_element_1_2_out_8, logic_element_1_3_out_8,
       logic_element_2_1_out_8, logic_element_2_2_out_8, logic_element_2_3_out_8, logic_element_3_1_out_8,
       logic_element_3_2_out_8, logic_element_4_1_out_8, mux_4_a_1_1__5, mux_8_a_1_1__5, n01s_1_out_4,
       n20_to_1_mux_1__26, n20_to_1_mux_2__26, or_1_out;

  LED led_1 (.in(n01s_1_out_4));
  _01S u_01s_1 (._2(in_11), ._3(in_15), ._4(in_22), .out_4(n01s_1_out_4));
  MUX_4_a_1 mux_4_a_1_1 (._1(in_37), ._5(mux_4_a_1_1__5), ._6(in_61), ._7(in_62), ._2(in_48), ._3(in_51), ._4(in_54));
  Clock clock_1 (.out(clock_1_out));
  Clock clock_2 (.out(clock_2_out));
  LED led_2 (.in(mux_4_a_1_1__5));
  Logic_element_1 logic_element_1_1 (
    .out_8(logic_element_1_1_out_8), .Clear(clock_1_out), .in_6(in_75), .Preset(_2_BITS), .A3(in_71),
    .A2(in_74), .A1(logic_element_2_1_out_8), .A0(logic_element_1_1_out_8));
  Logic_element_2 logic_element_2_1 (
    ._1(in_81), ._2(in_83), ._3(logic_element_2_1_out_8), ._4(logic_element_1_1_out_8),
    .out_8(logic_element_2_1_out_8), ._5(clock_2_out), ._6(in_84), ._7(in_85));
  MUX_8_a_1 mux_8_a_1_1 (
    ._1(in_8), ._2(in_12), ._3(in_16), ._4(in_19), ._5(mux_8_a_1_1__5), ._6(in_23), ._7(in_26), ._8(in_29),
    ._9(in_32), ._10(in_45), ._11(in_46), ._12(in_47));
  or or_1 (or_1_out, in_57, in_60, in_65, in_68);
  LED led_3 (.in(logic_element_1_1_out_8));
  LED led_4 (.in(logic_element_2_1_out_8));
  LED led_5 (.in(mux_8_a_1_1__5));
  LED led_6 (.in(or_1_out));
  Clock clock_3 (.out(clock_3_out));
  Clock clock_4 (.out(clock_4_out));
  Clock clock_5 (.out(clock_5_out));
  Logic_element_1 logic_element_1_2 (
    .out_8(logic_element_1_2_out_8), .Clear(clock_3_out), .in_6(in_77), .Preset(in_78), .A3(in_72),
    .A2(logic_element_3_1_out_8), .A1(logic_element_2_2_out_8), .A0(logic_element_1_2_out_8));
  Logic_element_2 logic_element_2_2 (
    ._1(in_82), ._2(logic_element_3_1_out_8), ._3(logic_element_2_2_out_8), ._4(logic_element_1_2_out_8),
    .out_8(logic_element_2_2_out_8), ._5(clock_4_out), ._6(in_86), ._7(in_87));
  Logic_element_3 logic_element_3_1 (
    ._1(in_90), ._2(logic_element_3_1_out_8), ._3(logic_element_2_2_out_8), ._4(logic_element_1_2_out_8),
    .out_8(logic_element_3_1_out_8), ._5(clock_5_out), ._6(in_91), ._7(in_92));
  LED led_7 (.in(logic_element_1_2_out_8));
  LED led_8 (.in(logic_element_2_2_out_8));
  LED led_9 (.in(logic_element_3_1_out_8));
  _20_to_1_MUX u_20_to_1_mux_1 (
    ._8(in_24), ._7(in_20), ._6(in_17), ._5(in_13), ._4(in_9), ._3(in_6), ._2(in_4), ._1(in_2), ._9(in_27),
    ._10(in_30), ._11(in_33), ._12(in_35), ._13(in_38), ._14(in_49), ._15(in_52), ._16(in_55), ._17(in_58),
    ._18(in_63), ._19(in_66), ._20(in_69), ._21(in_39), ._22(in_40), ._23(in_41), ._24(in_42), ._25(in_43),
    ._26(n20_to_1_mux_1__26));
  LED led_10 (.in(n20_to_1_mux_1__26));
  Clock clock_6 (.out(clock_6_out));
  Clock clock_7 (.out(clock_7_out));
  Clock clock_8 (.out(clock_8_out));
  Clock clock_9 (.out(clock_9_out));
  Logic_element_1 logic_element_1_3 (
    .out_8(logic_element_1_3_out_8), .Clear(clock_6_out), .in_6(in_79), .Preset(in_80),
    .A3(logic_element_4_1_out_8), .A2(logic_element_3_2_out_8), .A1(logic_element_2_3_out_8),
    .A0(logic_element_1_3_out_8));
  Logic_element_2 logic_element_2_3 (
    ._1(logic_element_4_1_out_8), ._2(logic_element_3_2_out_8), ._3(logic_element_2_3_out_8),
    ._4(logic_element_1_3_out_8), .out_8(logic_element_2_3_out_8), ._5(clock_7_out), ._6(in_88), ._7(in_89));
  Logic_element_3 logic_element_3_2 (
    ._1(logic_element_4_1_out_8), ._2(logic_element_3_2_out_8), ._3(logic_element_2_3_out_8),
    ._4(logic_element_1_3_out_8), .out_8(logic_element_3_2_out_8), ._5(clock_8_out), ._6(in_93), ._7(in_94));
  Logic_element_4 logic_element_4_1 (
    ._2(logic_element_3_2_out_8), ._3(logic_element_2_3_out_8), ._4(logic_element_1_3_out_8),
    .out_8(logic_element_4_1_out_8), ._5(clock_9_out), ._6(in_95), ._7(in_96), ._1(logic_element_4_1_out_8));
  LED led_11 (.in(logic_element_1_3_out_8));
  LED led_12 (.in(logic_element_2_3_out_8));
  LED led_13 (.in(logic_element_3_2_out_8));
  LED led_14 (.in(logic_element_4_1_out_8));
  ROM #(.addrWidth(2), .dataWidth(5)) rom_1 (.addr({in_73, LE_00}), .data(out_97), .sel(1'b1));
  _20_to_1_MUX u_20_to_1_mux_2 (
    ._8(in_21), ._7(in_18), ._6(in_14), ._5(in_10), ._4(in_7), ._3(in_5), ._2(in_3), ._1(in_1), ._9(in_25),
    ._10(in_28), ._11(in_31), ._12(in_34), ._13(in_36), ._14(in_44), ._15(in_50), ._16(in_53), ._17(in_56),
    ._18(in_59), ._19(in_64), ._20(in_67), ._21(out_97[4]), ._22(out_97[3]), ._23(out_97[2]),
    ._24(out_97[1]), ._25(out_97[0]), ._26(n20_to_1_mux_2__26));
  LED led_15 (.in(n20_to_1_mux_2__26));

  // Notes on the sheet:
  //   in_39: pull=down
  //   1001
  //   1100
  //   Empieza en 11
  //   3 BITS
  //   01010110
  //   01101010
  //   11110000
  //   Empieza en 100
  //   4 BITS
  //   1001100101100110
  //   1100101010101010
  //   0100110111110000
  //   1111011100100000
  //   Empieza en 1011
  //   contents of rom_1 (hex, n*v repeats v):
  //   13
endmodule

module Prueba_Local_Matrix (
  input  in_1,
  input  in_2,
  input  in_3,
  input  in_4,
  input  in_5,
  input  _15,
  input  in_7,
  input  in_8,
  input  _14,
  input  in_10,
  input  in_11,
  input  _13,
  input  _12,
  input  in_14,
  input  _11,
  input  _10,
  input  _9,
  input  in_18,
  input  in_19,
  input  _8,
  input  in_21,
  input  in_22,
  input  _7,
  input  _6,
  input  in_25,
  input  _5,
  input  _4,
  input  _3,
  input  _2,
  input  in_30,
  input  in_31,
  input  _1,
  input  in_33,
  input  in_34,
  input  _0,
  input  _15_2,
  input  _14_2,
  input  in_38,
  input  in_39,
  input  _13_2,
  input  _12_2,
  input  _11_2,
  input  _10_2,
  input  _9_2,
  input  _8_2,
  input  in_46,
  input  in_47,
  input  _7_2,
  input  _6_2,
  input  _5_2,
  input  _4_2,
  input  _3_2,
  input  _2_2,
  input  _1_2,
  input  in_55,
  input  in_56,
  input  _0_2,
  input  in_58,
  input  in_59
);

  wire clock_1_out, clock_2_out, clock_3_out, clock_4_out, clock_5_out, clock_6_out, clock_7_out,
       clock_8_out, clock_9_out, clock_10_out, logic_element_1_1_out_8, logic_element_1_2_out_8,
       logic_element_1_3_out_8, logic_element_2_1_out_8, logic_element_2_2_out_8, logic_element_2_3_out_8,
       logic_element_3_1_out_8, logic_element_3_2_out_8, logic_element_3_3_out_8, logic_element_4_1_out_8,
       programmable_local_interconnect_matrix_1__21, programmable_local_interconnect_matrix_1__22,
       programmable_local_interconnect_matrix_1__23, programmable_local_interconnect_matrix_1__24,
       programmable_local_interconnect_matrix_1__25, programmable_local_interconnect_matrix_1__26,
       programmable_local_interconnect_matrix_1__27, programmable_local_interconnect_matrix_1__28,
       programmable_local_interconnect_matrix_1__29, programmable_local_interconnect_matrix_1__30,
       programmable_local_interconnect_matrix_1__31, programmable_local_interconnect_matrix_1__32,
       programmable_local_interconnect_matrix_1__33, programmable_local_interconnect_matrix_1__34,
       programmable_local_interconnect_matrix_1__35, programmable_local_interconnect_matrix_1__36,
       programmable_local_interconnect_matrix_2__21, programmable_local_interconnect_matrix_2__22,
       programmable_local_interconnect_matrix_2__29;

  Programmable_local_interconnect_matrix programmable_local_interconnect_matrix_1 (
    ._16(_15_2), ._15(_14_2), ._14(_13_2), ._13(_12_2), ._12(_11_2), ._11(_10_2), ._10(_9_2), ._9(_8_2),
    ._8(_7_2), ._7(_6_2), ._6(_5_2), ._5(_4_2), ._4(_3_2), ._3(_2_2), ._2(_1_2), ._1(_0_2),
    ._20(logic_element_1_2_out_8), ._19(logic_element_2_2_out_8), ._18(logic_element_3_2_out_8),
    ._17(logic_element_4_1_out_8), ._21(programmable_local_interconnect_matrix_1__21),
    ._23(programmable_local_interconnect_matrix_1__23), ._27(programmable_local_interconnect_matrix_1__27),
    ._29(programmable_local_interconnect_matrix_1__29), ._31(programmable_local_interconnect_matrix_1__31),
    ._33(programmable_local_interconnect_matrix_1__33), ._35(programmable_local_interconnect_matrix_1__35),
    ._22(programmable_local_interconnect_matrix_1__22), ._24(programmable_local_interconnect_matrix_1__24),
    ._26(programmable_local_interconnect_matrix_1__26), ._28(programmable_local_interconnect_matrix_1__28),
    ._30(programmable_local_interconnect_matrix_1__30), ._32(programmable_local_interconnect_matrix_1__32),
    ._34(programmable_local_interconnect_matrix_1__34), ._36(programmable_local_interconnect_matrix_1__36),
    ._25(programmable_local_interconnect_matrix_1__25));
  Clock clock_1 (.out(clock_1_out));
  Clock clock_2 (.out(clock_2_out));
  Clock clock_3 (.out(clock_3_out));
  Logic_element_1 logic_element_1_1 (
    .out_8(logic_element_1_1_out_8), .Clear(clock_1_out), .in_6(in_7), .Preset(in_8), .A3(in_5),
    .A2(logic_element_3_1_out_8), .A1(logic_element_2_1_out_8), .A0(logic_element_1_1_out_8));
  Logic_element_2 logic_element_2_1 (
    ._1(in_14), ._2(logic_element_3_1_out_8), ._3(logic_element_2_1_out_8), ._4(logic_element_1_1_out_8),
    .out_8(logic_element_2_1_out_8), ._5(clock_2_out), ._6(in_18), ._7(in_19));
  Logic_element_3 logic_element_3_1 (
    ._1(in_25), ._2(logic_element_3_1_out_8), ._3(logic_element_2_1_out_8), ._4(logic_element_1_1_out_8),
    .out_8(logic_element_3_1_out_8), ._5(clock_3_out), ._6(in_30), ._7(in_31));
  LED led_1 (.in(logic_element_1_1_out_8));
  LED led_2 (.in(logic_element_2_1_out_8));
  LED led_3 (.in(logic_element_3_1_out_8));
  Clock clock_4 (.out(clock_4_out));
  Clock clock_5 (.out(clock_5_out));
  Clock clock_6 (.out(clock_6_out));
  Clock clock_7 (.out(clock_7_out));
  Logic_element_1 logic_element_1_2 (
    .out_8(logic_element_1_2_out_8), .Clear(clock_4_out), .in_6(in_38), .Preset(in_39),
    .A3(programmable_local_interconnect_matrix_1__21), .A2(programmable_local_interconnect_matrix_1__23),
    .A1(programmable_local_interconnect_matrix_1__25), .A0(programmable_local_interconnect_matrix_1__27));
  Logic_element_2 logic_element_2_2 (
    ._1(programmable_local_interconnect_matrix_1__29), ._2(programmable_local_interconnect_matrix_1__31),
    ._3(programmable_local_interconnect_matrix_1__33), ._4(programmable_local_interconnect_matrix_1__35),
    .out_8(logic_element_2_2_out_8), ._5(clock_5_out), ._6(in_46), ._7(in_47));
  Logic_element_3 logic_element_3_2 (
    ._1(programmable_local_interconnect_matrix_1__22), ._2(programmable_local_interconnect_matrix_1__24),
    ._3(programmable_local_interconnect_matrix_1__26), ._4(programmable_local_interconnect_matrix_1__28),
    .out_8(logic_element_3_2_out_8), ._5(clock_6_out), ._6(in_55), ._7(in_56));
  Logic_element_4 logic_element_4_1 (
    ._2(programmable_local_interconnect_matrix_1__32), ._3(programmable_local_interconnect_matrix_1__34),
    ._4(programmable_local_interconnect_matrix_1__36), .out_8(logic_element_4_1_out_8), ._5(clock_7_out),
    ._6(in_58), ._7(in_59), ._1(programmable_local_interconnect_matrix_1__30));
  LED led_4 (.in(logic_element_1_2_out_8));
  LED led_5 (.in(logic_element_2_2_out_8));
  LED led_6 (.in(logic_element_3_2_out_8));
  LED led_7 (.in(logic_element_4_1_out_8));
  Programmable_local_interconnect_matrix programmable_local_interconnect_matrix_2 (
    ._16(_15), ._15(_14), ._14(_13), ._13(_12), ._12(_11), ._11(_10), ._10(_9), ._9(_8), ._8(_7), ._7(_6),
    ._6(_5), ._5(_4), ._4(_3), ._3(_2), ._2(_1), ._1(_0), ._20(in_1), ._19(in_2), ._18(in_3), ._17(in_4),
    ._21(programmable_local_interconnect_matrix_2__21), ._29(programmable_local_interconnect_matrix_2__29),
    ._22(programmable_local_interconnect_matrix_2__22));  // open: _23, _27, _31, _33, _35, _24, _26, _28, _30, _32, _34, _36, _25
  Clock clock_8 (.out(clock_8_out));
  Clock clock_9 (.out(clock_9_out));
  Clock clock_10 (.out(clock_10_out));
  Logic_element_1 logic_element_1_3 (
    .out_8(logic_element_1_3_out_8), .Clear(clock_8_out), .in_6(in_10), .Preset(in_11),
    .A3(programmable_local_interconnect_matrix_2__21), .A2(logic_element_3_3_out_8),
    .A1(logic_element_2_3_out_8), .A0(logic_element_1_3_out_8));
  Logic_element_2 logic_element_2_3 (
    ._1(programmable_local_interconnect_matrix_2__29), ._2(logic_element_3_3_out_8),
    ._3(logic_element_2_3_out_8), ._4(logic_element_1_3_out_8), .out_8(logic_element_2_3_out_8),
    ._5(clock_9_out), ._6(in_21), ._7(in_22));
  Logic_element_3 logic_element_3_3 (
    ._1(programmable_local_interconnect_matrix_2__22), ._2(logic_element_3_3_out_8),
    ._3(logic_element_2_3_out_8), ._4(logic_element_1_3_out_8), .out_8(logic_element_3_3_out_8),
    ._5(clock_10_out), ._6(in_33), ._7(in_34));
  LED led_8 (.in(logic_element_1_3_out_8));
  LED led_9 (.in(logic_element_2_3_out_8));
  LED led_10 (.in(logic_element_3_3_out_8));

  // Notes on the sheet:
  //   3 BITS Up/Down
  //   1
  //   01101010
  //   11110000
endmodule
